// Logisim project dunk.circ as structural Verilog: 57 circuits, main circuit main
module main (
);

  wire button_1_out, button_2_out, clk_out, control_box_1_clock_out, control_box_1_out_12,
       control_box_1_reset_out, controlled_buffer_1_out, controlled_buffer_2_out, controlled_buffer_3_out,
       controlled_buffer_4_out, io_pins_4_1_out_11, io_pins_4_1_out_12, io_pins_4_1_out_13,
       io_pins_4_1_out_14, io_pins_4_1_out_15, io_pins_4_1_out_16, io_pins_4_1_out_17, io_pins_4_1_out_18,
       memory_ctrl_1_mem_write, memory_ctrl_1_reg_write, pause_out, reset_out, resume_out;
  wire [1:0] memory_ctrl_1_reg_select;
  wire [6:0] mmio_registers_1_out_6;
  wire [7:0] input_pins_8_1_out_9;
  wire [15:0] addr_bus_controller_1_addr_bus_out, alu_1_out_6, control_bus_controller_1_control_bus_1,
       control_bus_controller_1_control_bus_2, control_unit_1_addr_bus_out, control_unit_1_control_bus_1_out,
       control_unit_1_control_bus_2_out, control_unit_1_current_instr, control_unit_1_data_bus_out,
       control_unit_1_to_pk, data_bus_controller_1_data_bus_out, default_register_00ff_1_data_out,
       io_pins_4_1_data_bus_out, memory_ctrl_1_data_bus_out, memory_ctrl_1_data_to_mem,
       memory_ctrl_1_mem_addr_out, ram_1_dout, register_unit_1_addr_bus_out, register_unit_1_alu1_out,
       register_unit_1_alu2_out, register_unit_1_data_bus_out, special_registers_1_addr_bus_out,
       special_registers_1_data_bus_out, special_registers_1_offset_out, special_registers_1_program_kounter,
       special_registers_1_stack_pointer;
  wire [15:7] mmio_registers_1_out_6_2;

  Button pause (.out(pause_out));
  Button resume (.out(resume_out));
  Clock clk (.out(clk_out));
  Button reset (.out(reset_out));
  control_box control_box_1 (
    .instr(control_unit_1_current_instr), .clock_in(clk_out), .reset_in(reset_out),
    .program_kounter(special_registers_1_program_kounter),
    .control_bus_1(control_bus_controller_1_control_bus_1), .pause(pause_out), .resume(resume_out),
    .clock_out(control_box_1_clock_out), .reset_out(control_box_1_reset_out), .out_12(control_box_1_out_12));  // open: instr_breakpoint, pk_breakpoint
  LED #(.active("false")) running (.in(control_box_1_out_12));
  control_bus_controller control_bus_controller_1 (
    .control_1(control_unit_1_control_bus_1_out), .control_2(control_unit_1_control_bus_2_out),
    .clock(control_box_1_clock_out), .reset(control_box_1_reset_out),
    .control_bus_1(control_bus_controller_1_control_bus_1),
    .control_bus_2(control_bus_controller_1_control_bus_2));
  data_bus_controller data_bus_controller_1 (
    .control_bus_2(control_bus_controller_1_control_bus_2), .clock(control_box_1_clock_out),
    .reset(control_box_1_reset_out), .control_bus_1(control_bus_controller_1_control_bus_1),
    .addr_bus_in(addr_bus_controller_1_addr_bus_out), .control_unit_in(control_unit_1_data_bus_out),
    .registers_in(register_unit_1_data_bus_out), .special_registers_in(alu_1_out_6),
    .ALU_in(special_registers_1_data_bus_out), .memory_in(memory_ctrl_1_data_bus_out),
    .io_in(io_pins_4_1_data_bus_out), .data_bus_out(data_bus_controller_1_data_bus_out));
  addr_bus_controller addr_bus_controller_1 (
    .control_bus_1(control_bus_controller_1_control_bus_1),
    .control_bus_2(control_bus_controller_1_control_bus_2), .clock(control_box_1_clock_out),
    .reset(control_box_1_reset_out), .data_bus_in(data_bus_controller_1_data_bus_out),
    .control_unit_in(control_unit_1_addr_bus_out), .registers_in(register_unit_1_addr_bus_out),
    .special_registers_in(special_registers_1_addr_bus_out), .addr_bus_out(addr_bus_controller_1_addr_bus_out));
  default_register_00ff default_register_00ff_1 (
    .clock(control_box_1_clock_out), .reset(control_box_1_reset_out),
    .data_out(default_register_00ff_1_data_out));  // open: write, data_in, reset_value
  control_unit control_unit_1 (
    .preservation_mask(default_register_00ff_1_data_out), .stack_pointer(special_registers_1_stack_pointer),
    .addr_bus(addr_bus_controller_1_addr_bus_out), .control_bus_1(control_bus_controller_1_control_bus_1),
    .control_bus_2(control_bus_controller_1_control_bus_2), .clock(control_box_1_clock_out),
    .reset(control_box_1_reset_out), .RAM_direct(ram_1_dout),
    .data_bus_in(data_bus_controller_1_data_bus_out), .interrupt_pins(input_pins_8_1_out_9),
    .control_bus_1_out(control_unit_1_control_bus_1_out),
    .control_bus_2_out(control_unit_1_control_bus_2_out), .current_instr(control_unit_1_current_instr),
    .data_bus_out(control_unit_1_data_bus_out), .addr_bus_out(control_unit_1_addr_bus_out),
    .to_pk(control_unit_1_to_pk));
  input_pins_8 input_pins_8_1 (
    .in_7(button_1_out), .in_8(button_2_out), .out_9(input_pins_8_1_out_9));  // open: in_1, in_2, in_3, in_4, in_5, in_6
  Button button_1 (.out(button_1_out));
  Button button_2 (.out(button_2_out));
  register_unit register_unit_1 (
    .data_bus_in(data_bus_controller_1_data_bus_out), .clock(control_box_1_clock_out),
    .reset(control_box_1_reset_out), .control_bus_1(control_bus_controller_1_control_bus_1),
    .control_bus_2(control_bus_controller_1_control_bus_2), .data_bus_out(register_unit_1_data_bus_out),
    .addr_bus_out(register_unit_1_addr_bus_out), .alu1_out(register_unit_1_alu1_out),
    .alu2_out(register_unit_1_alu2_out));
  assign controlled_buffer_1_out = io_pins_4_1_out_12 ? io_pins_4_1_out_11 : 1'bz;  // Controlled_Buffer controlled_buffer_1
  ALU alu_1 (
    .argument1(register_unit_1_alu1_out), .argument2(register_unit_1_alu2_out),
    .clock(control_box_1_clock_out), .reset(control_box_1_reset_out),
    .control_bus(control_bus_controller_1_control_bus_1), .out_6(alu_1_out_6));  // open: out_7
  assign controlled_buffer_2_out = io_pins_4_1_out_14 ? io_pins_4_1_out_13 : 1'bz;  // Controlled_Buffer controlled_buffer_2
  assign controlled_buffer_3_out = io_pins_4_1_out_16 ? io_pins_4_1_out_15 : 1'bz;  // Controlled_Buffer controlled_buffer_3
  // Probe on special_registers_1_program_kounter
  // Probe on special_registers_1_stack_pointer
  special_registers special_registers_1 (
    .control_bus_1(control_bus_controller_1_control_bus_1),
    .control_bus_2(control_bus_controller_1_control_bus_2), .temp_register(control_unit_1_to_pk),
    .clock(control_box_1_clock_out), .reset(control_box_1_reset_out),
    .data_bus_in(data_bus_controller_1_data_bus_out), .program_kounter(special_registers_1_program_kounter),
    .data_bus_out(special_registers_1_data_bus_out), .addr_bus_out(special_registers_1_addr_bus_out),
    .stack_pointer(special_registers_1_stack_pointer), .offset_out(special_registers_1_offset_out));  // open: sp_reset_value
  io_pins_4 io_pins_4_1 (
    .in_8(controlled_buffer_3_out), .clock(control_box_1_clock_out), .reset(control_box_1_reset_out),
    .in_9(controlled_buffer_4_out), .control_bus(control_bus_controller_1_control_bus_1),
    .in_6(controlled_buffer_1_out), .data_bus_in(data_bus_controller_1_data_bus_out),
    .in_7(controlled_buffer_2_out), .addr_bus_in(addr_bus_controller_1_addr_bus_out),
    .out_15(io_pins_4_1_out_15), .out_16(io_pins_4_1_out_16), .out_17(io_pins_4_1_out_17),
    .out_18(io_pins_4_1_out_18), .data_bus_out(io_pins_4_1_data_bus_out), .out_11(io_pins_4_1_out_11),
    .out_12(io_pins_4_1_out_12), .out_13(io_pins_4_1_out_13), .out_14(io_pins_4_1_out_14));
  assign controlled_buffer_4_out = io_pins_4_1_out_18 ? io_pins_4_1_out_17 : 1'bz;  // Controlled_Buffer controlled_buffer_4
  memory_ctrl memory_ctrl_1 (
    .control_bus_2(control_bus_controller_1_control_bus_2), .data_bus_in(data_bus_controller_1_data_bus_out),
    .pk_in(special_registers_1_program_kounter), .mem_in(ram_1_dout),
    .addr_in(addr_bus_controller_1_addr_bus_out), .clock(control_box_1_clock_out),
    .reset(control_box_1_reset_out), .control_bus_1(control_bus_controller_1_control_bus_1),
    .offset_in(special_registers_1_offset_out), .data_to_mem(memory_ctrl_1_data_to_mem),
    .data_bus_out(memory_ctrl_1_data_bus_out), .mem_addr_out(memory_ctrl_1_mem_addr_out),
    .mem_write(memory_ctrl_1_mem_write), .reg_select(memory_ctrl_1_reg_select),
    .reg_write(memory_ctrl_1_reg_write));
  mmio_registers mmio_registers_1 (
    .write(memory_ctrl_1_reg_write), .clock(control_box_1_clock_out), .reset(control_box_1_reset_out),
    .data_in(memory_ctrl_1_data_to_mem), .reg_select(memory_ctrl_1_reg_select),
    .out_6({mmio_registers_1_out_6_2, mmio_registers_1_out_6}));  // open: out_7, out_8, out_9
  RAM #(.addrWidth(16), .dataWidth(16), .enables("line")) ram_1 (
    .addr(memory_ctrl_1_mem_addr_out), .we(memory_ctrl_1_mem_write), .clk(control_box_1_clock_out),
    .din(memory_ctrl_1_data_to_mem), .dout(ram_1_dout));
  // Probe on control_bus_controller_1_control_bus_1
  // Probe on control_bus_controller_1_control_bus_2
  // Probe on data_bus_controller_1_data_bus_out
  // Probe on addr_bus_controller_1_addr_bus_out
  TTY tty_1 (.data(mmio_registers_1_out_6), .clk(controlled_buffer_4_out), .clr(control_box_1_reset_out));  // open: we

  // Notes on the sheet:
  //   David's Universal Number Kounter
endmodule

module control_unit (
  input  [15:0] preservation_mask,
  input  [15:0] RAM_direct,
  input  [15:0] data_bus_in,
  input  [15:0] control_bus_1,
  input  [15:0] control_bus_2,
  input  clock,
  input  reset,
  input  [15:0] stack_pointer,
  input  [15:0] addr_bus,
  input  [7:0] interrupt_pins,
  output [15:0] current_instr,
  output [15:0] data_bus_out,
  output [15:0] addr_bus_out,
  output [15:0] control_bus_1_out,
  output [15:0] to_pk,
  output [15:0] control_bus_2_out
);

  wire and_1_out, and_2_out, and_3_out, and_4_out, buffer_1_out, buffer_2_out, buffer_3_out, buffer_4_out,
       button_1_out, comparator_1_gt, comparator_1_lt, d_ff_1_q, eight_bit_eq_cmp_1_out_3,
       eight_bit_eq_cmp_2_out_3, interrupt_queue_1_waiting, nor_1_out, or_1_out, or_4_out, or_5_out,
       or_9_out, register_2_q, register_3_q, register_4_q, sixt_bit_eq_cmp_1_out_3, sixt_bit_eq_cmp_2_out_3,
       sixt_bit_eq_cmp_3_out_3, sixt_bit_eq_cmp_4_out_3, sixt_bit_eq_cmp_5_out_3, sixt_bit_eq_cmp_7_out_3,
       sixt_bit_eq_cmp_8_out_3, stacker_1_active, unstacker_1_active;
  wire [7:0] interrupt_queue_1_id, multiplexer_1_out;
  wire [15:0] interrupt_table_1_ih_addr, interrupt_table_1_to_data_bus, microcode_mixer_1_microcode_out,
       microcode_mixer_2_microcode_out, multiplexer_2_out, multiplexer_3_out, or_6_out, or_7_out, or_8_out,
       register_5_q, rom_1_data, rom_2_data, rom_3_data, shifter_1_out, shifter_2_out,
       sixt_bit_gatekeeper_1_out_3, sixt_bit_gatekeeper_2_out_3, sixt_bit_gatekeeper_3_out_3,
       sixt_bit_gatekeeper_4_out_3, sixt_bit_gatekeeper_5_out_3, sixt_bit_incrementer_1_out_2,
       stacker_1_change_mask, stacker_1_control_bus_1_out, stacker_1_control_bus_2_out,
       stacker_1_to_data_bus, temp_registers_1_data_bus_out, temp_registers_1_out_9, temp_registers_1_out_11,
       temp_registers_1_out_12, temp_registers_1_to_pk, unstacker_1_control_bus_1_out,
       unstacker_1_control_bus_2_out;
  wire [31:0] tick_counter_1_cycle_count, tick_counter_1_negedge_count;

  Button button_1 (.out(button_1_out));
  sixt_bit_eq_cmp sixt_bit_eq_cmp_1 (.in_1(16'h1), .in_2(rom_2_data), .out_3(sixt_bit_eq_cmp_1_out_3));
  and and_1 (and_1_out, clock, ~sixt_bit_eq_cmp_2_out_3, ~or_1_out);  // AND_Gate
  or or_1 (or_1_out, button_1_out, reset);
  Register #(.trigger("falling"), .width(16)) register_1 (
    .D(data_bus_in), .en(sixt_bit_eq_cmp_1_out_3), .clk(and_1_out), .Q(current_instr), .clr(or_1_out));
  ROM #(.dataWidth(16)) rom_1 (.addr(multiplexer_1_out), .data(rom_1_data));
  Multiplexer #(.width(8)) multiplexer_1 (
    .in0(data_bus_in[7:0]), .in1(8'hfe), .out(multiplexer_1_out), .sel(and_2_out));
  interrupt_queue interrupt_queue_1 (
    .next_ir(and_3_out), .pins_in(interrupt_pins), .reset(or_1_out), .waiting(interrupt_queue_1_waiting),
    .id(interrupt_queue_1_id));
  // Probe on temp_registers_1_out_12
  // Probe on temp_registers_1_out_9
  // Probe on temp_registers_1_out_11
  temp_registers temp_registers_1 (
    .clock(and_1_out), .reset(or_1_out), .control_bus_1(control_bus_1), .control_bus_2(control_bus_2),
    .data_bus_in(data_bus_in), .ram_direct(RAM_direct), .out_9(temp_registers_1_out_9),
    .out_11(temp_registers_1_out_11), .out_12(temp_registers_1_out_12),
    .data_bus_out(temp_registers_1_data_bus_out), .to_pk(temp_registers_1_to_pk), .addr_bus_out(addr_bus_out));
  Register #(.width(1)) register_2 (
    .D(interrupt_queue_1_waiting), .clk(and_1_out), .Q(register_2_q), .clr(or_1_out));  // open: en
  sixt_bit_eq_cmp sixt_bit_eq_cmp_2 (.in_1(current_instr), .in_2(16'hff), .out_3(sixt_bit_eq_cmp_2_out_3));
  interrupt_table interrupt_table_1 (
    .control_bus_1(control_bus_1), .control_bus_2(control_bus_2), .id(interrupt_queue_1_id),
    .data_in(data_bus_in), .clk(and_1_out), .reset(or_1_out), .ih_addr(interrupt_table_1_ih_addr),
    .to_data_bus(interrupt_table_1_to_data_bus));
  sixt_bit_gatekeeper sixt_bit_gatekeeper_1 (
    .in_1(register_3_q), .in_2(interrupt_table_1_ih_addr), .out_3(sixt_bit_gatekeeper_1_out_3));
  and and_2 (and_2_out, sixt_bit_eq_cmp_3_out_3, interrupt_queue_1_waiting);
  assign data_bus_out = stacker_1_to_data_bus | interrupt_table_1_to_data_bus | temp_registers_1_data_bus_out;  // OR_Gate or_2, 16 bits wide
  assign to_pk = temp_registers_1_to_pk | sixt_bit_gatekeeper_1_out_3;  // OR_Gate or_3, 16 bits wide
  Register #(.trigger("falling"), .width(1)) register_3 (
    .D(interrupt_queue_1_waiting), .en(sixt_bit_eq_cmp_3_out_3), .clk(and_1_out), .Q(register_3_q),
    .clr(or_1_out));
  Multiplexer #(.width(16)) multiplexer_2 (
    .in0(sixt_bit_incrementer_1_out_2), .in1(rom_1_data), .out(multiplexer_2_out),
    .sel(sixt_bit_eq_cmp_3_out_3));
  sixt_bit_eq_cmp sixt_bit_eq_cmp_3 (.in_1(16'h1), .in_2(rom_2_data), .out_3(sixt_bit_eq_cmp_3_out_3));
  Multiplexer #(.width(16)) multiplexer_3 (
    .in0(multiplexer_2_out), .in1({16{1'b1}}), .out(multiplexer_3_out), .sel(comparator_1_lt));
  sixt_bit_eq_cmp sixt_bit_eq_cmp_4 (.in_1(16'hfffe), .in_2(rom_2_data), .out_3(sixt_bit_eq_cmp_4_out_3));
  Register #(.trigger("falling"), .width(1)) register_4 (
    .D(stacker_1_active), .en(register_3_q), .clk(and_1_out), .Q(register_4_q), .clr(or_1_out));
  // Probe on multiplexer_3_out
  Register #(.trigger("falling"), .width(16)) register_5 (
    .D(multiplexer_3_out), .en(or_5_out), .clk(and_1_out), .Q(register_5_q), .clr(or_4_out));
  or or_4 (or_4_out, sixt_bit_eq_cmp_4_out_3, or_1_out);
  sixt_bit_eq_cmp sixt_bit_eq_cmp_5 (.in_1({16{1'b0}}), .in_2(register_5_q), .out_3(sixt_bit_eq_cmp_5_out_3));
  buf buffer_1 (buffer_1_out, buffer_4_out);
  buf buffer_2 (buffer_2_out, buffer_1_out);
  buf buffer_3 (buffer_3_out, register_4_q);
  buf buffer_4 (buffer_4_out, buffer_3_out);
  ROM #(.addrWidth(16), .dataWidth(16)) rom_2 (.addr(register_5_q), .data(rom_2_data));
  ROM #(.addrWidth(16), .dataWidth(16)) rom_3 (.addr(register_5_q), .data(rom_3_data));
  and and_3 (and_3_out, ~register_4_q, buffer_2_out);  // AND_Gate
  sixt_bit_incrementer sixt_bit_incrementer_1 (.in_1(register_5_q), .out_2(sixt_bit_incrementer_1_out_2));
  tick_counter tick_counter_1 (
    .clock(and_1_out), .reset(or_1_out), .cycle_count(tick_counter_1_cycle_count),
    .negedge_count(tick_counter_1_negedge_count));  // open: posedge_count
  or or_5 (or_5_out, d_ff_1_q, comparator_1_lt);
  // Probe on tick_counter_1_cycle_count
  Comparator #(.width(32)) comparator_1 (
    .a(tick_counter_1_negedge_count), .b(32'h1), .gt(comparator_1_gt), .lt(comparator_1_lt));  // open: eq
  and and_4 (and_4_out, comparator_1_gt, ~sixt_bit_eq_cmp_2_out_3);  // AND_Gate
  sixt_bit_eq_cmp sixt_bit_eq_cmp_6 (.in_2(rom_2_data));  // open: in_1, out_3
  microcode_mixer microcode_mixer_1 (
    .microcode_in(rom_2_data), .instruction(current_instr), .tmpa_in(temp_registers_1_out_12),
    .tmpb_in(data_bus_in), .microcode_out(microcode_mixer_1_microcode_out));
  microcode_mixer microcode_mixer_2 (
    .microcode_in(rom_3_data), .instruction(current_instr), .tmpa_in(temp_registers_1_out_12),
    .tmpb_in(data_bus_in), .microcode_out(microcode_mixer_2_microcode_out));
  sixt_bit_gatekeeper sixt_bit_gatekeeper_2 (
    .in_1(and_4_out), .in_2(microcode_mixer_1_microcode_out), .out_3(sixt_bit_gatekeeper_2_out_3));
  sixt_bit_gatekeeper sixt_bit_gatekeeper_3 (
    .in_1(and_4_out), .in_2(microcode_mixer_2_microcode_out), .out_3(sixt_bit_gatekeeper_3_out_3));
  D_Flip_Flop #(.trigger("falling")) d_ff_1 (
    .D(nor_1_out), .clk(and_1_out), .Q(d_ff_1_q), .reset(or_1_out));  // open: Qn, preset
  Multiplexer #(.width(16)) multiplexer_4 (
    .in0(sixt_bit_gatekeeper_2_out_3), .in1(or_7_out), .out(control_bus_1_out), .sel(or_9_out));
  Multiplexer #(.width(16)) multiplexer_5 (
    .in0(sixt_bit_gatekeeper_3_out_3), .in1(or_8_out), .out(control_bus_2_out), .sel(or_9_out));
  nor nor_1 (nor_1_out, unstacker_1_active, stacker_1_active);
  eight_bit_eq_cmp eight_bit_eq_cmp_1 (.in_1(8'h24), .in_2(control_bus_1_out[7:0]), .out_3(eight_bit_eq_cmp_1_out_3));
  Shifter #(.width(16)) shifter_1 (.in(16'h1), .\dist (control_bus_1_out[15:12]), .out(shifter_1_out));
  eight_bit_eq_cmp eight_bit_eq_cmp_2 (.in_1(8'h24), .in_2(control_bus_2_out[7:0]), .out_3(eight_bit_eq_cmp_2_out_3));
  Shifter #(.width(16)) shifter_2 (.in(16'h1), .\dist (control_bus_2_out[15:12]), .out(shifter_2_out));
  assign or_6_out = sixt_bit_gatekeeper_4_out_3 | sixt_bit_gatekeeper_5_out_3;  // OR_Gate or_6, 16 bits wide
  sixt_bit_gatekeeper sixt_bit_gatekeeper_4 (
    .in_1(eight_bit_eq_cmp_1_out_3), .in_2(shifter_1_out), .out_3(sixt_bit_gatekeeper_4_out_3));
  sixt_bit_gatekeeper sixt_bit_gatekeeper_5 (
    .in_1(eight_bit_eq_cmp_2_out_3), .in_2(shifter_2_out), .out_3(sixt_bit_gatekeeper_5_out_3));
  sixt_bit_eq_cmp sixt_bit_eq_cmp_7 (.in_1(control_bus_1_out), .in_2(16'h60), .out_3(sixt_bit_eq_cmp_7_out_3));
  // Probe on stacker_1_change_mask
  stacker stacker_1 (
    .clk(and_1_out), .reset(or_1_out), .mem_in(RAM_direct), .register_write(or_6_out),
    .stacking_mask(preservation_mask), .write_changemask(sixt_bit_eq_cmp_8_out_3),
    .bypass_mask(register_2_q), .enable(sixt_bit_eq_cmp_7_out_3),
    .control_bus_1_out(stacker_1_control_bus_1_out), .control_bus_2_out(stacker_1_control_bus_2_out),
    .to_data_bus(stacker_1_to_data_bus), .active(stacker_1_active), .change_mask(stacker_1_change_mask));
  assign or_7_out = stacker_1_control_bus_1_out | unstacker_1_control_bus_1_out;  // OR_Gate or_7, 16 bits wide
  assign or_8_out = stacker_1_control_bus_2_out | unstacker_1_control_bus_2_out;  // OR_Gate or_8, 16 bits wide
  or or_9 (or_9_out, stacker_1_active, unstacker_1_active);
  // Probe on control_bus_1_out
  sixt_bit_eq_cmp sixt_bit_eq_cmp_8 (.in_1(control_bus_1_out), .in_2(16'h61), .out_3(sixt_bit_eq_cmp_8_out_3));
  unstacker unstacker_1 (
    .unstacking_mask(RAM_direct), .enable(sixt_bit_eq_cmp_8_out_3), .clk(and_1_out), .reset(or_1_out),
    .control_bus_1_out(unstacker_1_control_bus_1_out), .control_bus_2_out(unstacker_1_control_bus_2_out),
    .active(unstacker_1_active));
  // Probe on control_bus_2_out
  // Probe on stack_pointer
  // Probe on addr_bus

  // Notes on the sheet:
  //   contents of rom_1 (hex, n*v repeats v):
  //   2 4 7 a d 10 13 16 19 1c 1f 22 25 28 2b 31 37 3d 43 49 4f 52 55 58 5b 61 67 6d 73 79 7f 84 8a 8f 93
  //   99 a0 a4 aa b1 b4 b8 bb be c3 c6 c9 ce d2 d7 da de e4 e7 eb f1 f8 fe 103 108 110 115 11a 123 126 12a
  //   12d 131 136 139 13d 142 146 14b 14e 152 158 15b 15f 165 16b 172 177 17c 184 189 18e 1ee 1e8 1eb 1f7
  //   1fa 206 20c 21e 218 21b 227 233 236 23c 197 19b 19f 1a3 1a7 1ab 1af 1b3 1b7 1bb 1bf 1c3 1c7 1cb 1cf
  //   1d3 1d7 1db 1df 1e2 1e5 1f1 1f4 1fd 200 203 209 20f 212 215 221 224 22a 22d 230 239 23f 241 245 249
  //   24d 251 256 25a 25e 263 265 26a 26d 271 276 279 27d 282 288 28d 28f 291 295 299 29b 2a3 2a7 2a9 2ac
  //   2af 2b4 86*0 2b8
  //   contents of rom_2 (hex, n*v repeats v):
  //   11 1 0 fffe 4 6 fffe 10a0 4010 fffe 10a0 4010 fffe 10a0 4010 fffe 10a0 4010 fffe 10a0 4010 fffe 10a0
  //   4010 fffe 12c7 4010 fffe 12c7 4010 fffe 12c7 4010 fffe 12c7 4010 fffe 12c7 4010 fffe 12c7 4010 fffe
  //   10 11 102f 50 4010 fffe 10 11 102f 50 4010 fffe 10 11 102f 50 4010 fffe 10 11 102f 50 4010 fffe 10
  //   11 102f 50 4010 fffe 10 11 102f 50 4010 fffe 12c6 4010 fffe 12c6 4010 fffe 12c6 4010 fffe 12c6 4010
  //   fffe 10 11 102f 50 4010 fffe 10 11 102f 50 4010 fffe 10 11 102f 50 4010 fffe 10 11 102f 50 4010 fffe
  //   10 11 102f 50 4010 fffe 10 11 102f 50 4010 fffe 10a0 2006 10a4 20a4 fffe 11 2006 3006 3002 25 fffe
  //   11 2006 3006 27 fffe 11 53 25 fffe 11 2006 3006 2003 25 fffe 11 2006 5006 1a3 50 25 fffe 11 53 25
  //   fffe 11 2006 3006 2003 25 fffe 11 2006 5006 1085 50 25 fffe 11 10a4 fffe 11 53 10a4 fffe 20a0 10a4
  //   fffe 2a2 10a4 fffe 11 5006 2a3 10a4 fffe 2082 10a4 fffe 2084 10a4 fffe 11 5006 2085 10a4 fffe 11 50
  //   25 fffe 11 53 50 25 fffe 1a1 25 fffe 2a2 50 25 fffe 11 5006 2a3 50 25 fffe 1a1 25 fffe 2084 50 25
  //   fffe 11 5006 2085 50 25 fffe 11 5006 2006 1a1 2002 26 fffe 11 5006 53 50 26 fffe 11 5006 20a0 26
  //   fffe 11 5006 50 26 fffe 11 5006 2a3 2006 5006 2002 26 fffe 11 5006 2082 26 fffe 11 5006 50 26 fffe
  //   11 2006 5006 2085 3006 5006 3002 26 fffe 11 1086 fffe 11 53 1086 fffe 20a0 1086 fffe 2a1 27 1086
  //   fffe 11 5006 28 1086 fffe 2082 1086 fffe 2083 27 1086 fffe 11 5006 28 1086 fffe 11 50 25 fffe 11 53
  //   50 25 fffe 20a0 25 fffe 2a2 50 25 fffe 11 5006 2a3 50 25 fffe 2082 25 fffe 2084 50 25 fffe 11 5006
  //   2085 50 25 fffe 11 5006 11 50 26 fffe 11 5006 11 53 50 26 fffe 11 5006 20a0 26 fffe 11 5006 50 26
  //   fffe 11 2006 5006 3006 5006 3002 26 fffe 11 5006 2082 26 fffe 11 5006 50 26 fffe 11 2006 5006 2085
  //   3006 5006 3002 26 fffe 4002 102f 10a4 fffe 4002 102f 10a4 fffe 4002 102f 10a4 fffe 4002 102f 10a4
  //   fffe 4002 102f 10a4 fffe 4002 102f 10a4 fffe 4002 102f 10a4 fffe 4002 102f 10a4 fffe 4002 102f 10a4
  //   fffe 4002 102f b0a4 fffe 4002 102f b0a4 fffe 4002 102f b0a4 fffe 4002 102f b0a4 fffe 4002 102f b0a4
  //   fffe 4002 102f b0a4 fffe 4002 102f b0a4 fffe 4002 102f b0a4 fffe 4002 102f b0a4 fffe 12c0 10a4 fffe
  //   12c1 10a4 fffe 12c2 10a4 fffe 11c3 10a4 fffe 11c4 10a4 fffe 11c5 10a4 fffe 12c6 10a4 fffe 12c7 10a4
  //   fffe 11c8 10a4 fffe 11cc 10a4 fffe 12c9 10a4 fffe 12ca 10a4 fffe 12cb 10a4 fffe 11cd 10a4 fffe 12cf
  //   10a4 fffe 11ce 10a4 fffe 12c0 b0a4 fffe 12c1 b0a4 fffe 12c2 b0a4 fffe 12c3 10a4 fffe 12c4 10a4 fffe
  //   12c5 10a4 fffe 12c6 b0a4 fffe 12c7 b0a4 fffe 12c8 10a4 fffe 12c9 b0a4 fffe 12ca b0a4 fffe 12cb b0a4
  //   fffe 12cc 10a4 fffe 12cd 10a4 fffe 12cf b0a4 fffe 12ce 10a4 fffe 1011 fffe 11 50 25 fffe 11 50 25
  //   fffe 1011 1003 25 fffe 1a2 50 25 fffe 11 5006 50 26 fffe 1011 1003 25 fffe 1084 50 25 fffe 11 5006
  //   50 26 fffe 1010 fffe 11 2006 50 25 fffe 1004 10a4 fffe 1004 50 25 fffe 11 5006 50 26 fffe 1004 1086
  //   fffe 1004 50 25 fffe 11 5006 50 26 fffe 11 2006 50 25 60 fffe 1004 61 1004 6 fffe 10b0 fffe 10b1
  //   fffe 10a0 4006 10b0 fffe 10a0 4006 10b1 fffe 10b2 fffe 10b3 fffe 10b2 fffe 10a0 4006 b0b3 fffe 10a0
  //   4006 b0b2 fffe 10b3 fffe 10b4 20a4 fffe 20a0 10b5 fffe 10a0 4006 b0b4 20a4 fffe 10a0 4006 b0b5 fffe
  //   1011 2 25 60 fffe
  //   contents of rom_3 (hex, n*v repeats v):
  //   7*0 10 15 0 10 16 0 10 17 0 10 18 0 10 19 0 10 1a 0 10 15 0 10 16 0 10 17 0 10 19 0 10 1a 0 10 18 0
  //   0 0 1047 10 15 0 0 0 1047 10 16 0 0 0 1047 10 17 0 0 0 1047 10 19 0 0 0 1047 10 1a 0 0 0 1047 10 18
  //   0 10 17 0 10 19 0 10 1a 0 10 18 0 0 0 1047 10 15 0 0 0 1047 10 16 0 0 0 1047 10 17 0 0 0 1047 10 19
  //   0 0 0 1047 10 1a 0 0 0 1047 10 18 0 0 20a0 2002 0 0 0 11 2003 51 0 0 0 11 53 0 0 0 10a0 0 0 0 1a2 0
  //   3002 0 0 0 4 0 0 2003 0 0 0 1082 0 0 0 1084 0 3002 0 0 0 11 0 0 2003 6*0 27 25*0 1a1 0 0 0 27 1a1 0
  //   0 20a0 0 0 0 1a1 5*0 1a1 0 0 2082 0 0 0 1a1 5*0 1a1 0 0 0 11 0 51 51 0 0 0 11 27 1a1 4*0 1a1 0 0 0
  //   2a2 1a1 5*0 11 0 1a1 4*0 1a1 0 0 0 2084 1a1 0 0 0 11 0 0 2002 0 1a1 6*0 27 10*0 2a1 11*0 2083 4*0
  //   1083 0 0 0 27 1083 0 0 1083 0 0 0 1083 5*0 1083 0 0 1083 0 0 0 1083 5*0 1083 5*0 1083 5*0 27 1083
  //   4*0 1083 0 0 0 2a2 1083 0 0 0 11 2a3 2002 0 1083 4*0 1083 0 0 0 2084 1083 0 0 0 11 0 0 2002 0 1083 0
  //   0 0 10c0 0 0 0 10c1 0 0 0 10c2 0 0 0 10c6 0 0 0 10c7 0 0 0 10c9 0 0 0 10ca 0 0 0 10cb 0 0 0 10cf 0 0
  //   0 12c0 0 0 0 12c1 0 0 0 12c2 0 0 0 12c6 0 0 0 12c7 0 0 0 12c9 0 0 0 12ca 0 0 0 12cb 0 0 0 12cf 100*0
  //   1011 1003 0 0 1011 1003 0 0 0 10a0 0 0 1011 1003 0 0 1011 1a2 1003 0 0 0 1082 0 0 1011 1003 0 0 1011
  //   1082 1003 5*0 1004 2003 1010 0 0 1010 0 0 1a1 1010 0 0 1004 1a1 1010 0 0 1010 0 0 1083 1010 0 0 1004
  //   1083 1010 0 1011 2 1003 13 0 0 1010 0 1010 45*0 12 1003 1b
endmodule

module four_bit_incrementer (
  input  [3:0] in_1,
  output [3:0] out_2
);

  wire and_1_out, and_2_out, and_3_out, and_4_out, and_5_out, xor_2_out, xor_3_out, xor_4_out, xor_8_out,
       xor_9_out;

  xor xor_1 (out_2[0], in_1[0], 1'b1);
  and and_1 (and_1_out, in_1[0], 1'b1);
  xor xor_2 (xor_2_out, in_1[1], 1'b0);
  and and_2 (and_2_out, in_1[1], 1'b0);
  xor xor_3 (xor_3_out, in_1[2], 1'b0);
  and and_3 (and_3_out, in_1[2], 1'b0);
  xor xor_4 (xor_4_out, in_1[3], 1'b0);
  xor xor_5 (out_2[1], xor_2_out, and_1_out);
  and and_4 (and_4_out, xor_2_out, and_1_out);
  xor xor_6 (out_2[2], xor_3_out, xor_8_out);
  and and_5 (and_5_out, xor_3_out, xor_8_out);
  xor xor_7 (out_2[3], xor_4_out, xor_9_out);
  xor xor_8 (xor_8_out, and_2_out, and_4_out);
  xor xor_9 (xor_9_out, and_3_out, and_5_out);
endmodule

module special_registers (
  input  [15:0] data_bus_in,
  input  [15:0] control_bus_1,
  input  [15:0] control_bus_2,
  input  [15:0] temp_register,
  input  [15:0] sp_reset_value,
  input  clock,
  input  reset,
  output [15:0] program_kounter,
  output [15:0] data_bus_out,
  output [15:0] addr_bus_out,
  output [15:0] stack_pointer,
  output [15:0] offset_out
);

  wire and_1_out, and_2_out, and_3_out, buffer_1_out, buffer_2_out, buffer_3_out, buffer_4_out, buffer_5_out,
       buffer_6_out, buffer_7_out, d_ff_1_q, not_1_out, or_1_out, or_3_out, or_4_out, or_5_out, or_6_out,
       or_7_out, or_8_out, or_9_out, or_10_out, or_11_out, or_12_out, or_13_out, or_14_out, or_15_out,
       or_16_out, or_17_out, or_18_out, or_19_out, s_r_ff_1_qn, s_r_ff_2_q, s_r_ff_3_q,
       sixt_bit_eq_zero_1_out_2, special_registers_opdec_1_offs_to_addr,
       special_registers_opdec_1_offs_to_data, special_registers_opdec_1_offs_write,
       special_registers_opdec_1_pk_dec, special_registers_opdec_1_pk_inc,
       special_registers_opdec_1_pk_to_addr, special_registers_opdec_1_pk_to_data,
       special_registers_opdec_1_pk_write, special_registers_opdec_1_sp_dec,
       special_registers_opdec_1_sp_inc, special_registers_opdec_1_sp_predec_to_addr,
       special_registers_opdec_1_sp_to_addr, special_registers_opdec_1_sp_to_data,
       special_registers_opdec_1_sp_write, special_registers_opdec_2_offs_to_addr,
       special_registers_opdec_2_offs_to_data, special_registers_opdec_2_offs_write,
       special_registers_opdec_2_pk_dec, special_registers_opdec_2_pk_inc,
       special_registers_opdec_2_pk_to_addr, special_registers_opdec_2_pk_to_data,
       special_registers_opdec_2_pk_write, special_registers_opdec_2_sp_dec,
       special_registers_opdec_2_sp_inc, special_registers_opdec_2_sp_predec_to_addr,
       special_registers_opdec_2_sp_to_addr, special_registers_opdec_2_sp_to_data,
       special_registers_opdec_2_sp_write;
  wire [15:0] multiplexer_1_out, multiplexer_2_out, or_2_out, or_21_out, or_22_out, or_24_out, or_25_out,
       sixt_bit_gatekeeper_1_out_3, sixt_bit_gatekeeper_2_out_3, sixt_bit_gatekeeper_3_out_3,
       sixt_bit_gatekeeper_4_out_3, sixt_bit_gatekeeper_5_out_3, sixt_bit_gatekeeper_6_out_3,
       special_registers_opdec_1_data_to_pk, special_registers_opdec_2_data_to_pk, subtractor_1_out;

  Pull_Resistor pull_resistor_1 (.node(sp_reset_value));
  S_R_Flip_Flop s_r_ff_1 (.Qn(s_r_ff_1_qn), .preset(clock));  // open: S, R, clk, Q, reset
  Multiplexer #(.width(16)) multiplexer_1 (
    .in0(16'hff00), .in1(sp_reset_value), .out(multiplexer_1_out), .sel(not_1_out));
  not not_1 (not_1_out, sixt_bit_eq_zero_1_out_2);
  sixt_bit_eq_zero sixt_bit_eq_zero_1 (.in_1(sp_reset_value), .out_2(sixt_bit_eq_zero_1_out_2));
  or or_1 (or_1_out, s_r_ff_1_qn, reset);
  buf buffer_1 (buffer_1_out, clock);
  buf buffer_2 (buffer_2_out, buffer_1_out);
  buf buffer_3 (buffer_3_out, buffer_2_out);
  buf buffer_4 (buffer_4_out, buffer_3_out);
  S_R_Flip_Flop s_r_ff_2 (.Q(s_r_ff_2_q), .reset(and_1_out), .preset(or_1_out));  // open: S, R, clk, Qn
  and and_1 (and_1_out, ~s_r_ff_3_q, buffer_7_out, s_r_ff_2_q);  // AND_Gate
  special_registers_opdec special_registers_opdec_1 (
    .data_in(data_bus_in), .ctrl_unit_in(temp_register), .control(control_bus_2),
    .sp_to_data(special_registers_opdec_1_sp_to_data), .sp_to_addr(special_registers_opdec_1_sp_to_addr),
    .sp_write(special_registers_opdec_1_sp_write), .sp_inc(special_registers_opdec_1_sp_inc),
    .sp_dec(special_registers_opdec_1_sp_dec),
    .sp_predec_to_addr(special_registers_opdec_1_sp_predec_to_addr),
    .offs_to_data(special_registers_opdec_1_offs_to_data),
    .offs_to_addr(special_registers_opdec_1_offs_to_addr), .offs_write(special_registers_opdec_1_offs_write),
    .data_to_pk(special_registers_opdec_1_data_to_pk), .pk_to_data(special_registers_opdec_1_pk_to_data),
    .pk_to_addr(special_registers_opdec_1_pk_to_addr), .pk_inc(special_registers_opdec_1_pk_inc),
    .pk_dec(special_registers_opdec_1_pk_dec), .pk_write(special_registers_opdec_1_pk_write));
  Multiplexer #(.width(16)) multiplexer_2 (
    .in0(data_bus_in), .in1(multiplexer_1_out), .out(multiplexer_2_out), .sel(s_r_ff_2_q));
  and and_2 (and_2_out, clock, ~buffer_4_out);  // AND_Gate
  D_Flip_Flop d_ff_1 (.D(clock), .clk(s_r_ff_2_q), .Q(d_ff_1_q), .reset(and_2_out));  // open: Qn, preset
  buf buffer_5 (buffer_5_out, and_2_out);
  buf buffer_6 (buffer_6_out, buffer_5_out);
  buf buffer_7 (buffer_7_out, buffer_6_out);
  S_R_Flip_Flop s_r_ff_3 (.Q(s_r_ff_3_q), .reset(and_2_out), .preset(and_3_out));  // open: S, R, clk, Qn
  special_registers_opdec special_registers_opdec_2 (
    .data_in(data_bus_in), .ctrl_unit_in(temp_register), .control(control_bus_1),
    .sp_to_data(special_registers_opdec_2_sp_to_data), .sp_to_addr(special_registers_opdec_2_sp_to_addr),
    .sp_write(special_registers_opdec_2_sp_write), .sp_inc(special_registers_opdec_2_sp_inc),
    .sp_dec(special_registers_opdec_2_sp_dec),
    .sp_predec_to_addr(special_registers_opdec_2_sp_predec_to_addr),
    .offs_to_data(special_registers_opdec_2_offs_to_data),
    .offs_to_addr(special_registers_opdec_2_offs_to_addr), .offs_write(special_registers_opdec_2_offs_write),
    .data_to_pk(special_registers_opdec_2_data_to_pk), .pk_to_data(special_registers_opdec_2_pk_to_data),
    .pk_to_addr(special_registers_opdec_2_pk_to_addr), .pk_inc(special_registers_opdec_2_pk_inc),
    .pk_dec(special_registers_opdec_2_pk_dec), .pk_write(special_registers_opdec_2_pk_write));
  assign or_2_out = special_registers_opdec_2_data_to_pk | special_registers_opdec_1_data_to_pk;  // OR_Gate or_2, 16 bits wide
  or or_3 (or_3_out, special_registers_opdec_2_pk_to_addr, special_registers_opdec_1_pk_to_addr);
  or or_4 (or_4_out, special_registers_opdec_2_pk_to_data, special_registers_opdec_1_pk_to_data);
  or or_5 (or_5_out, special_registers_opdec_2_pk_inc, special_registers_opdec_1_pk_inc);
  or or_6 (or_6_out, special_registers_opdec_2_pk_dec, special_registers_opdec_1_pk_dec);
  or or_7 (or_7_out, special_registers_opdec_2_pk_write, special_registers_opdec_1_pk_write);
  or or_8 (or_8_out, special_registers_opdec_2_sp_to_data, special_registers_opdec_1_sp_to_data);
  or or_9 (or_9_out, special_registers_opdec_2_sp_to_addr, special_registers_opdec_1_sp_to_addr);
  or or_10 (or_10_out, special_registers_opdec_2_sp_inc, special_registers_opdec_1_sp_inc);
  or or_11 (or_11_out, special_registers_opdec_2_sp_dec, special_registers_opdec_1_sp_dec);
  or or_12 (or_12_out, special_registers_opdec_2_sp_predec_to_addr, special_registers_opdec_1_sp_predec_to_addr);
  or or_13 (or_13_out, special_registers_opdec_2_sp_write, special_registers_opdec_1_sp_write);
  or or_14 (or_14_out, special_registers_opdec_2_offs_to_data, special_registers_opdec_1_offs_to_data);
  or or_15 (or_15_out, special_registers_opdec_2_offs_to_addr, special_registers_opdec_1_offs_to_addr);
  or or_16 (or_16_out, special_registers_opdec_2_offs_write, special_registers_opdec_1_offs_write);
  and and_3 (and_3_out, d_ff_1_q, ~s_r_ff_3_q);  // AND_Gate
  or or_17 (or_17_out, or_12_out, or_11_out);
  or or_18 (or_18_out, or_12_out, or_9_out);
  // Probe on or_2_out
  or or_19 (or_19_out, or_13_out, s_r_ff_2_q);
  counting_register counting_register_1 (
    .data_in(or_2_out), .increment(or_5_out), .decrement(or_6_out), .write(or_7_out), .clk(clock),
    .reset(or_1_out), .out_7(program_kounter));
  counting_register counting_register_2 (
    .data_in(multiplexer_2_out), .increment(or_10_out), .decrement(or_17_out), .write(or_19_out),
    .clk(clock), .out_7(stack_pointer));  // open: reset
  Register #(.width(16)) register_1 (.D(data_bus_in), .en(or_16_out), .clk(clock), .Q(offset_out), .clr(or_1_out));
  assign data_bus_out = sixt_bit_gatekeeper_1_out_3 | or_21_out;  // OR_Gate or_20, 16 bits wide
  sixt_bit_gatekeeper sixt_bit_gatekeeper_1 (
    .in_1(or_4_out), .in_2(program_kounter), .out_3(sixt_bit_gatekeeper_1_out_3));
  sixt_bit_gatekeeper sixt_bit_gatekeeper_2 (
    .in_1(or_3_out), .in_2(program_kounter), .out_3(sixt_bit_gatekeeper_2_out_3));
  assign or_21_out = sixt_bit_gatekeeper_3_out_3 | or_22_out;  // OR_Gate or_21, 16 bits wide
  sixt_bit_gatekeeper sixt_bit_gatekeeper_3 (
    .in_1(or_8_out), .in_2(stack_pointer), .out_3(sixt_bit_gatekeeper_3_out_3));
  sixt_bit_gatekeeper sixt_bit_gatekeeper_4 (
    .in_1(or_18_out), .in_2(stack_pointer), .out_3(sixt_bit_gatekeeper_4_out_3));
  Subtractor #(.width(16)) subtractor_1 (
    .a(sixt_bit_gatekeeper_4_out_3), .b({16{1'b0}}), .out(subtractor_1_out), .bin(or_12_out));  // open: bout
  assign or_22_out = sixt_bit_gatekeeper_5_out_3 | sixt_bit_gatekeeper_5_out_3;  // OR_Gate or_22, 16 bits wide
  sixt_bit_gatekeeper sixt_bit_gatekeeper_5 (.in_1(or_14_out), .in_2(offset_out), .out_3(sixt_bit_gatekeeper_5_out_3));
  sixt_bit_gatekeeper sixt_bit_gatekeeper_6 (.in_1(or_15_out), .in_2(offset_out), .out_3(sixt_bit_gatekeeper_6_out_3));
  // Probe on program_kounter
  assign addr_bus_out = sixt_bit_gatekeeper_2_out_3 | or_24_out;  // OR_Gate or_23, 16 bits wide
  // Probe on stack_pointer
  assign or_24_out = subtractor_1_out | or_25_out;  // OR_Gate or_24, 16 bits wide
  assign or_25_out = sixt_bit_gatekeeper_6_out_3 | sixt_bit_gatekeeper_6_out_3;  // OR_Gate or_25, 16 bits wide

  // Notes on the sheet:
  //   this part handles automatic
  //   resetting of sp to a default
  //   value
  //   --->
endmodule

module temp_registers (
  input  [15:0] data_bus_in,
  input  [15:0] control_bus_1,
  input  [15:0] control_bus_2,
  input  [15:0] ram_direct,
  input  clock,
  input  reset,
  output [15:0] data_bus_out,
  output [15:0] addr_bus_out,
  output [15:0] out_9,
  output [15:0] to_pk,
  output [15:0] out_11,
  output [15:0] out_12
);

  wire or_1_out, or_2_out, sixt_bit_eq_cmp_1_out_3, sixt_bit_eq_cmp_2_out_3, sixt_bit_eq_cmp_3_out_3,
       special_register_dual_opdec_1_addr_bus_enable, special_register_dual_opdec_1_data_bus_enable,
       special_register_dual_opdec_1_write_enable, special_register_dual_opdec_2_addr_bus_enable,
       special_register_dual_opdec_2_data_bus_enable, special_register_dual_opdec_2_write_enable,
       special_register_dual_opdec_3_addr_bus_enable, special_register_dual_opdec_3_data_bus_enable,
       special_register_dual_opdec_3_write_enable;
  wire [15:0] multiplexer_1_out, register_1_q, sixt_bit_gatekeeper_1_out_3, sixt_bit_gatekeeper_2_out_3,
       sixt_bit_gatekeeper_3_out_3, sixt_bit_gatekeeper_4_out_3, sixt_bit_gatekeeper_5_out_3,
       sixt_bit_gatekeeper_6_out_3, sixt_bit_gatekeeper_7_out_3, sixt_bit_gatekeeper_8_out_3,
       sixt_bit_gatekeeper_9_out_3, special_register_dual_opdec_1_special_functions,
       special_register_dual_opdec_2_special_functions, special_register_dual_opdec_3_special_functions;

  Register #(.trigger("falling"), .width(16)) register_1 (
    .D(data_bus_in), .clk(clock), .Q(register_1_q), .clr(reset));  // open: en
  sixt_bit_eq_cmp sixt_bit_eq_cmp_1 (.in_1(control_bus_1), .in_2(16'h13), .out_3(sixt_bit_eq_cmp_1_out_3));
  sixt_bit_eq_cmp sixt_bit_eq_cmp_2 (.in_1(16'h13), .in_2(control_bus_2), .out_3(sixt_bit_eq_cmp_2_out_3));
  sixt_bit_eq_cmp sixt_bit_eq_cmp_3 (.in_1(control_bus_1), .in_2(16'h1), .out_3(sixt_bit_eq_cmp_3_out_3));
  special_register_dual_opdec special_register_dual_opdec_1 (
    .control_bus_2(control_bus_2), .id(4'b0010), .control_bus_1(control_bus_1),
    .data_bus_enable(special_register_dual_opdec_1_data_bus_enable),
    .addr_bus_enable(special_register_dual_opdec_1_addr_bus_enable),
    .write_enable(special_register_dual_opdec_1_write_enable),
    .special_functions(special_register_dual_opdec_1_special_functions));
  or or_1 (or_1_out, sixt_bit_eq_cmp_1_out_3, special_register_dual_opdec_1_special_functions[0], sixt_bit_eq_cmp_2_out_3);
  special_register_dual_opdec special_register_dual_opdec_2 (
    .control_bus_2(control_bus_2), .id(4'b0011), .control_bus_1(control_bus_1),
    .data_bus_enable(special_register_dual_opdec_2_data_bus_enable),
    .addr_bus_enable(special_register_dual_opdec_2_addr_bus_enable),
    .write_enable(special_register_dual_opdec_2_write_enable),
    .special_functions(special_register_dual_opdec_2_special_functions));
  special_register_dual_opdec special_register_dual_opdec_3 (
    .control_bus_2(control_bus_2), .id(4'b0100), .control_bus_1(control_bus_1),
    .data_bus_enable(special_register_dual_opdec_3_data_bus_enable),
    .addr_bus_enable(special_register_dual_opdec_3_addr_bus_enable),
    .write_enable(special_register_dual_opdec_3_write_enable),
    .special_functions(special_register_dual_opdec_3_special_functions));
  or or_2 (or_2_out, special_register_dual_opdec_3_write_enable, sixt_bit_eq_cmp_3_out_3);
  Register #(.width(16)) register_2 (
    .D(register_1_q), .en(special_register_dual_opdec_1_write_enable), .clk(clock), .Q(out_9), .clr(reset));
  Register #(.width(16)) register_3 (
    .D(register_1_q), .en(special_register_dual_opdec_2_write_enable), .clk(clock), .Q(out_11), .clr(reset));
  Multiplexer #(.width(16)) multiplexer_1 (
    .in0(register_1_q), .in1(ram_direct), .out(multiplexer_1_out), .sel(or_2_out));
  Register #(.trigger("falling"), .width(16)) register_4 (
    .D(multiplexer_1_out), .en(or_2_out), .clk(clock), .Q(out_12), .clr(reset));
  // Probe on out_12
  sixt_bit_gatekeeper sixt_bit_gatekeeper_1 (
    .in_1(special_register_dual_opdec_1_data_bus_enable), .in_2(out_9), .out_3(sixt_bit_gatekeeper_1_out_3));
  sixt_bit_gatekeeper sixt_bit_gatekeeper_2 (
    .in_1(special_register_dual_opdec_1_addr_bus_enable), .in_2(out_9), .out_3(sixt_bit_gatekeeper_2_out_3));
  sixt_bit_gatekeeper sixt_bit_gatekeeper_3 (.in_1(or_1_out), .in_2(out_9), .out_3(sixt_bit_gatekeeper_3_out_3));
  sixt_bit_gatekeeper sixt_bit_gatekeeper_4 (
    .in_1(special_register_dual_opdec_2_data_bus_enable), .in_2(out_11), .out_3(sixt_bit_gatekeeper_4_out_3));
  sixt_bit_gatekeeper sixt_bit_gatekeeper_5 (
    .in_1(special_register_dual_opdec_2_addr_bus_enable), .in_2(out_11), .out_3(sixt_bit_gatekeeper_5_out_3));
  sixt_bit_gatekeeper sixt_bit_gatekeeper_6 (
    .in_1(special_register_dual_opdec_2_special_functions[0]), .in_2(out_11),
    .out_3(sixt_bit_gatekeeper_6_out_3));
  sixt_bit_gatekeeper sixt_bit_gatekeeper_7 (
    .in_1(special_register_dual_opdec_3_data_bus_enable), .in_2(out_12), .out_3(sixt_bit_gatekeeper_7_out_3));
  sixt_bit_gatekeeper sixt_bit_gatekeeper_8 (
    .in_1(special_register_dual_opdec_3_addr_bus_enable), .in_2(out_12), .out_3(sixt_bit_gatekeeper_8_out_3));
  sixt_bit_gatekeeper sixt_bit_gatekeeper_9 (
    .in_1(special_register_dual_opdec_3_special_functions[0]), .in_2(out_12),
    .out_3(sixt_bit_gatekeeper_9_out_3));
  assign data_bus_out = sixt_bit_gatekeeper_1_out_3 | sixt_bit_gatekeeper_4_out_3 | sixt_bit_gatekeeper_7_out_3;  // OR_Gate or_3, 16 bits wide
  assign addr_bus_out = sixt_bit_gatekeeper_2_out_3 | sixt_bit_gatekeeper_8_out_3 | sixt_bit_gatekeeper_5_out_3;  // OR_Gate or_4, 16 bits wide
  assign to_pk = sixt_bit_gatekeeper_3_out_3 | sixt_bit_gatekeeper_9_out_3 | sixt_bit_gatekeeper_6_out_3;  // OR_Gate or_5, 16 bits wide
endmodule

module register_unit (
  input  [15:0] data_bus_in,
  input  [15:0] control_bus_1,
  input  [15:0] control_bus_2,
  input  clock,
  input  reset,
  output [15:0] data_bus_out,
  output [15:0] addr_bus_out,
  output [15:0] alu1_out,
  output [15:0] alu2_out
);

  wire and_5_out, and_6_out, and_7_out, and_8_out, and_9_out, and_10_out, and_11_out, and_12_out, and_13_out,
       and_14_out, and_15_out, and_16_out, and_17_out, and_18_out, and_19_out, and_20_out, and_21_out,
       and_22_out, and_23_out, and_24_out, eight_bit_eq_cmp_1_out_3, eight_bit_eq_cmp_2_out_3,
       eight_bit_eq_cmp_3_out_3, eight_bit_eq_cmp_4_out_3, eight_bit_eq_cmp_5_out_3,
       eight_bit_eq_cmp_6_out_3, eight_bit_eq_cmp_7_out_3, eight_bit_eq_cmp_8_out_3,
       eight_bit_eq_cmp_9_out_3, eight_bit_eq_cmp_10_out_3, eight_bit_eq_cmp_11_out_3,
       eight_bit_eq_cmp_12_out_3, four_bit_eq_cmp_1_out_3, four_bit_eq_cmp_2_out_3, four_bit_eq_cmp_3_out_3,
       four_bit_eq_cmp_4_out_3, four_bit_eq_cmp_5_out_3, four_bit_eq_cmp_6_out_3, four_bit_eq_cmp_7_out_3,
       four_bit_eq_cmp_8_out_3, four_bit_eq_cmp_9_out_3, four_bit_eq_cmp_10_out_3, four_bit_eq_cmp_11_out_3,
       four_bit_eq_cmp_12_out_3, four_bit_eq_cmp_13_out_3, four_bit_eq_cmp_14_out_3,
       four_bit_eq_cmp_15_out_3, four_bit_eq_cmp_16_out_3, four_bit_eq_cmp_17_out_3,
       four_bit_eq_cmp_18_out_3, four_bit_eq_cmp_19_out_3, four_bit_eq_cmp_20_out_3,
       four_bit_eq_cmp_21_out_3, four_bit_eq_cmp_22_out_3, four_bit_eq_cmp_23_out_3,
       four_bit_eq_cmp_24_out_3, four_bit_eq_cmp_25_out_3, four_bit_eq_cmp_26_out_3,
       four_bit_eq_cmp_27_out_3, four_bit_eq_cmp_28_out_3, four_bit_eq_cmp_29_out_3,
       four_bit_eq_cmp_30_out_3, four_bit_eq_cmp_31_out_3, four_bit_eq_cmp_32_out_3,
       four_bit_eq_cmp_33_out_3, four_bit_eq_cmp_34_out_3, or_1_out, or_2_out, or_3_out, or_4_out, or_5_out,
       or_6_out, or_7_out, or_8_out, or_9_out, or_10_out, or_11_out, or_14_out, or_15_out;
  wire [3:0] and_1_out, and_2_out, and_3_out, and_4_out, bit_extender_1_out, bit_extender_2_out,
       bit_extender_3_out, bit_extender_4_out, or_12_out, or_13_out;
  wire [15:0] and_25_out, and_26_out, and_27_out, and_28_out, and_29_out, and_30_out, and_31_out, and_32_out,
       and_33_out, and_34_out, and_35_out, and_36_out, and_37_out, and_38_out, and_39_out, and_40_out,
       and_41_out, and_42_out, and_43_out, and_44_out, and_45_out, and_46_out, and_47_out, and_48_out,
       and_49_out, and_50_out, and_51_out, and_52_out, and_53_out, and_54_out, and_55_out, and_56_out,
       bit_extender_5_out, bit_extender_6_out, bit_extender_7_out, bit_extender_8_out, bit_extender_9_out,
       bit_extender_10_out, bit_extender_11_out, bit_extender_12_out, bit_extender_13_out,
       bit_extender_14_out, bit_extender_15_out, bit_extender_16_out, bit_extender_17_out,
       bit_extender_18_out, bit_extender_19_out, bit_extender_20_out, bit_extender_21_out,
       bit_extender_22_out, bit_extender_23_out, bit_extender_24_out, bit_extender_25_out,
       bit_extender_26_out, bit_extender_27_out, bit_extender_28_out, bit_extender_29_out,
       bit_extender_30_out, bit_extender_31_out, bit_extender_32_out, bit_extender_33_out,
       bit_extender_34_out, bit_extender_35_out, bit_extender_36_out, or_16_out, or_17_out, or_18_out,
       or_19_out, or_20_out, or_21_out, or_22_out, or_23_out, or_24_out, or_25_out, or_26_out, or_27_out,
       or_28_out, or_29_out, or_30_out, or_31_out, or_32_out, or_33_out, or_34_out, or_35_out, or_36_out,
       or_37_out, or_38_out, or_39_out, or_40_out, or_41_out, or_42_out, or_43_out, or_44_out, or_45_out,
       or_46_out, or_47_out, register_1_q, register_2_q, register_3_q, register_4_q, register_5_q,
       register_6_q, register_7_q, register_8_q, register_9_q, register_10_q, register_11_q, register_12_q,
       register_13_q, register_14_q, register_15_q, register_16_q, register_17_q;

  four_bit_eq_cmp four_bit_eq_cmp_1 (.in_1(control_bus_1[7:4]), .in_2(4'b0100), .out_3(four_bit_eq_cmp_1_out_3));
  eight_bit_eq_cmp eight_bit_eq_cmp_1 (.in_1(control_bus_1[7:0]), .in_2(8'h20), .out_3(eight_bit_eq_cmp_1_out_3));
  eight_bit_eq_cmp eight_bit_eq_cmp_2 (.in_1(control_bus_1[7:0]), .in_2(8'h21), .out_3(eight_bit_eq_cmp_2_out_3));
  eight_bit_eq_cmp eight_bit_eq_cmp_3 (.in_1(control_bus_1[7:0]), .in_2(8'h22), .out_3(eight_bit_eq_cmp_3_out_3));
  eight_bit_eq_cmp eight_bit_eq_cmp_4 (.in_1(control_bus_1[7:0]), .in_2(8'h23), .out_3(eight_bit_eq_cmp_4_out_3));
  eight_bit_eq_cmp eight_bit_eq_cmp_5 (.in_1(control_bus_1[7:0]), .in_2(8'h24), .out_3(eight_bit_eq_cmp_5_out_3));
  eight_bit_eq_cmp eight_bit_eq_cmp_6 (.in_1(control_bus_1[7:0]), .in_2(8'h2f), .out_3(eight_bit_eq_cmp_6_out_3));
  eight_bit_eq_cmp eight_bit_eq_cmp_7 (.in_1(control_bus_2[7:0]), .in_2(8'h20), .out_3(eight_bit_eq_cmp_7_out_3));
  eight_bit_eq_cmp eight_bit_eq_cmp_8 (.in_1(control_bus_2[7:0]), .in_2(8'h21), .out_3(eight_bit_eq_cmp_8_out_3));
  eight_bit_eq_cmp eight_bit_eq_cmp_9 (.in_1(control_bus_2[7:0]), .in_2(8'h22), .out_3(eight_bit_eq_cmp_9_out_3));
  eight_bit_eq_cmp eight_bit_eq_cmp_10 (.in_1(control_bus_2[7:0]), .in_2(8'h23), .out_3(eight_bit_eq_cmp_10_out_3));
  eight_bit_eq_cmp eight_bit_eq_cmp_11 (.in_1(control_bus_2[7:0]), .in_2(8'h24), .out_3(eight_bit_eq_cmp_11_out_3));
  eight_bit_eq_cmp eight_bit_eq_cmp_12 (.in_1(control_bus_2[7:0]), .in_2(8'h2f), .out_3(eight_bit_eq_cmp_12_out_3));
  four_bit_eq_cmp four_bit_eq_cmp_2 (.in_1(control_bus_2[7:4]), .in_2(4'b0100), .out_3(four_bit_eq_cmp_2_out_3));
  Register #(.trigger("falling"), .width(16)) register_1 (
    .D(data_bus_in), .clk(clock), .Q(register_1_q), .clr(reset));  // open: en
  or or_1 (or_1_out, eight_bit_eq_cmp_2_out_3, or_2_out);
  or or_2 (or_2_out, eight_bit_eq_cmp_3_out_3, eight_bit_eq_cmp_4_out_3);
  or or_3 (or_3_out, eight_bit_eq_cmp_1_out_3, four_bit_eq_cmp_1_out_3, eight_bit_eq_cmp_5_out_3);
  or or_4 (or_4_out, eight_bit_eq_cmp_8_out_3, or_5_out);
  or or_5 (or_5_out, eight_bit_eq_cmp_9_out_3, eight_bit_eq_cmp_10_out_3);
  assign bit_extender_1_out = {{3{or_6_out}}, or_6_out};  // Bit_Extender bit_extender_1
  or or_6 (or_6_out, four_bit_eq_cmp_1_out_3, or_1_out);
  assign bit_extender_2_out = {{3{or_3_out}}, or_3_out};  // Bit_Extender bit_extender_2
  assign bit_extender_3_out = {{3{or_7_out}}, or_7_out};  // Bit_Extender bit_extender_3
  or or_7 (or_7_out, four_bit_eq_cmp_2_out_3, or_4_out);
  assign bit_extender_4_out = {{3{or_8_out}}, or_8_out};  // Bit_Extender bit_extender_4
  or or_8 (or_8_out, eight_bit_eq_cmp_7_out_3, four_bit_eq_cmp_2_out_3, eight_bit_eq_cmp_11_out_3);
  assign and_1_out = bit_extender_1_out & control_bus_1[11:8];  // AND_Gate and_1, 4 bits wide
  assign and_2_out = bit_extender_2_out & control_bus_1[15:12];  // AND_Gate and_2, 4 bits wide
  assign and_3_out = bit_extender_3_out & control_bus_2[11:8];  // AND_Gate and_3, 4 bits wide
  assign and_4_out = bit_extender_4_out & control_bus_2[15:12];  // AND_Gate and_4, 4 bits wide
  or or_9 (or_9_out, eight_bit_eq_cmp_1_out_3, eight_bit_eq_cmp_7_out_3);
  or or_10 (or_10_out, or_1_out, or_4_out);
  or or_11 (or_11_out, eight_bit_eq_cmp_5_out_3, eight_bit_eq_cmp_11_out_3);
  assign or_12_out = and_1_out | and_3_out;  // OR_Gate or_12, 4 bits wide
  assign or_13_out = and_2_out | and_4_out;  // OR_Gate or_13, 4 bits wide
  assign bit_extender_5_out = {{15{four_bit_eq_cmp_3_out_3}}, four_bit_eq_cmp_3_out_3};  // Bit_Extender bit_extender_5
  four_bit_eq_cmp four_bit_eq_cmp_3 (.in_1(or_13_out), .in_2(4'b0000), .out_3(four_bit_eq_cmp_3_out_3));
  four_bit_eq_cmp four_bit_eq_cmp_4 (.in_1(or_12_out), .in_2(4'b0000), .out_3(four_bit_eq_cmp_4_out_3));
  assign bit_extender_6_out = {{15{four_bit_eq_cmp_4_out_3}}, four_bit_eq_cmp_4_out_3};  // Bit_Extender bit_extender_6
  assign bit_extender_7_out = {{15{four_bit_eq_cmp_5_out_3}}, four_bit_eq_cmp_5_out_3};  // Bit_Extender bit_extender_7
  four_bit_eq_cmp four_bit_eq_cmp_5 (.in_1(or_13_out), .in_2(4'b0001), .out_3(four_bit_eq_cmp_5_out_3));
  four_bit_eq_cmp four_bit_eq_cmp_6 (.in_1(or_12_out), .in_2(4'b0001), .out_3(four_bit_eq_cmp_6_out_3));
  assign bit_extender_8_out = {{15{four_bit_eq_cmp_6_out_3}}, four_bit_eq_cmp_6_out_3};  // Bit_Extender bit_extender_8
  assign bit_extender_9_out = {{15{four_bit_eq_cmp_7_out_3}}, four_bit_eq_cmp_7_out_3};  // Bit_Extender bit_extender_9
  four_bit_eq_cmp four_bit_eq_cmp_7 (.in_1(or_13_out), .in_2(4'b0010), .out_3(four_bit_eq_cmp_7_out_3));
  four_bit_eq_cmp four_bit_eq_cmp_8 (.in_1(or_12_out), .in_2(4'b0010), .out_3(four_bit_eq_cmp_8_out_3));
  assign bit_extender_10_out = {{15{four_bit_eq_cmp_8_out_3}}, four_bit_eq_cmp_8_out_3};  // Bit_Extender bit_extender_10
  assign bit_extender_11_out = {{15{four_bit_eq_cmp_9_out_3}}, four_bit_eq_cmp_9_out_3};  // Bit_Extender bit_extender_11
  four_bit_eq_cmp four_bit_eq_cmp_9 (.in_1(or_13_out), .in_2(4'b0011), .out_3(four_bit_eq_cmp_9_out_3));
  four_bit_eq_cmp four_bit_eq_cmp_10 (.in_1(or_12_out), .in_2(4'b0011), .out_3(four_bit_eq_cmp_10_out_3));
  assign bit_extender_12_out = {{15{four_bit_eq_cmp_10_out_3}}, four_bit_eq_cmp_10_out_3};  // Bit_Extender bit_extender_12
  assign bit_extender_13_out = {{15{four_bit_eq_cmp_11_out_3}}, four_bit_eq_cmp_11_out_3};  // Bit_Extender bit_extender_13
  four_bit_eq_cmp four_bit_eq_cmp_11 (.in_1(or_13_out), .in_2(4'b0100), .out_3(four_bit_eq_cmp_11_out_3));
  four_bit_eq_cmp four_bit_eq_cmp_12 (.in_1(or_12_out), .in_2(4'b0100), .out_3(four_bit_eq_cmp_12_out_3));
  assign bit_extender_14_out = {{15{four_bit_eq_cmp_12_out_3}}, four_bit_eq_cmp_12_out_3};  // Bit_Extender bit_extender_14
  assign bit_extender_15_out = {{15{four_bit_eq_cmp_13_out_3}}, four_bit_eq_cmp_13_out_3};  // Bit_Extender bit_extender_15
  four_bit_eq_cmp four_bit_eq_cmp_13 (.in_1(or_13_out), .in_2(4'b0101), .out_3(four_bit_eq_cmp_13_out_3));
  four_bit_eq_cmp four_bit_eq_cmp_14 (.in_1(or_12_out), .in_2(4'b0101), .out_3(four_bit_eq_cmp_14_out_3));
  assign bit_extender_16_out = {{15{four_bit_eq_cmp_14_out_3}}, four_bit_eq_cmp_14_out_3};  // Bit_Extender bit_extender_16
  assign bit_extender_17_out = {{15{four_bit_eq_cmp_15_out_3}}, four_bit_eq_cmp_15_out_3};  // Bit_Extender bit_extender_17
  four_bit_eq_cmp four_bit_eq_cmp_15 (.in_1(or_13_out), .in_2(4'b0110), .out_3(four_bit_eq_cmp_15_out_3));
  four_bit_eq_cmp four_bit_eq_cmp_16 (.in_1(or_12_out), .in_2(4'b0110), .out_3(four_bit_eq_cmp_16_out_3));
  assign bit_extender_18_out = {{15{four_bit_eq_cmp_16_out_3}}, four_bit_eq_cmp_16_out_3};  // Bit_Extender bit_extender_18
  assign bit_extender_19_out = {{15{four_bit_eq_cmp_17_out_3}}, four_bit_eq_cmp_17_out_3};  // Bit_Extender bit_extender_19
  four_bit_eq_cmp four_bit_eq_cmp_17 (.in_1(or_13_out), .in_2(4'b0111), .out_3(four_bit_eq_cmp_17_out_3));
  four_bit_eq_cmp four_bit_eq_cmp_18 (.in_1(or_12_out), .in_2(4'b0111), .out_3(four_bit_eq_cmp_18_out_3));
  assign bit_extender_20_out = {{15{four_bit_eq_cmp_18_out_3}}, four_bit_eq_cmp_18_out_3};  // Bit_Extender bit_extender_20
  assign bit_extender_21_out = {{15{four_bit_eq_cmp_19_out_3}}, four_bit_eq_cmp_19_out_3};  // Bit_Extender bit_extender_21
  four_bit_eq_cmp four_bit_eq_cmp_19 (.in_1(or_13_out), .in_2(4'b1000), .out_3(four_bit_eq_cmp_19_out_3));
  four_bit_eq_cmp four_bit_eq_cmp_20 (.in_1(or_12_out), .in_2(4'b1000), .out_3(four_bit_eq_cmp_20_out_3));
  assign bit_extender_22_out = {{15{four_bit_eq_cmp_20_out_3}}, four_bit_eq_cmp_20_out_3};  // Bit_Extender bit_extender_22
  assign bit_extender_23_out = {{15{four_bit_eq_cmp_21_out_3}}, four_bit_eq_cmp_21_out_3};  // Bit_Extender bit_extender_23
  four_bit_eq_cmp four_bit_eq_cmp_21 (.in_1(or_13_out), .in_2(4'b1001), .out_3(four_bit_eq_cmp_21_out_3));
  four_bit_eq_cmp four_bit_eq_cmp_22 (.in_1(or_12_out), .in_2(4'b1001), .out_3(four_bit_eq_cmp_22_out_3));
  assign bit_extender_24_out = {{15{four_bit_eq_cmp_22_out_3}}, four_bit_eq_cmp_22_out_3};  // Bit_Extender bit_extender_24
  assign bit_extender_25_out = {{15{four_bit_eq_cmp_23_out_3}}, four_bit_eq_cmp_23_out_3};  // Bit_Extender bit_extender_25
  four_bit_eq_cmp four_bit_eq_cmp_23 (.in_1(or_13_out), .in_2(4'b1010), .out_3(four_bit_eq_cmp_23_out_3));
  four_bit_eq_cmp four_bit_eq_cmp_24 (.in_1(or_12_out), .in_2(4'b1010), .out_3(four_bit_eq_cmp_24_out_3));
  assign bit_extender_26_out = {{15{four_bit_eq_cmp_24_out_3}}, four_bit_eq_cmp_24_out_3};  // Bit_Extender bit_extender_26
  assign bit_extender_27_out = {{15{four_bit_eq_cmp_25_out_3}}, four_bit_eq_cmp_25_out_3};  // Bit_Extender bit_extender_27
  four_bit_eq_cmp four_bit_eq_cmp_25 (.in_1(or_13_out), .in_2(4'b1011), .out_3(four_bit_eq_cmp_25_out_3));
  four_bit_eq_cmp four_bit_eq_cmp_26 (.in_1(or_12_out), .in_2(4'b1011), .out_3(four_bit_eq_cmp_26_out_3));
  assign bit_extender_28_out = {{15{four_bit_eq_cmp_26_out_3}}, four_bit_eq_cmp_26_out_3};  // Bit_Extender bit_extender_28
  assign bit_extender_29_out = {{15{four_bit_eq_cmp_27_out_3}}, four_bit_eq_cmp_27_out_3};  // Bit_Extender bit_extender_29
  four_bit_eq_cmp four_bit_eq_cmp_27 (.in_1(or_13_out), .in_2(4'b1100), .out_3(four_bit_eq_cmp_27_out_3));
  four_bit_eq_cmp four_bit_eq_cmp_28 (.in_1(or_12_out), .in_2(4'b1100), .out_3(four_bit_eq_cmp_28_out_3));
  assign bit_extender_30_out = {{15{four_bit_eq_cmp_28_out_3}}, four_bit_eq_cmp_28_out_3};  // Bit_Extender bit_extender_30
  assign bit_extender_31_out = {{15{four_bit_eq_cmp_29_out_3}}, four_bit_eq_cmp_29_out_3};  // Bit_Extender bit_extender_31
  four_bit_eq_cmp four_bit_eq_cmp_29 (.in_1(or_13_out), .in_2(4'b1101), .out_3(four_bit_eq_cmp_29_out_3));
  four_bit_eq_cmp four_bit_eq_cmp_30 (.in_1(or_12_out), .in_2(4'b1101), .out_3(four_bit_eq_cmp_30_out_3));
  assign bit_extender_32_out = {{15{four_bit_eq_cmp_30_out_3}}, four_bit_eq_cmp_30_out_3};  // Bit_Extender bit_extender_32
  assign bit_extender_33_out = {{15{four_bit_eq_cmp_31_out_3}}, four_bit_eq_cmp_31_out_3};  // Bit_Extender bit_extender_33
  four_bit_eq_cmp four_bit_eq_cmp_31 (.in_1(or_13_out), .in_2(4'b1110), .out_3(four_bit_eq_cmp_31_out_3));
  four_bit_eq_cmp four_bit_eq_cmp_32 (.in_1(or_12_out), .in_2(4'b1110), .out_3(four_bit_eq_cmp_32_out_3));
  assign bit_extender_34_out = {{15{four_bit_eq_cmp_32_out_3}}, four_bit_eq_cmp_32_out_3};  // Bit_Extender bit_extender_34
  assign bit_extender_35_out = {{15{four_bit_eq_cmp_33_out_3}}, four_bit_eq_cmp_33_out_3};  // Bit_Extender bit_extender_35
  four_bit_eq_cmp four_bit_eq_cmp_33 (.in_1(or_13_out), .in_2(4'b1111), .out_3(four_bit_eq_cmp_33_out_3));
  four_bit_eq_cmp four_bit_eq_cmp_34 (.in_1(or_12_out), .in_2(4'b1111), .out_3(four_bit_eq_cmp_34_out_3));
  assign bit_extender_36_out = {{15{four_bit_eq_cmp_34_out_3}}, four_bit_eq_cmp_34_out_3};  // Bit_Extender bit_extender_36
  and and_5 (and_5_out, or_11_out, four_bit_eq_cmp_3_out_3);
  and and_6 (and_6_out, or_11_out, four_bit_eq_cmp_5_out_3);
  and and_7 (and_7_out, or_11_out, four_bit_eq_cmp_7_out_3);
  and and_8 (and_8_out, or_11_out, four_bit_eq_cmp_9_out_3);
  and and_9 (and_9_out, or_11_out, four_bit_eq_cmp_11_out_3);
  and and_10 (and_10_out, or_11_out, four_bit_eq_cmp_13_out_3);
  and and_11 (and_11_out, or_11_out, four_bit_eq_cmp_15_out_3);
  and and_12 (and_12_out, or_11_out, four_bit_eq_cmp_17_out_3);
  and and_13 (and_13_out, or_11_out, four_bit_eq_cmp_19_out_3);
  and and_14 (and_14_out, or_11_out, four_bit_eq_cmp_21_out_3);
  and and_15 (and_15_out, or_11_out, four_bit_eq_cmp_23_out_3);
  and and_16 (and_16_out, or_11_out, four_bit_eq_cmp_25_out_3);
  and and_17 (and_17_out, or_11_out, four_bit_eq_cmp_27_out_3);
  and and_18 (and_18_out, or_11_out, four_bit_eq_cmp_29_out_3);
  and and_19 (and_19_out, or_11_out, four_bit_eq_cmp_31_out_3);
  and and_20 (and_20_out, or_11_out, four_bit_eq_cmp_33_out_3);
  Register #(.width(16)) register_2 (.D(register_1_q), .en(and_5_out), .clk(clock), .Q(register_2_q), .clr(reset));
  Register #(.width(16)) register_3 (.D(register_1_q), .en(and_6_out), .clk(clock), .Q(register_3_q), .clr(reset));
  Register #(.width(16)) register_4 (.D(register_1_q), .en(and_7_out), .clk(clock), .Q(register_4_q), .clr(reset));
  Register #(.width(16)) register_5 (.D(register_1_q), .en(and_8_out), .clk(clock), .Q(register_5_q), .clr(reset));
  Register #(.width(16)) register_6 (.D(register_1_q), .en(and_9_out), .clk(clock), .Q(register_6_q), .clr(reset));
  Register #(.width(16)) register_7 (.D(register_1_q), .en(and_10_out), .clk(clock), .Q(register_7_q), .clr(reset));
  Register #(.width(16)) register_8 (.D(register_1_q), .en(and_11_out), .clk(clock), .Q(register_8_q), .clr(reset));
  Register #(.width(16)) register_9 (.D(register_1_q), .en(and_12_out), .clk(clock), .Q(register_9_q), .clr(reset));
  Register #(.width(16)) register_10 (.D(register_1_q), .en(and_13_out), .clk(clock), .Q(register_10_q), .clr(reset));
  Register #(.width(16)) register_11 (.D(register_1_q), .en(and_14_out), .clk(clock), .Q(register_11_q), .clr(reset));
  Register #(.width(16)) register_12 (.D(register_1_q), .en(and_15_out), .clk(clock), .Q(register_12_q), .clr(reset));
  Register #(.width(16)) register_13 (.D(register_1_q), .en(and_16_out), .clk(clock), .Q(register_13_q), .clr(reset));
  Register #(.width(16)) register_14 (.D(register_1_q), .en(and_17_out), .clk(clock), .Q(register_14_q), .clr(reset));
  Register #(.width(16)) register_15 (.D(register_1_q), .en(and_18_out), .clk(clock), .Q(register_15_q), .clr(reset));
  Register #(.width(16)) register_16 (.D(register_1_q), .en(and_19_out), .clk(clock), .Q(register_16_q), .clr(reset));
  Register #(.width(16)) register_17 (.D(register_1_q), .en(and_20_out), .clk(clock), .Q(register_17_q), .clr(reset));
  and and_21 (and_21_out, control_bus_1[12], eight_bit_eq_cmp_6_out_3);
  or or_14 (or_14_out, and_24_out, and_22_out);
  and and_22 (and_22_out, ~control_bus_1[12], eight_bit_eq_cmp_6_out_3);  // AND_Gate
  or or_15 (or_15_out, and_21_out, and_23_out);
  and and_23 (and_23_out, control_bus_2[12], eight_bit_eq_cmp_12_out_3);
  and and_24 (and_24_out, ~control_bus_2[12], eight_bit_eq_cmp_12_out_3);  // AND_Gate
  assign and_25_out = register_2_q & bit_extender_5_out;  // AND_Gate and_25, 16 bits wide
  assign or_16_out = and_25_out | and_25_out;  // OR_Gate or_16, 16 bits wide
  assign and_26_out = register_3_q & bit_extender_7_out;  // AND_Gate and_26, 16 bits wide
  assign or_17_out = and_26_out | or_16_out;  // OR_Gate or_17, 16 bits wide
  assign and_27_out = register_4_q & bit_extender_9_out;  // AND_Gate and_27, 16 bits wide
  assign or_18_out = and_27_out | or_17_out;  // OR_Gate or_18, 16 bits wide
  assign and_28_out = register_5_q & bit_extender_11_out;  // AND_Gate and_28, 16 bits wide
  assign or_19_out = and_28_out | or_18_out;  // OR_Gate or_19, 16 bits wide
  assign and_29_out = register_6_q & bit_extender_13_out;  // AND_Gate and_29, 16 bits wide
  assign or_20_out = and_29_out | or_19_out;  // OR_Gate or_20, 16 bits wide
  assign and_30_out = register_7_q & bit_extender_15_out;  // AND_Gate and_30, 16 bits wide
  assign or_21_out = and_30_out | or_20_out;  // OR_Gate or_21, 16 bits wide
  assign and_31_out = register_8_q & bit_extender_17_out;  // AND_Gate and_31, 16 bits wide
  assign or_22_out = and_31_out | or_21_out;  // OR_Gate or_22, 16 bits wide
  assign and_32_out = register_9_q & bit_extender_19_out;  // AND_Gate and_32, 16 bits wide
  assign or_23_out = and_32_out | or_22_out;  // OR_Gate or_23, 16 bits wide
  assign and_33_out = register_10_q & bit_extender_21_out;  // AND_Gate and_33, 16 bits wide
  assign or_24_out = and_33_out | or_23_out;  // OR_Gate or_24, 16 bits wide
  assign and_34_out = register_11_q & bit_extender_23_out;  // AND_Gate and_34, 16 bits wide
  assign or_25_out = and_34_out | or_24_out;  // OR_Gate or_25, 16 bits wide
  assign and_35_out = register_12_q & bit_extender_25_out;  // AND_Gate and_35, 16 bits wide
  assign or_26_out = and_35_out | or_25_out;  // OR_Gate or_26, 16 bits wide
  assign and_36_out = register_13_q & bit_extender_27_out;  // AND_Gate and_36, 16 bits wide
  assign or_27_out = and_36_out | or_26_out;  // OR_Gate or_27, 16 bits wide
  assign and_37_out = register_14_q & bit_extender_29_out;  // AND_Gate and_37, 16 bits wide
  assign or_28_out = and_37_out | or_27_out;  // OR_Gate or_28, 16 bits wide
  assign and_38_out = register_15_q & bit_extender_31_out;  // AND_Gate and_38, 16 bits wide
  assign or_29_out = and_38_out | or_28_out;  // OR_Gate or_29, 16 bits wide
  assign and_39_out = register_16_q & bit_extender_33_out;  // AND_Gate and_39, 16 bits wide
  assign or_30_out = and_39_out | or_29_out;  // OR_Gate or_30, 16 bits wide
  assign and_40_out = register_17_q & bit_extender_35_out;  // AND_Gate and_40, 16 bits wide
  assign or_31_out = and_40_out | or_30_out;  // OR_Gate or_31, 16 bits wide
  assign and_41_out = register_2_q & bit_extender_6_out;  // AND_Gate and_41, 16 bits wide
  assign or_32_out = and_41_out | and_41_out;  // OR_Gate or_32, 16 bits wide
  assign and_42_out = register_3_q & bit_extender_8_out;  // AND_Gate and_42, 16 bits wide
  assign or_33_out = and_42_out | or_32_out;  // OR_Gate or_33, 16 bits wide
  assign and_43_out = register_4_q & bit_extender_10_out;  // AND_Gate and_43, 16 bits wide
  assign or_34_out = and_43_out | or_33_out;  // OR_Gate or_34, 16 bits wide
  assign and_44_out = register_5_q & bit_extender_12_out;  // AND_Gate and_44, 16 bits wide
  assign or_35_out = and_44_out | or_34_out;  // OR_Gate or_35, 16 bits wide
  assign and_45_out = register_6_q & bit_extender_14_out;  // AND_Gate and_45, 16 bits wide
  assign or_36_out = and_45_out | or_35_out;  // OR_Gate or_36, 16 bits wide
  assign and_46_out = register_7_q & bit_extender_16_out;  // AND_Gate and_46, 16 bits wide
  assign or_37_out = and_46_out | or_36_out;  // OR_Gate or_37, 16 bits wide
  assign and_47_out = register_8_q & bit_extender_18_out;  // AND_Gate and_47, 16 bits wide
  assign or_38_out = and_47_out | or_37_out;  // OR_Gate or_38, 16 bits wide
  assign and_48_out = register_9_q & bit_extender_20_out;  // AND_Gate and_48, 16 bits wide
  assign or_39_out = and_48_out | or_38_out;  // OR_Gate or_39, 16 bits wide
  assign and_49_out = register_10_q & bit_extender_22_out;  // AND_Gate and_49, 16 bits wide
  assign or_40_out = and_49_out | or_39_out;  // OR_Gate or_40, 16 bits wide
  assign and_50_out = register_11_q & bit_extender_24_out;  // AND_Gate and_50, 16 bits wide
  assign or_41_out = and_50_out | or_40_out;  // OR_Gate or_41, 16 bits wide
  assign and_51_out = register_12_q & bit_extender_26_out;  // AND_Gate and_51, 16 bits wide
  assign or_42_out = and_51_out | or_41_out;  // OR_Gate or_42, 16 bits wide
  assign and_52_out = register_13_q & bit_extender_28_out;  // AND_Gate and_52, 16 bits wide
  assign or_43_out = and_52_out | or_42_out;  // OR_Gate or_43, 16 bits wide
  assign and_53_out = register_14_q & bit_extender_30_out;  // AND_Gate and_53, 16 bits wide
  assign or_44_out = and_53_out | or_43_out;  // OR_Gate or_44, 16 bits wide
  assign and_54_out = register_15_q & bit_extender_32_out;  // AND_Gate and_54, 16 bits wide
  assign or_45_out = and_54_out | or_44_out;  // OR_Gate or_45, 16 bits wide
  assign and_55_out = register_16_q & bit_extender_34_out;  // AND_Gate and_55, 16 bits wide
  assign or_46_out = and_55_out | or_45_out;  // OR_Gate or_46, 16 bits wide
  assign and_56_out = register_17_q & bit_extender_36_out;  // AND_Gate and_56, 16 bits wide
  assign or_47_out = and_56_out | or_46_out;  // OR_Gate or_47, 16 bits wide
  Multiplexer #(.width(16)) multiplexer_1 (.in0(or_31_out), .in1(register_1_q), .out(alu1_out), .sel(or_14_out));
  Multiplexer #(.width(16)) multiplexer_2 (.in0(or_47_out), .in1(register_1_q), .out(alu2_out), .sel(or_15_out));
  sixt_bit_gatekeeper sixt_bit_gatekeeper_1 (.in_1(or_9_out), .in_2(or_31_out), .out_3(data_bus_out));
  sixt_bit_gatekeeper sixt_bit_gatekeeper_2 (.in_1(or_10_out), .in_2(or_47_out), .out_3(addr_bus_out));
endmodule

module ALU (
  input  [15:0] control_bus,
  input  [15:0] argument1,
  input  [15:0] argument2,
  input  clock,
  input  reset,
  output [15:0] out_6,
  output out_7
);

  wire and_3_out, comparator_1_gt, comparator_1_lt, comparator_2_gt, comparator_2_lt,
       eight_bit_eq_cmp_1_out_3, eight_bit_eq_cmp_2_out_3, eight_bit_eq_cmp_3_out_3,
       eight_bit_eq_cmp_4_out_3, eight_bit_eq_cmp_5_out_3, eight_bit_eq_cmp_6_out_3,
       eight_bit_eq_cmp_7_out_3, eight_bit_eq_cmp_8_out_3, eight_bit_eq_cmp_9_out_3,
       eight_bit_eq_cmp_10_out_3, eight_bit_eq_cmp_11_out_3, eight_bit_eq_cmp_12_out_3,
       eight_bit_eq_cmp_13_out_3, eight_bit_eq_cmp_14_out_3, eight_bit_eq_cmp_15_out_3,
       eight_bit_eq_cmp_16_out_3, four_bit_eq_cmp_1_out_3, nor_1_out, or_1_out,
       sixt_bit_adder_subtractor_1_out_5, sixt_bit_comparator_1_out_3, sixt_bit_comparator_1_out_4;
  wire [15:0] and_2_out, multiplexer_1_out, not_1_out, not_2_out, not_3_out, or_2_out, or_3_out, or_4_out,
       or_5_out, or_6_out, or_7_out, or_8_out, or_9_out, or_10_out, or_11_out, or_12_out, or_13_out,
       or_14_out, or_15_out, or_16_out, or_17_out, or_18_out, or_19_out, register_1_q, register_2_q,
       shifter_1_out, shifter_2_out, shifter_3_out, sixt_bit_adder_subtractor_1_out_4,
       sixt_bit_decrementer_1_out_2, sixt_bit_gatekeeper_1_out_3, sixt_bit_gatekeeper_2_out_3,
       sixt_bit_gatekeeper_3_out_3, sixt_bit_gatekeeper_4_out_3, sixt_bit_gatekeeper_5_out_3,
       sixt_bit_gatekeeper_6_out_3, sixt_bit_gatekeeper_7_out_3, sixt_bit_gatekeeper_8_out_3,
       sixt_bit_gatekeeper_9_out_3, sixt_bit_gatekeeper_10_out_3, sixt_bit_gatekeeper_11_out_3,
       sixt_bit_gatekeeper_12_out_3, sixt_bit_gatekeeper_13_out_3, sixt_bit_gatekeeper_14_out_3,
       sixt_bit_gatekeeper_15_out_3, sixt_bit_gatekeeper_16_out_3, sixt_bit_gatekeeper_17_out_3,
       sixt_bit_gatekeeper_18_out_3, sixt_bit_gatekeeper_19_out_3, sixt_bit_gatekeeper_20_out_3,
       sixt_bit_gatekeeper_21_out_3, sixt_bit_incrementer_1_out_2, sixt_bit_incrementer_2_out_2,
       sixt_bit_incrementer_3_out_2, sixt_bit_multuiplier_1_out_3, xor_1_out;

  Register #(.trigger("falling"), .width(16)) register_1 (
    .D(argument1), .clk(clock), .Q(register_1_q), .clr(reset));  // open: en
  Register #(.trigger("falling"), .width(16)) register_2 (
    .D(argument2), .clk(clock), .Q(register_2_q), .clr(reset));  // open: en
  four_bit_eq_cmp four_bit_eq_cmp_1 (.in_1(control_bus[7:4]), .in_2(4'b0100), .out_3(four_bit_eq_cmp_1_out_3));
  eight_bit_eq_cmp eight_bit_eq_cmp_1 (
    .in_1({4'b0000, control_bus[3:0]}), .in_2({8{1'b0}}), .out_3(eight_bit_eq_cmp_1_out_3));
  eight_bit_eq_cmp eight_bit_eq_cmp_2 (
    .in_1({4'b0000, control_bus[3:0]}), .in_2(8'h1), .out_3(eight_bit_eq_cmp_2_out_3));
  eight_bit_eq_cmp eight_bit_eq_cmp_3 (
    .in_1({4'b0000, control_bus[3:0]}), .in_2(8'h2), .out_3(eight_bit_eq_cmp_3_out_3));
  eight_bit_eq_cmp eight_bit_eq_cmp_4 (
    .in_1({4'b0000, control_bus[3:0]}), .in_2(8'h3), .out_3(eight_bit_eq_cmp_4_out_3));
  eight_bit_eq_cmp eight_bit_eq_cmp_5 (
    .in_1({4'b0000, control_bus[3:0]}), .in_2(8'h4), .out_3(eight_bit_eq_cmp_5_out_3));
  eight_bit_eq_cmp eight_bit_eq_cmp_6 (
    .in_1({4'b0000, control_bus[3:0]}), .in_2(8'h5), .out_3(eight_bit_eq_cmp_6_out_3));
  eight_bit_eq_cmp eight_bit_eq_cmp_7 (
    .in_1({4'b0000, control_bus[3:0]}), .in_2(8'h6), .out_3(eight_bit_eq_cmp_7_out_3));
  eight_bit_eq_cmp eight_bit_eq_cmp_8 (
    .in_1({4'b0000, control_bus[3:0]}), .in_2(8'h7), .out_3(eight_bit_eq_cmp_8_out_3));
  eight_bit_eq_cmp eight_bit_eq_cmp_9 (
    .in_1({4'b0000, control_bus[3:0]}), .in_2(8'h8), .out_3(eight_bit_eq_cmp_9_out_3));
  eight_bit_eq_cmp eight_bit_eq_cmp_10 (
    .in_1({4'b0000, control_bus[3:0]}), .in_2(8'h9), .out_3(eight_bit_eq_cmp_10_out_3));
  eight_bit_eq_cmp eight_bit_eq_cmp_11 (
    .in_1({4'b0000, control_bus[3:0]}), .in_2(8'ha), .out_3(eight_bit_eq_cmp_11_out_3));
  eight_bit_eq_cmp eight_bit_eq_cmp_12 (
    .in_1({4'b0000, control_bus[3:0]}), .in_2(8'hb), .out_3(eight_bit_eq_cmp_12_out_3));
  eight_bit_eq_cmp eight_bit_eq_cmp_13 (
    .in_1({4'b0000, control_bus[3:0]}), .in_2(8'hc), .out_3(eight_bit_eq_cmp_13_out_3));
  eight_bit_eq_cmp eight_bit_eq_cmp_14 (
    .in_1({4'b0000, control_bus[3:0]}), .in_2(8'hd), .out_3(eight_bit_eq_cmp_14_out_3));
  eight_bit_eq_cmp eight_bit_eq_cmp_15 (
    .in_1({4'b0000, control_bus[3:0]}), .in_2(8'he), .out_3(eight_bit_eq_cmp_15_out_3));
  eight_bit_eq_cmp eight_bit_eq_cmp_16 (
    .in_1({4'b0000, control_bus[3:0]}), .in_2(8'hf), .out_3(eight_bit_eq_cmp_16_out_3));
  sixt_bit_adder_subtractor sixt_bit_adder_subtractor_1 (
    .in_3(eight_bit_eq_cmp_2_out_3), .in_1(register_1_q), .in_2(register_2_q),
    .out_5(sixt_bit_adder_subtractor_1_out_5), .out_4(sixt_bit_adder_subtractor_1_out_4));
  // Probe on register_1_q
  // Probe on register_2_q
  or or_1 (or_1_out, eight_bit_eq_cmp_2_out_3, eight_bit_eq_cmp_1_out_3);
  sixt_bit_gatekeeper sixt_bit_gatekeeper_1 (
    .in_1(or_1_out), .in_2(sixt_bit_adder_subtractor_1_out_4), .out_3(sixt_bit_gatekeeper_1_out_3));
  and and_1 (out_7, or_1_out, sixt_bit_adder_subtractor_1_out_5);
  sixt_bit_multuiplier sixt_bit_multuiplier_1 (
    .in_1(register_1_q), .in_2(register_2_q), .out_3(sixt_bit_multuiplier_1_out_3));
  sixt_bit_gatekeeper sixt_bit_gatekeeper_2 (
    .in_1(eight_bit_eq_cmp_3_out_3), .in_2(sixt_bit_multuiplier_1_out_3), .out_3(sixt_bit_gatekeeper_2_out_3));
  sixt_bit_incrementer sixt_bit_incrementer_1 (.in_1(register_1_q), .out_2(sixt_bit_incrementer_1_out_2));
  sixt_bit_gatekeeper sixt_bit_gatekeeper_3 (
    .in_1(eight_bit_eq_cmp_4_out_3), .in_2(sixt_bit_incrementer_1_out_2), .out_3(sixt_bit_gatekeeper_3_out_3));
  sixt_bit_decrementer sixt_bit_decrementer_1 (.in_1(register_1_q), .out_2(sixt_bit_decrementer_1_out_2));
  sixt_bit_gatekeeper sixt_bit_gatekeeper_4 (
    .in_1(eight_bit_eq_cmp_5_out_3), .in_2(sixt_bit_decrementer_1_out_2), .out_3(sixt_bit_gatekeeper_4_out_3));
  assign not_1_out = ~register_1_q;  // NOT_Gate not_1, 16 bits wide
  sixt_bit_incrementer sixt_bit_incrementer_2 (.in_1(not_1_out), .out_2(sixt_bit_incrementer_2_out_2));
  sixt_bit_gatekeeper sixt_bit_gatekeeper_5 (
    .in_1(eight_bit_eq_cmp_6_out_3), .in_2(sixt_bit_incrementer_2_out_2), .out_3(sixt_bit_gatekeeper_5_out_3));
  sixt_bit_comparator sixt_bit_comparator_1 (
    .in_1(register_1_q), .in_2(register_2_q), .out_3(sixt_bit_comparator_1_out_3),
    .out_4(sixt_bit_comparator_1_out_4));
  Comparator #(.width(16)) comparator_1 (
    .a(register_1_q), .b(register_2_q), .gt(comparator_1_gt), .lt(comparator_1_lt));  // open: eq
  Comparator #(.width(16)) comparator_2 (
    .a(register_1_q), .b({16{1'b0}}), .gt(comparator_2_gt), .lt(comparator_2_lt));  // open: eq
  assign and_2_out = register_1_q & register_2_q;  // AND_Gate and_2, 16 bits wide
  sixt_bit_gatekeeper sixt_bit_gatekeeper_6 (
    .in_1(eight_bit_eq_cmp_10_out_3), .in_2(and_2_out), .out_3(sixt_bit_gatekeeper_6_out_3));
  assign or_2_out = register_1_q | register_2_q;  // OR_Gate or_2, 16 bits wide
  sixt_bit_gatekeeper sixt_bit_gatekeeper_7 (
    .in_1(eight_bit_eq_cmp_11_out_3), .in_2(or_2_out), .out_3(sixt_bit_gatekeeper_7_out_3));
  assign xor_1_out = register_1_q ^ register_2_q;  // XOR_Gate xor_1, 16 bits wide
  sixt_bit_gatekeeper sixt_bit_gatekeeper_8 (
    .in_1(eight_bit_eq_cmp_12_out_3), .in_2(xor_1_out), .out_3(sixt_bit_gatekeeper_8_out_3));
  assign not_2_out = ~register_2_q;  // NOT_Gate not_2, 16 bits wide
  sixt_bit_gatekeeper sixt_bit_gatekeeper_9 (
    .in_1(eight_bit_eq_cmp_13_out_3), .in_2(not_2_out), .out_3(sixt_bit_gatekeeper_9_out_3));
  Shifter #(.width(16)) shifter_1 (.in(register_1_q), .\dist (4'b0001), .out(shifter_1_out));
  sixt_bit_gatekeeper sixt_bit_gatekeeper_10 (
    .in_1(eight_bit_eq_cmp_14_out_3), .in_2(shifter_1_out), .out_3(sixt_bit_gatekeeper_10_out_3));
  Shifter #(.shift("lr"), .width(16)) shifter_2 (.in(register_1_q), .\dist (4'b0001), .out(shifter_2_out));
  sixt_bit_gatekeeper sixt_bit_gatekeeper_11 (
    .in_1(eight_bit_eq_cmp_15_out_3), .in_2(shifter_2_out), .out_3(sixt_bit_gatekeeper_11_out_3));
  Multiplexer #(.width(16)) multiplexer_1 (
    .in0(register_2_q), .in1(sixt_bit_incrementer_3_out_2), .out(multiplexer_1_out), .sel(register_2_q[15]));
  assign not_3_out = ~register_2_q;  // NOT_Gate not_3, 16 bits wide
  sixt_bit_incrementer sixt_bit_incrementer_3 (.in_1(not_3_out), .out_2(sixt_bit_incrementer_3_out_2));
  assign or_3_out = sixt_bit_gatekeeper_1_out_3 | sixt_bit_gatekeeper_2_out_3;  // OR_Gate or_3, 16 bits wide
  sixt_bit_gatekeeper sixt_bit_gatekeeper_12 (
    .in_1(sixt_bit_comparator_1_out_3), .in_2(16'h1), .out_3(sixt_bit_gatekeeper_12_out_3));
  sixt_bit_gatekeeper sixt_bit_gatekeeper_13 (
    .in_1(sixt_bit_comparator_1_out_4), .in_2({16{1'b1}}), .out_3(sixt_bit_gatekeeper_13_out_3));
  sixt_bit_gatekeeper sixt_bit_gatekeeper_14 (
    .in_1(comparator_1_gt), .in_2(16'h1), .out_3(sixt_bit_gatekeeper_14_out_3));
  sixt_bit_gatekeeper sixt_bit_gatekeeper_15 (
    .in_1(comparator_1_lt), .in_2({16{1'b1}}), .out_3(sixt_bit_gatekeeper_15_out_3));
  sixt_bit_gatekeeper sixt_bit_gatekeeper_16 (
    .in_1(comparator_2_gt), .in_2(16'h1), .out_3(sixt_bit_gatekeeper_16_out_3));
  sixt_bit_gatekeeper sixt_bit_gatekeeper_17 (
    .in_1(comparator_2_lt), .in_2({16{1'b1}}), .out_3(sixt_bit_gatekeeper_17_out_3));
  nor nor_1 (nor_1_out, multiplexer_1_out[4], multiplexer_1_out[5], multiplexer_1_out[6], multiplexer_1_out[7], multiplexer_1_out[8], multiplexer_1_out[9], multiplexer_1_out[10], multiplexer_1_out[11], multiplexer_1_out[12], multiplexer_1_out[13], multiplexer_1_out[14]);
  assign or_4_out = or_3_out | sixt_bit_gatekeeper_3_out_3;  // OR_Gate or_4, 16 bits wide
  assign or_5_out = sixt_bit_gatekeeper_12_out_3 | sixt_bit_gatekeeper_13_out_3;  // OR_Gate or_5, 16 bits wide
  sixt_bit_gatekeeper sixt_bit_gatekeeper_18 (
    .in_1(eight_bit_eq_cmp_7_out_3), .in_2(or_5_out), .out_3(sixt_bit_gatekeeper_18_out_3));
  assign or_6_out = sixt_bit_gatekeeper_14_out_3 | sixt_bit_gatekeeper_15_out_3;  // OR_Gate or_6, 16 bits wide
  sixt_bit_gatekeeper sixt_bit_gatekeeper_19 (
    .in_1(eight_bit_eq_cmp_8_out_3), .in_2(or_6_out), .out_3(sixt_bit_gatekeeper_19_out_3));
  assign or_7_out = sixt_bit_gatekeeper_16_out_3 | sixt_bit_gatekeeper_17_out_3;  // OR_Gate or_7, 16 bits wide
  sixt_bit_gatekeeper sixt_bit_gatekeeper_20 (
    .in_1(eight_bit_eq_cmp_9_out_3), .in_2(or_7_out), .out_3(sixt_bit_gatekeeper_20_out_3));
  and and_3 (and_3_out, eight_bit_eq_cmp_16_out_3, nor_1_out);
  Shifter #(.width(16)) shifter_3 (.in(register_1_q), .\dist (multiplexer_1_out[3:0]), .out(shifter_3_out));
  assign or_8_out = or_4_out | sixt_bit_gatekeeper_4_out_3;  // OR_Gate or_8, 16 bits wide
  sixt_bit_gatekeeper sixt_bit_gatekeeper_21 (
    .in_1(and_3_out), .in_2(shifter_3_out), .out_3(sixt_bit_gatekeeper_21_out_3));
  assign or_9_out = or_8_out | sixt_bit_gatekeeper_5_out_3;  // OR_Gate or_9, 16 bits wide
  assign or_10_out = or_9_out | sixt_bit_gatekeeper_18_out_3;  // OR_Gate or_10, 16 bits wide
  assign or_11_out = or_10_out | sixt_bit_gatekeeper_19_out_3;  // OR_Gate or_11, 16 bits wide
  assign or_12_out = or_11_out | sixt_bit_gatekeeper_20_out_3;  // OR_Gate or_12, 16 bits wide
  assign or_13_out = or_12_out | sixt_bit_gatekeeper_6_out_3;  // OR_Gate or_13, 16 bits wide
  assign or_14_out = or_13_out | sixt_bit_gatekeeper_7_out_3;  // OR_Gate or_14, 16 bits wide
  assign or_15_out = or_14_out | sixt_bit_gatekeeper_8_out_3;  // OR_Gate or_15, 16 bits wide
  assign or_16_out = or_15_out | sixt_bit_gatekeeper_9_out_3;  // OR_Gate or_16, 16 bits wide
  assign or_17_out = or_16_out | sixt_bit_gatekeeper_10_out_3;  // OR_Gate or_17, 16 bits wide
  assign or_18_out = or_17_out | sixt_bit_gatekeeper_11_out_3;  // OR_Gate or_18, 16 bits wide
  assign or_19_out = or_18_out | sixt_bit_gatekeeper_21_out_3;  // OR_Gate or_19, 16 bits wide
  sixt_bit_gatekeeper sixt_bit_gatekeeper_22 (.in_1(four_bit_eq_cmp_1_out_3), .in_2(or_19_out), .out_3(out_6));

  // Notes on the sheet:
  //   Unsigned Cmp
  //   Signed Cmp
  //   Add
  //   Subtract
  //   Multiply
  //   Increment
  //   Decrement
  //   Negate
  //   cmp0
  //   AND
  //   OR
  //   XOR
  //   NOT
  //   <<
  //   >>
  //   Bit shift
endmodule

module mmio_registers (
  input  [15:0] data_in,
  input  [1:0] reg_select,
  input  write,
  input  clock,
  input  reset,
  output [15:0] out_6,
  output [15:0] out_7,
  output [15:0] out_8,
  output [15:0] out_9
);

  wire and_1_out, and_2_out, and_3_out, and_4_out, decoder_1_out0, decoder_1_out1, decoder_1_out2,
       decoder_1_out3;

  Decoder #(.enable("false"), .select(2)) decoder_1 (
    .out0(decoder_1_out0), .out1(decoder_1_out1), .out2(decoder_1_out2), .out3(decoder_1_out3),
    .sel(reg_select));
  Register #(.width(16)) register_1 (.D(data_in), .en(and_1_out), .clk(clock), .Q(out_6), .clr(reset));
  and and_1 (and_1_out, decoder_1_out0, write);
  Register #(.width(16)) register_2 (.D(data_in), .en(and_2_out), .clk(clock), .Q(out_7), .clr(reset));
  and and_2 (and_2_out, write, decoder_1_out1);
  Register #(.width(16)) register_3 (.D(data_in), .en(and_3_out), .clk(clock), .Q(out_8), .clr(reset));
  and and_3 (and_3_out, write, decoder_1_out2);
  Register #(.width(16)) register_4 (.D(data_in), .en(and_4_out), .clk(clock), .Q(out_9), .clr(reset));
  and and_4 (and_4_out, write, decoder_1_out3);
endmodule

module control_box (
  input  [15:0] program_kounter,
  input  [15:0] control_bus_1,
  input  pause,
  input  resume,
  input  [15:0] instr,
  input  [15:0] instr_breakpoint,
  input  [15:0] pk_breakpoint,
  input  clock_in,
  input  reset_in,
  output clock_out,
  output reset_out,
  output out_12
);

  wire and_1_out, and_2_out, and_3_out, and_4_out, and_5_out, buffer_1_out, buffer_2_out, buffer_3_out,
       buffer_4_out, buffer_5_out, buffer_6_out, buffer_7_out, buffer_8_out, buffer_9_out, buffer_10_out,
       buffer_11_out, buffer_12_out, buffer_13_out, buffer_14_out, buffer_16_out, buffer_17_out,
       buffer_18_out, buffer_19_out, buffer_20_out, buffer_21_out, buffer_22_out, buffer_23_out,
       buffer_24_out, buffer_26_out, buffer_27_out, or_1_out, or_2_out, or_3_out, pull_resistor_2_node,
       sixt_bit_eq_cmp_1_out_3, sixt_bit_eq_cmp_2_out_3, sixt_bit_eq_cmp_3_out_3, sixt_bit_eq_cmp_4_out_3;

  and and_1 (and_1_out, clock_in, ~reset_in);  // AND_Gate
  buf buffer_1 (buffer_1_out, 1'b1);
  buf buffer_2 (buffer_2_out, buffer_1_out);
  buf buffer_3 (buffer_3_out, buffer_2_out);
  buf buffer_4 (buffer_4_out, buffer_5_out);
  buf buffer_5 (buffer_5_out, buffer_6_out);
  buf buffer_6 (buffer_6_out, buffer_7_out);
  buf buffer_7 (buffer_7_out, buffer_13_out);
  buf buffer_8 (buffer_8_out, buffer_4_out);
  buf buffer_9 (buffer_9_out, buffer_8_out);
  buf buffer_10 (buffer_10_out, buffer_9_out);
  Pull_Resistor #(.pull(1)) pull_resistor_1 (.node(instr_breakpoint));
  Pull_Resistor pull_resistor_2 (.node(pull_resistor_2_node));
  buf buffer_11 (buffer_11_out, buffer_3_out);
  buf buffer_12 (buffer_12_out, buffer_11_out);
  buf buffer_13 (buffer_13_out, buffer_12_out);
  buf buffer_14 (buffer_14_out, buffer_10_out);
  buf buffer_15 (pull_resistor_2_node, buffer_14_out);
  sixt_bit_eq_cmp sixt_bit_eq_cmp_1 (.in_1(instr_breakpoint), .in_2(instr), .out_3(sixt_bit_eq_cmp_1_out_3));
  and and_2 (and_2_out, 1'b1, ~pull_resistor_2_node);  // AND_Gate
  sixt_bit_eq_cmp sixt_bit_eq_cmp_2 (.in_1(pk_breakpoint), .in_2({16{1'b1}}), .out_3(sixt_bit_eq_cmp_2_out_3));
  Pull_Resistor #(.pull(1)) pull_resistor_3 (.node(pk_breakpoint));
  or or_1 (or_1_out, reset_in, and_2_out);
  buf buffer_16 (buffer_16_out, or_1_out);
  buf buffer_17 (buffer_17_out, buffer_16_out);
  sixt_bit_eq_cmp sixt_bit_eq_cmp_3 (.in_1(program_kounter), .in_2(pk_breakpoint), .out_3(sixt_bit_eq_cmp_3_out_3));
  buf buffer_18 (buffer_18_out, buffer_17_out);
  buf buffer_19 (buffer_19_out, buffer_18_out);
  buf buffer_20 (buffer_20_out, buffer_19_out);
  buf buffer_21 (buffer_21_out, buffer_20_out);
  sixt_bit_eq_cmp sixt_bit_eq_cmp_4 (.in_1(16'h11), .in_2(control_bus_1), .out_3(sixt_bit_eq_cmp_4_out_3));
  Pull_Resistor pull_resistor_4 (.node(pause));
  and and_3 (and_3_out, ~sixt_bit_eq_cmp_2_out_3, and_4_out);  // AND_Gate
  and and_4 (and_4_out, sixt_bit_eq_cmp_3_out_3, sixt_bit_eq_cmp_4_out_3);
  buf buffer_22 (buffer_22_out, buffer_21_out);
  buf buffer_23 (buffer_23_out, buffer_22_out);
  buf buffer_24 (buffer_24_out, buffer_23_out);
  buf buffer_25 (reset_out, buffer_24_out);
  or or_2 (or_2_out, and_3_out, pause, sixt_bit_eq_cmp_1_out_3);
  buf buffer_26 (buffer_26_out, or_2_out);
  and and_5 (and_5_out, or_2_out, ~buffer_27_out);  // AND_Gate
  buf buffer_27 (buffer_27_out, buffer_26_out);
  S_R_Flip_Flop s_r_ff_1 (.Q(out_12), .reset(or_3_out), .preset(and_5_out));  // open: S, R, clk, Qn
  or or_3 (or_3_out, reset_out, resume);
  Pull_Resistor #(.pull(1)) pull_resistor_5 (.node(resume));
  Pull_Resistor pull_resistor_6 (.node(out_12));
  and and_6 (clock_out, ~out_12, and_1_out);  // AND_Gate
endmodule

module data_bus_controller (
  input  [15:0] control_bus_1,
  input  [15:0] control_bus_2,
  input  [15:0] addr_bus_in,
  input  clock,
  input  reset,
  input  [15:0] control_unit_in,
  input  [15:0] registers_in,
  input  [15:0] special_registers_in,
  input  [15:0] ALU_in,
  input  [15:0] memory_in,
  input  [15:0] io_in,
  output [15:0] data_bus_out
);

  wire nor_1_out, or_1_out, sixt_bit_eq_cmp_1_out_3, sixt_bit_eq_cmp_2_out_3, sixt_bit_eq_cmp_3_out_3,
       sixt_bit_eq_cmp_4_out_3;
  wire [15:0] multiplexer_1_out, or_2_out;

  sixt_bit_eq_cmp sixt_bit_eq_cmp_1 (.in_1(control_bus_1), .in_2(16'h50), .out_3(sixt_bit_eq_cmp_1_out_3));
  sixt_bit_eq_cmp sixt_bit_eq_cmp_2 (.in_1(control_bus_1), .in_2(16'h52), .out_3(sixt_bit_eq_cmp_2_out_3));
  sixt_bit_eq_cmp sixt_bit_eq_cmp_3 (.in_1(control_bus_2), .in_2(16'h50), .out_3(sixt_bit_eq_cmp_3_out_3));
  sixt_bit_eq_cmp sixt_bit_eq_cmp_4 (.in_1(control_bus_2), .in_2(16'h52), .out_3(sixt_bit_eq_cmp_4_out_3));
  nor nor_1 (nor_1_out, sixt_bit_eq_cmp_1_out_3, sixt_bit_eq_cmp_3_out_3);
  or or_1 (or_1_out, sixt_bit_eq_cmp_2_out_3, sixt_bit_eq_cmp_4_out_3);
  assign or_2_out = control_unit_in | registers_in | special_registers_in | ALU_in | memory_in | io_in;  // OR_Gate or_2, 16 bits wide
  Register #(.width(16)) register_1 (.D(multiplexer_1_out), .en(nor_1_out), .clk(clock), .Q(data_bus_out), .clr(reset));
  Multiplexer #(.width(16)) multiplexer_1 (.in0(or_2_out), .in1(addr_bus_in), .out(multiplexer_1_out), .sel(or_1_out));
endmodule

module memory_ctrl (
  input  [15:0] data_bus_in,
  input  [15:0] pk_in,
  input  [15:0] mem_in,
  input  [15:0] addr_in,
  input  [15:0] offset_in,
  input  clock,
  input  reset,
  input  [15:0] control_bus_1,
  input  [15:0] control_bus_2,
  output [15:0] data_to_mem,
  output [15:0] data_bus_out,
  output [15:0] mem_addr_out,
  output mem_write,
  output [1:0] reg_select,
  output reg_write
);

  wire and_1_out, comparator_2_lt, eight_bit_eq_cmp_1_out_3, eight_bit_eq_cmp_2_out_3,
       eight_bit_eq_cmp_3_out_3, eight_bit_eq_cmp_4_out_3, eight_bit_eq_cmp_5_out_3,
       eight_bit_eq_cmp_6_out_3, eight_bit_eq_cmp_7_out_3, eight_bit_eq_cmp_8_out_3,
       eight_bit_eq_cmp_9_out_3, eight_bit_eq_cmp_10_out_3, eight_bit_eq_cmp_11_out_3,
       eight_bit_eq_cmp_12_out_3, eight_bit_eq_cmp_13_out_3, eight_bit_eq_cmp_14_out_3,
       eight_bit_eq_cmp_15_out_3, eight_bit_eq_cmp_16_out_3, eight_bit_eq_cmp_17_out_3,
       eight_bit_eq_cmp_18_out_3, or_1_out, or_2_out, or_3_out, or_4_out, or_5_out, or_6_out, or_7_out,
       or_8_out, or_9_out, or_10_out, or_11_out, or_12_out, or_13_out, or_14_out, or_15_out, or_16_out,
       or_17_out, or_18_out, or_19_out, or_20_out, or_21_out, or_22_out, sixt_bit_eq_cmp_1_out_3,
       use_offset_out, write_out;
  wire [15:0] multiplexer_3_out, register_1_q, register_2_q, register_3_q, sixt_bit_adder_1_out_3;
  wire [15:2] multiplexer_1_out;

  Register #(.trigger("falling"), .width(16)) register_1 (
    .D(data_bus_in), .clk(clock), .Q(register_1_q), .clr(reset));  // open: en
  Register #(.width(16)) register_2 (.D(addr_in), .clk(or_14_out), .Q(register_2_q), .clr(reset));  // open: en
  sixt_bit_eq_cmp sixt_bit_eq_cmp_1 (.in_1(control_bus_1), .in_2(16'h1), .out_3(sixt_bit_eq_cmp_1_out_3));
  or or_1 (or_1_out, eight_bit_eq_cmp_1_out_3, or_2_out);
  eight_bit_eq_cmp eight_bit_eq_cmp_1 (.in_1(control_bus_1[7:0]), .in_2(8'h4), .out_3(eight_bit_eq_cmp_1_out_3));
  or or_2 (or_2_out, eight_bit_eq_cmp_2_out_3, or_3_out);
  eight_bit_eq_cmp eight_bit_eq_cmp_2 (.in_1(control_bus_1[7:0]), .in_2(8'h5), .out_3(eight_bit_eq_cmp_2_out_3));
  or or_3 (or_3_out, eight_bit_eq_cmp_3_out_3, or_4_out);
  eight_bit_eq_cmp eight_bit_eq_cmp_3 (.in_1(control_bus_1[7:0]), .in_2(8'h11), .out_3(eight_bit_eq_cmp_3_out_3));
  or or_4 (or_4_out, eight_bit_eq_cmp_4_out_3, or_5_out);
  eight_bit_eq_cmp eight_bit_eq_cmp_4 (.in_1(control_bus_1[7:0]), .in_2(8'h22), .out_3(eight_bit_eq_cmp_4_out_3));
  or or_5 (or_5_out, eight_bit_eq_cmp_5_out_3, or_6_out);
  eight_bit_eq_cmp eight_bit_eq_cmp_5 (.in_1(control_bus_1[7:0]), .in_2(8'h23), .out_3(eight_bit_eq_cmp_5_out_3));
  eight_bit_eq_cmp eight_bit_eq_cmp_6 (.in_1(control_bus_1[7:0]), .in_2(8'h25), .out_3(eight_bit_eq_cmp_6_out_3));
  eight_bit_eq_cmp eight_bit_eq_cmp_7 (.in_1(control_bus_1[7:0]), .in_2(8'h26), .out_3(eight_bit_eq_cmp_7_out_3));
  or or_6 (or_6_out, eight_bit_eq_cmp_8_out_3, or_7_out);
  or or_7 (or_7_out, or_8_out, eight_bit_eq_cmp_9_out_3);
  eight_bit_eq_cmp eight_bit_eq_cmp_8 (.in_1(control_bus_1[7:0]), .in_2(8'h27), .out_3(eight_bit_eq_cmp_8_out_3));
  eight_bit_eq_cmp eight_bit_eq_cmp_9 (.in_1(control_bus_1[7:0]), .in_2(8'h28), .out_3(eight_bit_eq_cmp_9_out_3));
  or or_8 (or_8_out, eight_bit_eq_cmp_10_out_3, or_9_out);
  eight_bit_eq_cmp eight_bit_eq_cmp_10 (.in_1(control_bus_2[7:0]), .in_2(8'h4), .out_3(eight_bit_eq_cmp_10_out_3));
  or or_9 (or_9_out, eight_bit_eq_cmp_11_out_3, or_10_out);
  eight_bit_eq_cmp eight_bit_eq_cmp_11 (.in_1(control_bus_2[7:0]), .in_2(8'h5), .out_3(eight_bit_eq_cmp_11_out_3));
  or or_10 (or_10_out, eight_bit_eq_cmp_12_out_3, or_11_out);
  eight_bit_eq_cmp eight_bit_eq_cmp_12 (.in_1(control_bus_2[7:0]), .in_2(8'h11), .out_3(eight_bit_eq_cmp_12_out_3));
  or or_11 (or_11_out, eight_bit_eq_cmp_13_out_3, or_12_out);
  eight_bit_eq_cmp eight_bit_eq_cmp_13 (.in_1(control_bus_2[7:0]), .in_2(8'h22), .out_3(eight_bit_eq_cmp_13_out_3));
  or or_12 (or_12_out, eight_bit_eq_cmp_14_out_3, or_13_out);
  eight_bit_eq_cmp eight_bit_eq_cmp_14 (.in_1(control_bus_2[7:0]), .in_2(8'h23), .out_3(eight_bit_eq_cmp_14_out_3));
  eight_bit_eq_cmp eight_bit_eq_cmp_15 (.in_1(control_bus_2[7:0]), .in_2(8'h25), .out_3(eight_bit_eq_cmp_15_out_3));
  eight_bit_eq_cmp eight_bit_eq_cmp_16 (.in_1(control_bus_2[7:0]), .in_2(8'h26), .out_3(eight_bit_eq_cmp_16_out_3));
  or or_13 (or_13_out, eight_bit_eq_cmp_17_out_3, eight_bit_eq_cmp_18_out_3);
  eight_bit_eq_cmp eight_bit_eq_cmp_17 (.in_1(control_bus_2[7:0]), .in_2(8'h27), .out_3(eight_bit_eq_cmp_17_out_3));
  eight_bit_eq_cmp eight_bit_eq_cmp_18 (.in_1(control_bus_2[7:0]), .in_2(8'h28), .out_3(eight_bit_eq_cmp_18_out_3));
  Register #(.width(16)) register_3 (.D(data_bus_in), .clk(or_14_out), .Q(register_3_q), .clr(reset));  // open: en
  Multiplexer #(.width(16)) multiplexer_1 (
    .in0(addr_in), .in1(register_2_q), .out({multiplexer_1_out, reg_select}), .sel(or_14_out));
  or or_14 (or_14_out, write_out, or_18_out);
  or write (write_out, eight_bit_eq_cmp_6_out_3, eight_bit_eq_cmp_7_out_3);
  or or_15 (or_15_out, eight_bit_eq_cmp_11_out_3, or_16_out);
  or or_16 (or_16_out, eight_bit_eq_cmp_14_out_3, or_17_out);
  or or_17 (or_17_out, eight_bit_eq_cmp_16_out_3, eight_bit_eq_cmp_18_out_3);
  or or_18 (or_18_out, eight_bit_eq_cmp_15_out_3, eight_bit_eq_cmp_16_out_3);
  Multiplexer #(.width(16)) multiplexer_2 (.in0(register_1_q), .in1(register_3_q), .out(data_to_mem), .sel(or_14_out));
  Comparator #(.mode("unsigned"), .width(16)) comparator_1 (
    .a({multiplexer_1_out, reg_select}), .b({16{1'b0}}));  // open: gt, eq, lt
  or use_offset (use_offset_out, eight_bit_eq_cmp_2_out_3, or_19_out);
  or or_19 (or_19_out, eight_bit_eq_cmp_5_out_3, or_20_out);
  or or_20 (or_20_out, eight_bit_eq_cmp_7_out_3, or_21_out);
  or or_21 (or_21_out, eight_bit_eq_cmp_9_out_3, or_15_out);
  sixt_bit_adder sixt_bit_adder_1 (
    .in_1({multiplexer_1_out, reg_select}), .in_2(offset_in), .out_3(sixt_bit_adder_1_out_3));  // open: out_4
  Comparator #(.mode("unsigned"), .width(16)) comparator_2 (
    .a({multiplexer_1_out, reg_select}), .b(16'hfffb), .lt(comparator_2_lt));  // open: gt, eq
  Multiplexer #(.width(16)) multiplexer_3 (
    .in0({multiplexer_1_out, reg_select}), .in1(sixt_bit_adder_1_out_3), .out(multiplexer_3_out),
    .sel(use_offset_out));
  sixt_bit_gatekeeper sixt_bit_gatekeeper_1 (.in_1(or_22_out), .in_2(mem_in), .out_3(data_bus_out));
  or or_22 (or_22_out, and_1_out, sixt_bit_eq_cmp_1_out_3);
  and and_1 (and_1_out, comparator_2_lt, or_1_out);
  and and_2 (mem_write, comparator_2_lt, or_14_out);
  and and_3 (reg_write, ~comparator_2_lt, or_14_out);  // AND_Gate
  Multiplexer #(.width(16)) multiplexer_4 (
    .in0(multiplexer_3_out), .in1(pk_in), .out(mem_addr_out), .sel(sixt_bit_eq_cmp_1_out_3));
  // Probe on mem_addr_out
endmodule

module sixt_bit_adder (
  input  [15:0] in_1,
  input  [15:0] in_2,
  output [15:0] out_3,
  output out_4
);

  wire and_1_out, and_2_out, and_3_out, and_4_out, and_5_out, and_6_out, and_7_out, and_8_out, and_9_out,
       and_10_out, and_11_out, and_12_out, and_13_out, and_14_out, and_15_out, and_16_out, and_17_out,
       and_18_out, and_19_out, and_20_out, and_21_out, and_22_out, and_23_out, and_24_out, and_25_out,
       and_26_out, and_27_out, and_28_out, and_29_out, and_30_out, and_31_out, xor_2_out, xor_3_out,
       xor_4_out, xor_5_out, xor_6_out, xor_7_out, xor_8_out, xor_9_out, xor_10_out, xor_11_out, xor_12_out,
       xor_13_out, xor_14_out, xor_15_out, xor_16_out, xor_32_out, xor_33_out, xor_34_out, xor_35_out,
       xor_36_out, xor_37_out, xor_38_out, xor_39_out, xor_40_out, xor_41_out, xor_42_out, xor_43_out,
       xor_44_out, xor_45_out;

  xor xor_1 (out_3[0], in_1[0], in_2[0]);
  and and_1 (and_1_out, in_1[0], in_2[0]);
  xor xor_2 (xor_2_out, in_1[1], in_2[1]);
  and and_2 (and_2_out, in_1[1], in_2[1]);
  xor xor_3 (xor_3_out, in_1[2], in_2[2]);
  and and_3 (and_3_out, in_1[2], in_2[2]);
  xor xor_4 (xor_4_out, in_1[3], in_2[3]);
  and and_4 (and_4_out, in_1[3], in_2[3]);
  xor xor_5 (xor_5_out, in_1[4], in_2[4]);
  and and_5 (and_5_out, in_1[4], in_2[4]);
  xor xor_6 (xor_6_out, in_1[5], in_2[5]);
  and and_6 (and_6_out, in_1[5], in_2[5]);
  xor xor_7 (xor_7_out, in_1[6], in_2[6]);
  and and_7 (and_7_out, in_1[6], in_2[6]);
  xor xor_8 (xor_8_out, in_1[7], in_2[7]);
  and and_8 (and_8_out, in_1[7], in_2[7]);
  xor xor_9 (xor_9_out, in_1[8], in_2[8]);
  and and_9 (and_9_out, in_1[8], in_2[8]);
  xor xor_10 (xor_10_out, in_1[9], in_2[9]);
  and and_10 (and_10_out, in_1[9], in_2[9]);
  xor xor_11 (xor_11_out, in_1[10], in_2[10]);
  and and_11 (and_11_out, in_1[10], in_2[10]);
  xor xor_12 (xor_12_out, in_1[11], in_2[11]);
  and and_12 (and_12_out, in_1[11], in_2[11]);
  xor xor_13 (xor_13_out, in_1[12], in_2[12]);
  and and_13 (and_13_out, in_1[12], in_2[12]);
  xor xor_14 (xor_14_out, in_1[13], in_2[13]);
  and and_14 (and_14_out, in_1[13], in_2[13]);
  xor xor_15 (xor_15_out, in_1[14], in_2[14]);
  and and_15 (and_15_out, in_1[14], in_2[14]);
  xor xor_16 (xor_16_out, in_1[15], in_2[15]);
  and and_16 (and_16_out, in_1[15], in_2[15]);
  xor xor_17 (out_3[1], xor_2_out, and_1_out);
  and and_17 (and_17_out, xor_2_out, and_1_out);
  xor xor_18 (out_3[2], xor_3_out, xor_32_out);
  and and_18 (and_18_out, xor_3_out, xor_32_out);
  xor xor_19 (out_3[3], xor_4_out, xor_33_out);
  and and_19 (and_19_out, xor_4_out, xor_33_out);
  xor xor_20 (out_3[4], xor_5_out, xor_34_out);
  and and_20 (and_20_out, xor_5_out, xor_34_out);
  xor xor_21 (out_3[5], xor_6_out, xor_35_out);
  and and_21 (and_21_out, xor_6_out, xor_35_out);
  xor xor_22 (out_3[6], xor_7_out, xor_36_out);
  and and_22 (and_22_out, xor_7_out, xor_36_out);
  xor xor_23 (out_3[7], xor_8_out, xor_37_out);
  and and_23 (and_23_out, xor_8_out, xor_37_out);
  xor xor_24 (out_3[8], xor_9_out, xor_38_out);
  and and_24 (and_24_out, xor_9_out, xor_38_out);
  xor xor_25 (out_3[9], xor_10_out, xor_39_out);
  and and_25 (and_25_out, xor_10_out, xor_39_out);
  xor xor_26 (out_3[10], xor_11_out, xor_40_out);
  and and_26 (and_26_out, xor_11_out, xor_40_out);
  xor xor_27 (out_3[11], xor_12_out, xor_41_out);
  and and_27 (and_27_out, xor_12_out, xor_41_out);
  xor xor_28 (out_3[12], xor_13_out, xor_42_out);
  and and_28 (and_28_out, xor_13_out, xor_42_out);
  xor xor_29 (out_3[13], xor_14_out, xor_43_out);
  and and_29 (and_29_out, xor_14_out, xor_43_out);
  xor xor_30 (out_3[14], xor_15_out, xor_44_out);
  and and_30 (and_30_out, xor_15_out, xor_44_out);
  xor xor_31 (out_3[15], xor_16_out, xor_45_out);
  and and_31 (and_31_out, xor_16_out, xor_45_out);
  xor xor_32 (xor_32_out, and_2_out, and_17_out);
  xor xor_33 (xor_33_out, and_3_out, and_18_out);
  xor xor_34 (xor_34_out, and_4_out, and_19_out);
  xor xor_35 (xor_35_out, and_5_out, and_20_out);
  xor xor_36 (xor_36_out, and_6_out, and_21_out);
  xor xor_37 (xor_37_out, and_7_out, and_22_out);
  xor xor_38 (xor_38_out, and_8_out, and_23_out);
  xor xor_39 (xor_39_out, and_9_out, and_24_out);
  xor xor_40 (xor_40_out, and_10_out, and_25_out);
  xor xor_41 (xor_41_out, and_11_out, and_26_out);
  xor xor_42 (xor_42_out, and_12_out, and_27_out);
  xor xor_43 (xor_43_out, and_13_out, and_28_out);
  xor xor_44 (xor_44_out, and_14_out, and_29_out);
  xor xor_45 (xor_45_out, and_15_out, and_30_out);
  xor xor_46 (out_4, and_16_out, and_31_out);
endmodule
module sixt_bit_adder_subtractor (
  input  [15:0] in_1,
  input  [15:0] in_2,
  input  in_3,
  output [15:0] out_4,
  output out_5
);

  wire and_1_out, and_2_out, and_3_out, and_4_out, and_5_out, and_6_out, and_7_out, and_8_out, and_9_out,
       and_10_out, and_11_out, and_12_out, and_13_out, and_14_out, and_15_out, and_16_out, and_17_out,
       and_18_out, and_19_out, and_20_out, and_21_out, and_22_out, and_23_out, and_24_out, and_25_out,
       and_26_out, and_27_out, and_28_out, and_29_out, and_30_out, and_31_out, xor_2_out, xor_4_out,
       xor_6_out, xor_8_out, xor_10_out, xor_12_out, xor_14_out, xor_16_out, xor_18_out, xor_20_out,
       xor_22_out, xor_24_out, xor_26_out, xor_28_out, xor_30_out, xor_32_out, xor_33_out, xor_34_out,
       xor_35_out, xor_36_out, xor_37_out, xor_38_out, xor_39_out, xor_40_out, xor_41_out, xor_42_out,
       xor_43_out, xor_44_out, xor_45_out;
  wire [15:0] not_1_out, sixt_bit_incrementer_1_out_2, sixt_bit_selector_1_out_4;

  assign not_1_out = ~in_2;  // NOT_Gate not_1, 16 bits wide
  sixt_bit_selector sixt_bit_selector_1 (
    .in_3(sixt_bit_incrementer_1_out_2), .in_1(in_3), .in_2(in_2), .out_4(sixt_bit_selector_1_out_4));
  sixt_bit_incrementer sixt_bit_incrementer_1 (.in_1(not_1_out), .out_2(sixt_bit_incrementer_1_out_2));
  xor xor_1 (out_4[0], in_1[0], sixt_bit_selector_1_out_4[0]);
  and and_1 (and_1_out, in_1[0], sixt_bit_selector_1_out_4[0]);
  xor xor_2 (xor_2_out, in_1[1], sixt_bit_selector_1_out_4[1]);
  xor xor_3 (out_4[1], xor_2_out, and_1_out);
  and and_2 (and_2_out, in_1[1], sixt_bit_selector_1_out_4[1]);
  and and_3 (and_3_out, xor_2_out, and_1_out);
  xor xor_4 (xor_4_out, in_1[2], sixt_bit_selector_1_out_4[2]);
  xor xor_5 (out_4[2], xor_4_out, xor_32_out);
  and and_4 (and_4_out, in_1[2], sixt_bit_selector_1_out_4[2]);
  and and_5 (and_5_out, xor_4_out, xor_32_out);
  xor xor_6 (xor_6_out, in_1[3], sixt_bit_selector_1_out_4[3]);
  xor xor_7 (out_4[3], xor_6_out, xor_33_out);
  and and_6 (and_6_out, in_1[3], sixt_bit_selector_1_out_4[3]);
  and and_7 (and_7_out, xor_6_out, xor_33_out);
  xor xor_8 (xor_8_out, in_1[4], sixt_bit_selector_1_out_4[4]);
  xor xor_9 (out_4[4], xor_8_out, xor_34_out);
  and and_8 (and_8_out, in_1[4], sixt_bit_selector_1_out_4[4]);
  and and_9 (and_9_out, xor_8_out, xor_34_out);
  xor xor_10 (xor_10_out, in_1[5], sixt_bit_selector_1_out_4[5]);
  xor xor_11 (out_4[5], xor_10_out, xor_35_out);
  and and_10 (and_10_out, in_1[5], sixt_bit_selector_1_out_4[5]);
  and and_11 (and_11_out, xor_10_out, xor_35_out);
  xor xor_12 (xor_12_out, in_1[6], sixt_bit_selector_1_out_4[6]);
  xor xor_13 (out_4[6], xor_12_out, xor_36_out);
  and and_12 (and_12_out, in_1[6], sixt_bit_selector_1_out_4[6]);
  and and_13 (and_13_out, xor_12_out, xor_36_out);
  xor xor_14 (xor_14_out, in_1[7], sixt_bit_selector_1_out_4[7]);
  xor xor_15 (out_4[7], xor_14_out, xor_37_out);
  and and_14 (and_14_out, in_1[7], sixt_bit_selector_1_out_4[7]);
  and and_15 (and_15_out, xor_14_out, xor_37_out);
  xor xor_16 (xor_16_out, in_1[8], sixt_bit_selector_1_out_4[8]);
  xor xor_17 (out_4[8], xor_16_out, xor_38_out);
  and and_16 (and_16_out, in_1[8], sixt_bit_selector_1_out_4[8]);
  and and_17 (and_17_out, xor_16_out, xor_38_out);
  xor xor_18 (xor_18_out, in_1[9], sixt_bit_selector_1_out_4[9]);
  xor xor_19 (out_4[9], xor_18_out, xor_39_out);
  and and_18 (and_18_out, in_1[9], sixt_bit_selector_1_out_4[9]);
  and and_19 (and_19_out, xor_18_out, xor_39_out);
  xor xor_20 (xor_20_out, in_1[10], sixt_bit_selector_1_out_4[10]);
  xor xor_21 (out_4[10], xor_20_out, xor_40_out);
  and and_20 (and_20_out, in_1[10], sixt_bit_selector_1_out_4[10]);
  and and_21 (and_21_out, xor_20_out, xor_40_out);
  xor xor_22 (xor_22_out, in_1[11], sixt_bit_selector_1_out_4[11]);
  xor xor_23 (out_4[11], xor_22_out, xor_41_out);
  and and_22 (and_22_out, in_1[11], sixt_bit_selector_1_out_4[11]);
  and and_23 (and_23_out, xor_22_out, xor_41_out);
  xor xor_24 (xor_24_out, in_1[12], sixt_bit_selector_1_out_4[12]);
  xor xor_25 (out_4[12], xor_24_out, xor_42_out);
  and and_24 (and_24_out, in_1[12], sixt_bit_selector_1_out_4[12]);
  and and_25 (and_25_out, xor_24_out, xor_42_out);
  xor xor_26 (xor_26_out, in_1[13], sixt_bit_selector_1_out_4[13]);
  xor xor_27 (out_4[13], xor_26_out, xor_43_out);
  and and_26 (and_26_out, in_1[13], sixt_bit_selector_1_out_4[13]);
  and and_27 (and_27_out, xor_26_out, xor_43_out);
  xor xor_28 (xor_28_out, in_1[14], sixt_bit_selector_1_out_4[14]);
  xor xor_29 (out_4[14], xor_28_out, xor_44_out);
  and and_28 (and_28_out, in_1[14], sixt_bit_selector_1_out_4[14]);
  and and_29 (and_29_out, xor_28_out, xor_44_out);
  xor xor_30 (xor_30_out, in_1[15], sixt_bit_selector_1_out_4[15]);
  xor xor_31 (out_4[15], xor_30_out, xor_45_out);
  and and_30 (and_30_out, in_1[15], sixt_bit_selector_1_out_4[15]);
  and and_31 (and_31_out, xor_30_out, xor_45_out);
  xor xor_32 (xor_32_out, and_2_out, and_3_out);
  xor xor_33 (xor_33_out, and_4_out, and_5_out);
  xor xor_34 (xor_34_out, and_6_out, and_7_out);
  xor xor_35 (xor_35_out, and_8_out, and_9_out);
  xor xor_36 (xor_36_out, and_10_out, and_11_out);
  xor xor_37 (xor_37_out, and_12_out, and_13_out);
  xor xor_38 (xor_38_out, and_14_out, and_15_out);
  xor xor_39 (xor_39_out, and_16_out, and_17_out);
  xor xor_40 (xor_40_out, and_18_out, and_19_out);
  xor xor_41 (xor_41_out, and_20_out, and_21_out);
  xor xor_42 (xor_42_out, and_22_out, and_23_out);
  xor xor_43 (xor_43_out, and_24_out, and_25_out);
  xor xor_44 (xor_44_out, and_26_out, and_27_out);
  xor xor_45 (xor_45_out, and_28_out, and_29_out);
  xor xor_46 (out_5, and_30_out, and_31_out);
endmodule

module sixt_bit_incrementer (
  input  [15:0] in_1,
  output [15:0] out_2
);

  sixt_bit_adder sixt_bit_adder_1 (.in_1(16'h1), .in_2(in_1), .out_3(out_2));  // open: out_4
endmodule

module sixt_bit_decrementer (
  input  [15:0] in_1,
  output [15:0] out_2
);

  sixt_bit_adder sixt_bit_adder_1 (.in_1({16{1'b1}}), .in_2(in_1), .out_3(out_2));  // open: out_4
endmodule

module sixt_bit_selector (
  input  in_1,
  input  [15:0] in_2,
  input  [15:0] in_3,
  output [15:0] out_4
);

  wire [15:0] and_1_out, and_2_out;
  wire [15:15] not_1_out;

  not not_1 (not_1_out[15], in_1);
  assign and_1_out = {16{not_1_out[15]}} & in_2;  // AND_Gate and_1, 16 bits wide
  assign and_2_out = in_3 & {16{in_1}};  // AND_Gate and_2, 16 bits wide
  assign out_4 = and_1_out | and_2_out;  // OR_Gate or_1, 16 bits wide
endmodule

module sixt_bit_shift_by_one (
  input  [15:0] in_1,
  output [15:0] out_2
);


  assign out_2 = {in_1[14:0], 1'b0};
endmodule

module sixt_bit_gatekeeper (
  input  in_1,
  input  [15:0] in_2,
  output [15:0] out_3
);

  assign out_3 = {16{in_1}} & in_2;  // AND_Gate and_1, 16 bits wide
endmodule

module sixt_bit_gatekeeper_vert (
  input  in_1,
  input  [15:0] in_2,
  output [15:0] out_3
);

  assign out_3 = {16{in_1}} & in_2;  // AND_Gate and_1, 16 bits wide
endmodule

module sixt_bit_multuiplier (
  input  [15:0] in_1,
  input  [15:0] in_2,
  output [15:0] out_3
);

  wire [15:0] sixt_bit_adder_1_out_3, sixt_bit_adder_2_out_3, sixt_bit_adder_3_out_3, sixt_bit_adder_4_out_3,
       sixt_bit_adder_5_out_3, sixt_bit_adder_6_out_3, sixt_bit_adder_7_out_3, sixt_bit_adder_8_out_3,
       sixt_bit_adder_9_out_3, sixt_bit_adder_10_out_3, sixt_bit_adder_11_out_3, sixt_bit_adder_12_out_3,
       sixt_bit_adder_13_out_3, sixt_bit_adder_14_out_3, sixt_bit_gatekeeper_vert_1_out_3,
       sixt_bit_gatekeeper_vert_2_out_3, sixt_bit_gatekeeper_vert_3_out_3, sixt_bit_gatekeeper_vert_4_out_3,
       sixt_bit_gatekeeper_vert_5_out_3, sixt_bit_gatekeeper_vert_6_out_3, sixt_bit_gatekeeper_vert_7_out_3,
       sixt_bit_gatekeeper_vert_8_out_3, sixt_bit_gatekeeper_vert_9_out_3, sixt_bit_gatekeeper_vert_10_out_3,
       sixt_bit_gatekeeper_vert_11_out_3, sixt_bit_gatekeeper_vert_12_out_3,
       sixt_bit_gatekeeper_vert_13_out_3, sixt_bit_gatekeeper_vert_14_out_3,
       sixt_bit_gatekeeper_vert_15_out_3, sixt_bit_gatekeeper_vert_16_out_3, sixt_bit_shift_by_one_1_out_2,
       sixt_bit_shift_by_one_2_out_2, sixt_bit_shift_by_one_3_out_2, sixt_bit_shift_by_one_4_out_2,
       sixt_bit_shift_by_one_5_out_2, sixt_bit_shift_by_one_6_out_2, sixt_bit_shift_by_one_7_out_2,
       sixt_bit_shift_by_one_8_out_2, sixt_bit_shift_by_one_9_out_2, sixt_bit_shift_by_one_10_out_2,
       sixt_bit_shift_by_one_11_out_2, sixt_bit_shift_by_one_12_out_2, sixt_bit_shift_by_one_13_out_2,
       sixt_bit_shift_by_one_14_out_2, sixt_bit_shift_by_one_15_out_2;

  sixt_bit_gatekeeper_vert sixt_bit_gatekeeper_vert_1 (
    .in_1(in_1[0]), .in_2(in_2), .out_3(sixt_bit_gatekeeper_vert_1_out_3));
  sixt_bit_shift_by_one sixt_bit_shift_by_one_1 (.in_1(in_2), .out_2(sixt_bit_shift_by_one_1_out_2));
  sixt_bit_shift_by_one sixt_bit_shift_by_one_2 (
    .in_1(sixt_bit_shift_by_one_1_out_2), .out_2(sixt_bit_shift_by_one_2_out_2));
  sixt_bit_gatekeeper_vert sixt_bit_gatekeeper_vert_2 (
    .in_1(in_1[1]), .in_2(sixt_bit_shift_by_one_1_out_2), .out_3(sixt_bit_gatekeeper_vert_2_out_3));
  sixt_bit_gatekeeper_vert sixt_bit_gatekeeper_vert_3 (
    .in_1(in_1[2]), .in_2(sixt_bit_shift_by_one_2_out_2), .out_3(sixt_bit_gatekeeper_vert_3_out_3));
  sixt_bit_adder sixt_bit_adder_1 (
    .in_1(sixt_bit_gatekeeper_vert_2_out_3), .in_2(sixt_bit_gatekeeper_vert_1_out_3),
    .out_3(sixt_bit_adder_1_out_3));  // open: out_4
  sixt_bit_shift_by_one sixt_bit_shift_by_one_3 (
    .in_1(sixt_bit_shift_by_one_2_out_2), .out_2(sixt_bit_shift_by_one_3_out_2));
  sixt_bit_gatekeeper_vert sixt_bit_gatekeeper_vert_4 (
    .in_1(in_1[3]), .in_2(sixt_bit_shift_by_one_3_out_2), .out_3(sixt_bit_gatekeeper_vert_4_out_3));
  sixt_bit_adder sixt_bit_adder_2 (
    .in_1(sixt_bit_gatekeeper_vert_3_out_3), .in_2(sixt_bit_adder_1_out_3), .out_3(sixt_bit_adder_2_out_3));  // open: out_4
  sixt_bit_adder sixt_bit_adder_3 (
    .in_1(sixt_bit_gatekeeper_vert_4_out_3), .in_2(sixt_bit_adder_2_out_3), .out_3(sixt_bit_adder_3_out_3));  // open: out_4
  sixt_bit_shift_by_one sixt_bit_shift_by_one_4 (
    .in_1(sixt_bit_shift_by_one_3_out_2), .out_2(sixt_bit_shift_by_one_4_out_2));
  sixt_bit_shift_by_one sixt_bit_shift_by_one_5 (
    .in_1(sixt_bit_shift_by_one_4_out_2), .out_2(sixt_bit_shift_by_one_5_out_2));
  sixt_bit_gatekeeper_vert sixt_bit_gatekeeper_vert_5 (
    .in_1(in_1[4]), .in_2(sixt_bit_shift_by_one_4_out_2), .out_3(sixt_bit_gatekeeper_vert_5_out_3));
  sixt_bit_gatekeeper_vert sixt_bit_gatekeeper_vert_6 (
    .in_1(in_1[5]), .in_2(sixt_bit_shift_by_one_5_out_2), .out_3(sixt_bit_gatekeeper_vert_6_out_3));
  sixt_bit_adder sixt_bit_adder_4 (
    .in_1(sixt_bit_gatekeeper_vert_5_out_3), .in_2(sixt_bit_adder_3_out_3), .out_3(sixt_bit_adder_4_out_3));  // open: out_4
  sixt_bit_shift_by_one sixt_bit_shift_by_one_6 (
    .in_1(sixt_bit_shift_by_one_5_out_2), .out_2(sixt_bit_shift_by_one_6_out_2));
  sixt_bit_gatekeeper_vert sixt_bit_gatekeeper_vert_7 (
    .in_1(in_1[6]), .in_2(sixt_bit_shift_by_one_6_out_2), .out_3(sixt_bit_gatekeeper_vert_7_out_3));
  sixt_bit_gatekeeper_vert sixt_bit_gatekeeper_vert_8 (
    .in_1(in_1[7]), .in_2(sixt_bit_shift_by_one_7_out_2), .out_3(sixt_bit_gatekeeper_vert_8_out_3));
  sixt_bit_adder sixt_bit_adder_5 (
    .in_1(sixt_bit_gatekeeper_vert_6_out_3), .in_2(sixt_bit_adder_4_out_3), .out_3(sixt_bit_adder_5_out_3));  // open: out_4
  sixt_bit_adder sixt_bit_adder_6 (
    .in_1(sixt_bit_gatekeeper_vert_7_out_3), .in_2(sixt_bit_adder_5_out_3), .out_3(sixt_bit_adder_6_out_3));  // open: out_4
  sixt_bit_shift_by_one sixt_bit_shift_by_one_7 (
    .in_1(sixt_bit_shift_by_one_6_out_2), .out_2(sixt_bit_shift_by_one_7_out_2));
  sixt_bit_shift_by_one sixt_bit_shift_by_one_8 (
    .in_1(sixt_bit_shift_by_one_7_out_2), .out_2(sixt_bit_shift_by_one_8_out_2));
  sixt_bit_gatekeeper_vert sixt_bit_gatekeeper_vert_9 (
    .in_1(in_1[8]), .in_2(sixt_bit_shift_by_one_8_out_2), .out_3(sixt_bit_gatekeeper_vert_9_out_3));
  sixt_bit_adder sixt_bit_adder_7 (
    .in_1(sixt_bit_gatekeeper_vert_8_out_3), .in_2(sixt_bit_adder_6_out_3), .out_3(sixt_bit_adder_7_out_3));  // open: out_4
  sixt_bit_adder sixt_bit_adder_8 (
    .in_1(sixt_bit_gatekeeper_vert_9_out_3), .in_2(sixt_bit_adder_7_out_3), .out_3(sixt_bit_adder_8_out_3));  // open: out_4
  sixt_bit_shift_by_one sixt_bit_shift_by_one_9 (
    .in_1(sixt_bit_shift_by_one_8_out_2), .out_2(sixt_bit_shift_by_one_9_out_2));
  sixt_bit_shift_by_one sixt_bit_shift_by_one_10 (
    .in_1(sixt_bit_shift_by_one_9_out_2), .out_2(sixt_bit_shift_by_one_10_out_2));
  sixt_bit_gatekeeper_vert sixt_bit_gatekeeper_vert_10 (
    .in_1(in_1[9]), .in_2(sixt_bit_shift_by_one_9_out_2), .out_3(sixt_bit_gatekeeper_vert_10_out_3));
  sixt_bit_gatekeeper_vert sixt_bit_gatekeeper_vert_11 (
    .in_1(in_1[10]), .in_2(sixt_bit_shift_by_one_10_out_2), .out_3(sixt_bit_gatekeeper_vert_11_out_3));
  sixt_bit_adder sixt_bit_adder_9 (
    .in_1(sixt_bit_gatekeeper_vert_10_out_3), .in_2(sixt_bit_adder_8_out_3), .out_3(sixt_bit_adder_9_out_3));  // open: out_4
  sixt_bit_shift_by_one sixt_bit_shift_by_one_11 (
    .in_1(sixt_bit_shift_by_one_10_out_2), .out_2(sixt_bit_shift_by_one_11_out_2));
  sixt_bit_gatekeeper_vert sixt_bit_gatekeeper_vert_12 (
    .in_1(in_1[11]), .in_2(sixt_bit_shift_by_one_11_out_2), .out_3(sixt_bit_gatekeeper_vert_12_out_3));
  sixt_bit_adder sixt_bit_adder_10 (
    .in_1(sixt_bit_gatekeeper_vert_11_out_3), .in_2(sixt_bit_adder_9_out_3), .out_3(sixt_bit_adder_10_out_3));  // open: out_4
  sixt_bit_adder sixt_bit_adder_11 (
    .in_1(sixt_bit_gatekeeper_vert_12_out_3), .in_2(sixt_bit_adder_10_out_3), .out_3(sixt_bit_adder_11_out_3));  // open: out_4
  sixt_bit_shift_by_one sixt_bit_shift_by_one_12 (
    .in_1(sixt_bit_shift_by_one_11_out_2), .out_2(sixt_bit_shift_by_one_12_out_2));
  sixt_bit_shift_by_one sixt_bit_shift_by_one_13 (
    .in_1(sixt_bit_shift_by_one_12_out_2), .out_2(sixt_bit_shift_by_one_13_out_2));
  sixt_bit_gatekeeper_vert sixt_bit_gatekeeper_vert_13 (
    .in_1(in_1[12]), .in_2(sixt_bit_shift_by_one_12_out_2), .out_3(sixt_bit_gatekeeper_vert_13_out_3));
  sixt_bit_gatekeeper_vert sixt_bit_gatekeeper_vert_14 (
    .in_1(in_1[13]), .in_2(sixt_bit_shift_by_one_13_out_2), .out_3(sixt_bit_gatekeeper_vert_14_out_3));
  sixt_bit_adder sixt_bit_adder_12 (
    .in_1(sixt_bit_gatekeeper_vert_13_out_3), .in_2(sixt_bit_adder_11_out_3), .out_3(sixt_bit_adder_12_out_3));  // open: out_4
  sixt_bit_shift_by_one sixt_bit_shift_by_one_14 (
    .in_1(sixt_bit_shift_by_one_13_out_2), .out_2(sixt_bit_shift_by_one_14_out_2));
  sixt_bit_gatekeeper_vert sixt_bit_gatekeeper_vert_15 (
    .in_1(in_1[14]), .in_2(sixt_bit_shift_by_one_14_out_2), .out_3(sixt_bit_gatekeeper_vert_15_out_3));
  sixt_bit_gatekeeper_vert sixt_bit_gatekeeper_vert_16 (
    .in_1(in_1[15]), .in_2(sixt_bit_shift_by_one_15_out_2), .out_3(sixt_bit_gatekeeper_vert_16_out_3));
  sixt_bit_adder sixt_bit_adder_13 (
    .in_1(sixt_bit_gatekeeper_vert_14_out_3), .in_2(sixt_bit_adder_12_out_3), .out_3(sixt_bit_adder_13_out_3));  // open: out_4
  sixt_bit_adder sixt_bit_adder_14 (
    .in_1(sixt_bit_gatekeeper_vert_15_out_3), .in_2(sixt_bit_adder_13_out_3), .out_3(sixt_bit_adder_14_out_3));  // open: out_4
  sixt_bit_shift_by_one sixt_bit_shift_by_one_15 (
    .in_1(sixt_bit_shift_by_one_14_out_2), .out_2(sixt_bit_shift_by_one_15_out_2));
  sixt_bit_adder sixt_bit_adder_15 (
    .in_1(sixt_bit_gatekeeper_vert_16_out_3), .in_2(sixt_bit_adder_14_out_3), .out_3(out_3));  // open: out_4
endmodule

module sixt_bit_eq_cmp (
  input  [15:0] in_1,
  input  [15:0] in_2,
  output out_3
);

  wire or_1_out;
  wire [15:0] xor_1_out;

  Pull_Resistor #(.pull(1)) pull_resistor_1 (.node(in_1));
  Pull_Resistor pull_resistor_2 (.node(in_2));
  xor xor_1 (xor_1_out[0], in_1[0], in_2[0]);
  xor xor_2 (xor_1_out[1], in_1[1], in_2[1]);
  xor xor_3 (xor_1_out[2], in_1[2], in_2[2]);
  xor xor_4 (xor_1_out[3], in_1[3], in_2[3]);
  xor xor_5 (xor_1_out[4], in_1[4], in_2[4]);
  xor xor_6 (xor_1_out[5], in_1[5], in_2[5]);
  xor xor_7 (xor_1_out[6], in_1[6], in_2[6]);
  xor xor_8 (xor_1_out[7], in_1[7], in_2[7]);
  xor xor_9 (xor_1_out[8], in_1[8], in_2[8]);
  xor xor_10 (xor_1_out[9], in_1[9], in_2[9]);
  xor xor_11 (xor_1_out[10], in_1[10], in_2[10]);
  xor xor_12 (xor_1_out[11], in_1[11], in_2[11]);
  xor xor_13 (xor_1_out[12], in_1[12], in_2[12]);
  xor xor_14 (xor_1_out[13], in_1[13], in_2[13]);
  xor xor_15 (xor_1_out[14], in_1[14], in_2[14]);
  xor xor_16 (xor_1_out[15], in_1[15], in_2[15]);
  or or_1 (or_1_out, xor_1_out[0], xor_1_out[1], xor_1_out[2], xor_1_out[3], xor_1_out[4], xor_1_out[5], xor_1_out[6], xor_1_out[7], xor_1_out[8], xor_1_out[9], xor_1_out[10], xor_1_out[11], xor_1_out[12], xor_1_out[13], xor_1_out[14], xor_1_out[15]);
  not not_1 (out_3, or_1_out);
endmodule

module eight_bit_eq_cmp (
  input  [7:0] in_1,
  input  [7:0] in_2,
  output out_3
);

  wire xor_1_out, xor_2_out, xor_3_out, xor_4_out, xor_5_out, xor_6_out, xor_7_out, xor_8_out;

  xor xor_1 (xor_1_out, in_1[0], in_2[0]);
  xor xor_2 (xor_2_out, in_1[1], in_2[1]);
  xor xor_3 (xor_3_out, in_1[2], in_2[2]);
  xor xor_4 (xor_4_out, in_1[3], in_2[3]);
  xor xor_5 (xor_5_out, in_1[4], in_2[4]);
  xor xor_6 (xor_6_out, in_1[5], in_2[5]);
  xor xor_7 (xor_7_out, in_1[6], in_2[6]);
  xor xor_8 (xor_8_out, in_1[7], in_2[7]);
  nor nor_1 (out_3, xor_1_out, xor_2_out, xor_3_out, xor_4_out, xor_5_out, xor_6_out, xor_7_out, xor_8_out);
endmodule

module four_bit_eq_cmp (
  input  [3:0] in_1,
  input  [3:0] in_2,
  output out_3
);

  wire xor_1_out, xor_2_out, xor_3_out, xor_4_out;

  xor xor_1 (xor_1_out, in_1[0], in_2[0]);
  xor xor_2 (xor_2_out, in_1[1], in_2[1]);
  xor xor_3 (xor_3_out, in_1[2], in_2[2]);
  xor xor_4 (xor_4_out, in_1[3], in_2[3]);
  nor nor_1 (out_3, xor_1_out, xor_2_out, xor_3_out, xor_4_out);
endmodule

module sixt_bit_comparator (
  input  [15:0] in_1,
  input  [15:0] in_2,
  output out_3,
  output out_4
);

  wire and_1_out, and_2_out, and_3_out, and_4_out, and_5_out, and_6_out, and_7_out, and_8_out, and_9_out,
       and_10_out, and_11_out, and_12_out, and_13_out, and_14_out, and_15_out, and_16_out, and_17_out,
       and_18_out, and_19_out, and_20_out, and_21_out, and_22_out, and_23_out, and_24_out, and_25_out,
       and_26_out, and_27_out, and_28_out, and_29_out, and_30_out, or_1_out, or_2_out, or_3_out, or_4_out,
       or_5_out, or_6_out, or_7_out, or_8_out, or_9_out, or_10_out, or_11_out, or_12_out, or_13_out,
       or_14_out, or_15_out, or_17_out, or_18_out, or_19_out, or_20_out, or_21_out, or_22_out, or_23_out,
       or_24_out, or_25_out, or_26_out, or_27_out, or_28_out, or_29_out, or_30_out, xor_1_out, xor_2_out,
       xor_3_out, xor_4_out, xor_5_out, xor_6_out, xor_7_out, xor_8_out, xor_9_out, xor_10_out, xor_11_out,
       xor_12_out, xor_13_out, xor_14_out, xor_15_out, xor_16_out;

  xor xor_1 (xor_1_out, in_1[0], in_2[0]);
  xor xor_2 (xor_2_out, in_1[1], in_2[1]);
  xor xor_3 (xor_3_out, in_1[2], in_2[2]);
  xor xor_4 (xor_4_out, in_1[3], in_2[3]);
  xor xor_5 (xor_5_out, in_1[4], in_2[4]);
  xor xor_6 (xor_6_out, in_1[5], in_2[5]);
  xor xor_7 (xor_7_out, in_1[6], in_2[6]);
  xor xor_8 (xor_8_out, in_1[7], in_2[7]);
  xor xor_9 (xor_9_out, in_1[8], in_2[8]);
  xor xor_10 (xor_10_out, in_1[9], in_2[9]);
  xor xor_11 (xor_11_out, in_1[10], in_2[10]);
  xor xor_12 (xor_12_out, in_1[11], in_2[11]);
  xor xor_13 (xor_13_out, in_1[12], in_2[12]);
  xor xor_14 (xor_14_out, in_1[13], in_2[13]);
  xor xor_15 (xor_15_out, in_1[14], in_2[14]);
  xor xor_16 (xor_16_out, in_1[15], in_2[15]);
  or or_1 (or_1_out, or_2_out, xor_1_out);
  and and_1 (and_1_out, xor_1_out, ~or_2_out);  // AND_Gate
  or or_2 (or_2_out, or_3_out, xor_2_out);
  and and_2 (and_2_out, xor_2_out, ~or_3_out);  // AND_Gate
  or or_3 (or_3_out, or_4_out, xor_3_out);
  and and_3 (and_3_out, xor_3_out, ~or_4_out);  // AND_Gate
  or or_4 (or_4_out, or_5_out, xor_4_out);
  and and_4 (and_4_out, xor_4_out, ~or_5_out);  // AND_Gate
  or or_5 (or_5_out, or_6_out, xor_5_out);
  and and_5 (and_5_out, xor_5_out, ~or_6_out);  // AND_Gate
  or or_6 (or_6_out, or_7_out, xor_6_out);
  and and_6 (and_6_out, xor_6_out, ~or_7_out);  // AND_Gate
  or or_7 (or_7_out, or_8_out, xor_7_out);
  and and_7 (and_7_out, xor_7_out, ~or_8_out);  // AND_Gate
  or or_8 (or_8_out, or_9_out, xor_8_out);
  and and_8 (and_8_out, xor_8_out, ~or_9_out);  // AND_Gate
  or or_9 (or_9_out, or_10_out, xor_9_out);
  and and_9 (and_9_out, xor_9_out, ~or_10_out);  // AND_Gate
  or or_10 (or_10_out, or_11_out, xor_10_out);
  and and_10 (and_10_out, xor_10_out, ~or_11_out);  // AND_Gate
  or or_11 (or_11_out, or_12_out, xor_11_out);
  and and_11 (and_11_out, xor_11_out, ~or_12_out);  // AND_Gate
  or or_12 (or_12_out, or_13_out, xor_12_out);
  and and_12 (and_12_out, xor_12_out, ~or_13_out);  // AND_Gate
  or or_13 (or_13_out, or_14_out, xor_13_out);
  and and_13 (and_13_out, xor_13_out, ~or_14_out);  // AND_Gate
  or or_14 (or_14_out, or_15_out, xor_14_out);
  and and_14 (and_14_out, xor_14_out, ~or_15_out);  // AND_Gate
  or or_15 (or_15_out, xor_16_out, xor_15_out);
  and and_15 (and_15_out, xor_15_out, ~xor_16_out);  // AND_Gate
  and and_16 (and_16_out, and_1_out, in_1[0]);
  or or_16 (out_3, and_16_out, or_17_out);
  and and_17 (and_17_out, and_2_out, in_1[1]);
  or or_17 (or_17_out, and_17_out, or_18_out);
  and and_18 (and_18_out, and_3_out, in_1[2]);
  or or_18 (or_18_out, and_18_out, or_19_out);
  and and_19 (and_19_out, and_4_out, in_1[3]);
  or or_19 (or_19_out, and_19_out, or_20_out);
  and and_20 (and_20_out, and_5_out, in_1[4]);
  or or_20 (or_20_out, and_20_out, or_21_out);
  and and_21 (and_21_out, and_6_out, in_1[5]);
  or or_21 (or_21_out, and_21_out, or_22_out);
  and and_22 (and_22_out, and_7_out, in_1[6]);
  or or_22 (or_22_out, and_22_out, or_23_out);
  and and_23 (and_23_out, and_8_out, in_1[7]);
  or or_23 (or_23_out, and_23_out, or_24_out);
  and and_24 (and_24_out, and_9_out, in_1[8]);
  or or_24 (or_24_out, and_24_out, or_25_out);
  and and_25 (and_25_out, and_10_out, in_1[9]);
  or or_25 (or_25_out, and_25_out, or_26_out);
  and and_26 (and_26_out, and_11_out, in_1[10]);
  or or_26 (or_26_out, and_26_out, or_27_out);
  and and_27 (and_27_out, and_12_out, in_1[11]);
  or or_27 (or_27_out, and_27_out, or_28_out);
  and and_28 (and_28_out, and_13_out, in_1[12]);
  or or_28 (or_28_out, and_28_out, or_29_out);
  and and_29 (and_29_out, and_14_out, in_1[13]);
  or or_29 (or_29_out, and_29_out, or_30_out);
  and and_30 (and_30_out, and_15_out, in_1[14]);
  or or_30 (or_30_out, and_30_out, xor_16_out);
  and and_31 (out_4, ~out_3, or_1_out);  // AND_Gate
endmodule

module sixt_bit_eq_zero (
  input  [15:0] in_1,
  output out_2
);

  wire [15:0] not_1_out;

  assign not_1_out = ~in_1;  // NOT_Gate not_1, 16 bits wide
  and and_1 (out_2, not_1_out[0], not_1_out[1], not_1_out[2], not_1_out[3], not_1_out[4], not_1_out[5], not_1_out[6], not_1_out[7], not_1_out[8], not_1_out[9], not_1_out[10], not_1_out[11], not_1_out[12], not_1_out[13], not_1_out[14], not_1_out[15]);
endmodule

module four_bit_eq_zero (
  input  [3:0] in_1,
  output out_2
);

  nor nor_1 (out_2, in_1[0], in_1[1], in_1[2], in_1[3]);
endmodule

module counting_register (
  input  [15:0] data_in,
  input  increment,
  input  decrement,
  input  write,
  input  clk,
  input  reset,
  output [15:0] out_7
);

  wire or_1_out;
  wire [15:0] multiplexer_1_out, sixt_bit_adder_subtractor_1_out_4;

  Multiplexer #(.width(16)) multiplexer_1 (
    .in0(sixt_bit_adder_subtractor_1_out_4), .in1(data_in), .out(multiplexer_1_out), .sel(write));
  Register #(.width(16)) register_1 (.D(multiplexer_1_out), .en(or_1_out), .clk(clk), .Q(out_7), .clr(reset));
  or or_1 (or_1_out, increment, decrement, write);
  sixt_bit_adder_subtractor sixt_bit_adder_subtractor_1 (
    .in_3(decrement), .in_1(out_7), .in_2(16'h1), .out_4(sixt_bit_adder_subtractor_1_out_4));  // open: out_5
endmodule

module pulse_extender (
  input  in_1,
  input  in_2,
  input  in_3,
  output out_4,
  output out_5,
  output out_6
);

  wire not_1_out;

  S_R_Flip_Flop s_r_ff_1 (.S(1'b0), .R(not_1_out), .clk(in_2), .Q(out_6), .reset(in_3), .preset(in_1));  // open: Qn
  not not_1 (not_1_out, in_1);

  assign out_4 = in_3;
  assign out_5 = in_2;
endmodule

module four_bit_g8 (
  input  in_1,
  input  [3:0] in_2,
  output [3:0] out_3
);

  assign out_3 = {4{in_1}} & in_2;  // AND_Gate and_1, 4 bits wide
endmodule

module two_ticker (
  input  signal_in,
  input  clock,
  input  reset,
  output out_4
);

  wire and_1_out, and_2_out, and_3_out, and_4_out, and_5_out, and_6_out, and_7_out, buffer_1_out,
       buffer_2_out, buffer_3_out, buffer_4_out, buffer_5_out, buffer_6_out, buffer_7_out, buffer_8_out,
       buffer_9_out, buffer_10_out, buffer_11_out, buffer_12_out, buffer_13_out, buffer_14_out,
       buffer_15_out, buffer_16_out, buffer_17_out, buffer_18_out, clk_at_signal_q, fall_next_q, not_1_out,
       or_1_out, or_2_out, or_3_out, xor_1_out;

  not not_1 (not_1_out, clock);
  buf buffer_1 (buffer_1_out, signal_in);
  buf buffer_2 (buffer_2_out, buffer_1_out);
  buf buffer_3 (buffer_3_out, clock);
  buf buffer_4 (buffer_4_out, buffer_3_out);
  buf buffer_5 (buffer_5_out, not_1_out);
  buf buffer_6 (buffer_6_out, buffer_5_out);
  buf buffer_7 (buffer_7_out, buffer_2_out);
  and and_1 (and_1_out, ~buffer_7_out, signal_in);  // AND_Gate
  buf buffer_8 (buffer_8_out, buffer_4_out);
  and and_2 (and_2_out, ~buffer_8_out, clock);  // AND_Gate
  buf buffer_9 (buffer_9_out, buffer_6_out);
  and and_3 (and_3_out, ~buffer_9_out, not_1_out);  // AND_Gate
  or or_1 (or_1_out, and_2_out, and_3_out);
  and and_4 (and_4_out, ~out_4, and_1_out);  // AND_Gate
  xor xor_1 (xor_1_out, clock, clk_at_signal_q);
  and and_5 (and_5_out, signal_in, and_4_out);
  or or_2 (or_2_out, and_5_out, and_6_out);
  and and_6 (and_6_out, fall_next_q, out_4, or_1_out);
  or or_3 (or_3_out, and_6_out, and_4_out);
  and and_7 (and_7_out, xor_1_out, out_4);
  D_Flip_Flop signal_out (.D(or_2_out), .clk(buffer_12_out), .Q(out_4), .reset(reset));  // open: Qn, preset
  buf buffer_10 (buffer_10_out, or_3_out);
  buf buffer_11 (buffer_11_out, buffer_10_out);
  buf buffer_12 (buffer_12_out, buffer_11_out);
  D_Flip_Flop clk_at_signal (.D(clock), .clk(buffer_15_out), .Q(clk_at_signal_q), .reset(reset));  // open: Qn, preset
  buf buffer_13 (buffer_13_out, and_4_out);
  buf buffer_14 (buffer_14_out, buffer_13_out);
  buf buffer_15 (buffer_15_out, buffer_14_out);
  D_Flip_Flop fall_next (.D(and_7_out), .clk(buffer_18_out), .Q(fall_next_q), .reset(reset));  // open: Qn, preset
  buf buffer_16 (buffer_16_out, or_1_out);
  buf buffer_17 (buffer_17_out, buffer_16_out);
  buf buffer_18 (buffer_18_out, buffer_17_out);
endmodule

module special_register_opdec (
  input  [15:0] control,
  input  [3:0] id,
  output data_bus_enable,
  output addr_bus_enable,
  output write_enable,
  output [15:0] special_functions
);

  wire and_2_out, and_3_out, and_4_out, eight_bit_eq_cmp_1_out_3, eight_bit_eq_cmp_2_out_3,
       eight_bit_eq_cmp_3_out_3, eight_bit_eq_cmp_4_out_3, eight_bit_eq_cmp_5_out_3,
       eight_bit_eq_cmp_6_out_3, eight_bit_eq_cmp_7_out_3, eight_bit_eq_cmp_8_out_3,
       eight_bit_eq_cmp_9_out_3, eight_bit_eq_cmp_10_out_3, eight_bit_eq_cmp_11_out_3,
       eight_bit_eq_cmp_12_out_3, eight_bit_eq_cmp_13_out_3, eight_bit_eq_cmp_14_out_3,
       eight_bit_eq_cmp_15_out_3, eight_bit_eq_cmp_16_out_3, four_bit_eq_cmp_1_out_3, load_data_bus_out_3,
       to_addr_bus_out_3, to_data_bus_indirect_out_3, to_data_bus_indirect_w_offset_out_3, to_data_bus_out_3;

  four_bit_eq_cmp four_bit_eq_cmp_1 (.in_1(control[15:12]), .in_2(id), .out_3(four_bit_eq_cmp_1_out_3));
  eight_bit_eq_cmp to_data_bus (.in_1(control[7:0]), .in_2(8'h2), .out_3(to_data_bus_out_3));
  eight_bit_eq_cmp to_addr_bus (.in_1(control[7:0]), .in_2(8'h3), .out_3(to_addr_bus_out_3));
  eight_bit_eq_cmp to_data_bus_indirect (.in_1(control[7:0]), .in_2(8'h4), .out_3(to_data_bus_indirect_out_3));
  eight_bit_eq_cmp to_data_bus_indirect_w_offset (
    .in_1(control[7:0]), .in_2(8'h5), .out_3(to_data_bus_indirect_w_offset_out_3));
  eight_bit_eq_cmp load_data_bus (.in_1(control[7:0]), .in_2(8'h6), .out_3(load_data_bus_out_3));
  eight_bit_eq_cmp eight_bit_eq_cmp_1 (.in_1(control[7:0]), .in_2(8'h10), .out_3(eight_bit_eq_cmp_1_out_3));
  eight_bit_eq_cmp eight_bit_eq_cmp_2 (.in_1(control[7:0]), .in_2(8'h11), .out_3(eight_bit_eq_cmp_2_out_3));
  eight_bit_eq_cmp eight_bit_eq_cmp_3 (.in_1(control[7:0]), .in_2(8'h12), .out_3(eight_bit_eq_cmp_3_out_3));
  eight_bit_eq_cmp eight_bit_eq_cmp_4 (.in_1(control[7:0]), .in_2(8'h13), .out_3(eight_bit_eq_cmp_4_out_3));
  eight_bit_eq_cmp eight_bit_eq_cmp_5 (.in_1(control[7:0]), .in_2(8'h14), .out_3(eight_bit_eq_cmp_5_out_3));
  eight_bit_eq_cmp eight_bit_eq_cmp_6 (.in_1(control[7:0]), .in_2(8'h15), .out_3(eight_bit_eq_cmp_6_out_3));
  eight_bit_eq_cmp eight_bit_eq_cmp_7 (.in_1(control[7:0]), .in_2(8'h16), .out_3(eight_bit_eq_cmp_7_out_3));
  eight_bit_eq_cmp eight_bit_eq_cmp_8 (.in_1(control[7:0]), .in_2(8'h17), .out_3(eight_bit_eq_cmp_8_out_3));
  eight_bit_eq_cmp eight_bit_eq_cmp_9 (.in_1(control[7:0]), .in_2(8'h18), .out_3(eight_bit_eq_cmp_9_out_3));
  eight_bit_eq_cmp eight_bit_eq_cmp_10 (.in_1(control[7:0]), .in_2(8'h19), .out_3(eight_bit_eq_cmp_10_out_3));
  eight_bit_eq_cmp eight_bit_eq_cmp_11 (.in_1(control[7:0]), .in_2(8'h1a), .out_3(eight_bit_eq_cmp_11_out_3));
  eight_bit_eq_cmp eight_bit_eq_cmp_12 (.in_1(control[7:0]), .in_2(8'h1b), .out_3(eight_bit_eq_cmp_12_out_3));
  eight_bit_eq_cmp eight_bit_eq_cmp_13 (.in_1(control[7:0]), .in_2(8'h1c), .out_3(eight_bit_eq_cmp_13_out_3));
  eight_bit_eq_cmp eight_bit_eq_cmp_14 (.in_1(control[7:0]), .in_2(8'h1d), .out_3(eight_bit_eq_cmp_14_out_3));
  eight_bit_eq_cmp eight_bit_eq_cmp_15 (.in_1(control[7:0]), .in_2(8'h1e), .out_3(eight_bit_eq_cmp_15_out_3));
  eight_bit_eq_cmp eight_bit_eq_cmp_16 (.in_1(control[7:0]), .in_2(8'h1f), .out_3(eight_bit_eq_cmp_16_out_3));
  and and_1 (data_bus_enable, four_bit_eq_cmp_1_out_3, to_data_bus_out_3);
  and and_2 (and_2_out, four_bit_eq_cmp_1_out_3, to_addr_bus_out_3);
  and and_3 (and_3_out, four_bit_eq_cmp_1_out_3, to_data_bus_indirect_out_3);
  and and_4 (and_4_out, four_bit_eq_cmp_1_out_3, to_data_bus_indirect_w_offset_out_3);
  and and_5 (write_enable, four_bit_eq_cmp_1_out_3, load_data_bus_out_3);
  and and_6 (special_functions[0], four_bit_eq_cmp_1_out_3, eight_bit_eq_cmp_1_out_3);
  and and_7 (special_functions[1], four_bit_eq_cmp_1_out_3, eight_bit_eq_cmp_2_out_3);
  and and_8 (special_functions[2], four_bit_eq_cmp_1_out_3, eight_bit_eq_cmp_3_out_3);
  and and_9 (special_functions[3], four_bit_eq_cmp_1_out_3, eight_bit_eq_cmp_4_out_3);
  and and_10 (special_functions[4], four_bit_eq_cmp_1_out_3, eight_bit_eq_cmp_5_out_3);
  and and_11 (special_functions[5], four_bit_eq_cmp_1_out_3, eight_bit_eq_cmp_6_out_3);
  and and_12 (special_functions[6], four_bit_eq_cmp_1_out_3, eight_bit_eq_cmp_7_out_3);
  and and_13 (special_functions[7], four_bit_eq_cmp_1_out_3, eight_bit_eq_cmp_8_out_3);
  and and_14 (special_functions[8], four_bit_eq_cmp_1_out_3, eight_bit_eq_cmp_9_out_3);
  and and_15 (special_functions[9], four_bit_eq_cmp_1_out_3, eight_bit_eq_cmp_10_out_3);
  and and_16 (special_functions[10], four_bit_eq_cmp_1_out_3, eight_bit_eq_cmp_11_out_3);
  and and_17 (special_functions[11], four_bit_eq_cmp_1_out_3, eight_bit_eq_cmp_12_out_3);
  and and_18 (special_functions[12], four_bit_eq_cmp_1_out_3, eight_bit_eq_cmp_13_out_3);
  and and_19 (special_functions[13], four_bit_eq_cmp_1_out_3, eight_bit_eq_cmp_14_out_3);
  and and_20 (special_functions[14], four_bit_eq_cmp_1_out_3, eight_bit_eq_cmp_15_out_3);
  and and_21 (special_functions[15], four_bit_eq_cmp_1_out_3, eight_bit_eq_cmp_16_out_3);
  or or_1 (addr_bus_enable, and_2_out, and_3_out, and_4_out);

  // Notes on the sheet:
  //   special functions
endmodule

module special_register_dual_opdec (
  input  [15:0] control_bus_1,
  input  [15:0] control_bus_2,
  input  [3:0] id,
  output data_bus_enable,
  output addr_bus_enable,
  output write_enable,
  output [15:0] special_functions
);

  wire special_register_opdec_1_addr_bus_enable, special_register_opdec_1_data_bus_enable,
       special_register_opdec_1_write_enable, special_register_opdec_2_addr_bus_enable,
       special_register_opdec_2_data_bus_enable, special_register_opdec_2_write_enable;
  wire [15:0] special_register_opdec_1_special_functions, special_register_opdec_2_special_functions;

  special_register_opdec special_register_opdec_1 (
    .control(control_bus_1), .id(id), .data_bus_enable(special_register_opdec_1_data_bus_enable),
    .addr_bus_enable(special_register_opdec_1_addr_bus_enable),
    .write_enable(special_register_opdec_1_write_enable),
    .special_functions(special_register_opdec_1_special_functions));
  special_register_opdec special_register_opdec_2 (
    .control(control_bus_2), .id(id), .data_bus_enable(special_register_opdec_2_data_bus_enable),
    .addr_bus_enable(special_register_opdec_2_addr_bus_enable),
    .write_enable(special_register_opdec_2_write_enable),
    .special_functions(special_register_opdec_2_special_functions));
  or or_1 (data_bus_enable, special_register_opdec_2_data_bus_enable, special_register_opdec_1_data_bus_enable);
  or or_2 (addr_bus_enable, special_register_opdec_2_addr_bus_enable, special_register_opdec_1_addr_bus_enable);
  or or_3 (write_enable, special_register_opdec_2_write_enable, special_register_opdec_1_write_enable);
  assign special_functions = special_register_opdec_2_special_functions | special_register_opdec_1_special_functions;  // OR_Gate or_4, 16 bits wide
endmodule

module special_registers_opdec (
  input  [15:0] data_in,
  input  [15:0] ctrl_unit_in,
  input  [15:0] control,
  output [15:0] data_to_pk,
  output pk_to_data,
  output pk_to_addr,
  output pk_inc,
  output sp_to_data,
  output sp_to_addr,
  output pk_dec,
  output sp_write,
  output pk_write,
  output sp_inc,
  output sp_dec,
  output sp_predec_to_addr,
  output offs_to_data,
  output offs_to_addr,
  output offs_write
);

  wire and_1_out, and_2_out, and_3_out, and_4_out, and_5_out, and_6_out, comparator_1_eq, comparator_1_gt,
       comparator_1_lt, or_1_out, special_register_opdec_1_addr_bus_enable,
       special_register_opdec_1_write_enable;
  wire [15:0] multiplexer_1_out, special_register_opdec_1_special_functions;
  wire [15:3] special_register_opdec_2_special_functions;

  special_register_opdec special_register_opdec_1 (
    .control(control), .id(4'b0000), .data_bus_enable(pk_to_data),
    .addr_bus_enable(special_register_opdec_1_addr_bus_enable),
    .write_enable(special_register_opdec_1_write_enable),
    .special_functions({special_register_opdec_1_special_functions[15:3], pk_dec, special_register_opdec_1_special_functions[1:0]}));
  special_register_opdec special_register_opdec_2 (
    .control(control), .id(4'b0001), .data_bus_enable(sp_to_data), .addr_bus_enable(sp_to_addr),
    .write_enable(sp_write),
    .special_functions({special_register_opdec_2_special_functions, sp_predec_to_addr, sp_dec, sp_inc}));
  special_register_opdec special_register_opdec_3 (
    .control(control), .id(4'b0100), .data_bus_enable(offs_to_data), .addr_bus_enable(offs_to_addr),
    .write_enable(offs_write));  // open: special_functions
  Multiplexer #(.width(16)) multiplexer_1 (.in0(data_in), .in1(ctrl_unit_in), .out(multiplexer_1_out), .sel(or_1_out));
  or or_1 (or_1_out, special_register_opdec_1_special_functions[3], special_register_opdec_1_special_functions[4], special_register_opdec_1_special_functions[5], special_register_opdec_1_special_functions[6], special_register_opdec_1_special_functions[7], special_register_opdec_1_special_functions[8], special_register_opdec_1_special_functions[9], special_register_opdec_1_special_functions[10], special_register_opdec_1_special_functions[11]);
  or or_2 (pk_to_addr, special_register_opdec_1_addr_bus_enable, special_register_opdec_1_special_functions[1]);
  Comparator #(.width(16)) comparator_1 (
    .a(data_in), .b({16{1'b0}}), .gt(comparator_1_gt), .eq(comparator_1_eq), .lt(comparator_1_lt));
  Multiplexer #(.width(16)) multiplexer_2 (.in0({16{1'b0}}), .in1(multiplexer_1_out), .out(data_to_pk), .sel(pk_write));
  or or_3 (pk_write, special_register_opdec_1_special_functions[11], special_register_opdec_1_write_enable, special_register_opdec_1_special_functions[3], special_register_opdec_1_special_functions[4], and_1_out, and_2_out, and_3_out, and_4_out, and_5_out, and_6_out);
  and and_1 (and_1_out, special_register_opdec_1_special_functions[5], comparator_1_eq);
  and and_2 (and_2_out, special_register_opdec_1_special_functions[6], ~comparator_1_eq);  // AND_Gate
  and and_3 (and_3_out, special_register_opdec_1_special_functions[7], comparator_1_lt);
  and and_4 (and_4_out, special_register_opdec_1_special_functions[8], ~comparator_1_lt);  // AND_Gate
  and and_5 (and_5_out, special_register_opdec_1_special_functions[9], comparator_1_gt);
  and and_6 (and_6_out, special_register_opdec_1_special_functions[10], ~comparator_1_gt);  // AND_Gate
  or or_4 (pk_inc, special_register_opdec_1_special_functions[0], special_register_opdec_1_special_functions[1]);

  // Notes on the sheet:
  //   <- the combinatorial logic for conditional gotos
endmodule

module io_pins_4 (
  input  [15:0] control_bus,
  input  [15:0] data_bus_in,
  input  [15:0] addr_bus_in,
  input  clock,
  input  reset,
  input  in_6,
  input  in_7,
  input  in_8,
  input  in_9,
  output [15:0] data_bus_out,
  output out_11,
  output out_12,
  output out_13,
  output out_14,
  output out_15,
  output out_16,
  output out_17,
  output out_18
);

  wire and_1_out, and_2_out, and_3_out, and_4_out, and_5_out, and_6_out, and_7_out, and_8_out, and_9_out,
       and_10_out, and_11_out, and_12_out, comparator_1_eq, comparator_2_eq, comparator_3_eq,
       comparator_4_eq, comparator_5_eq, comparator_6_eq, decoder_1_out0, decoder_1_out1, decoder_1_out2,
       decoder_1_out3, multiplexer_1_out, not_1_out, not_2_out, or_1_out, or_2_out, or_3_out, or_4_out,
       or_5_out, or_6_out;
  wire [0:0] or_7_out;

  not not_1 (not_1_out, clock);
  Comparator comparator_1 (.a(control_bus[7:0]), .b(8'h30), .eq(comparator_1_eq));  // open: gt, lt
  Comparator comparator_2 (.a(control_bus[7:0]), .b(8'h31), .eq(comparator_2_eq));  // open: gt, lt
  Comparator comparator_3 (.a(control_bus[7:0]), .b(8'h32), .eq(comparator_3_eq));  // open: gt, lt
  Comparator comparator_4 (.a(control_bus[7:0]), .b(8'h33), .eq(comparator_4_eq));  // open: gt, lt
  Comparator comparator_5 (.a(control_bus[7:0]), .b(8'h34), .eq(comparator_5_eq));  // open: gt, lt
  Comparator comparator_6 (.a(control_bus[7:0]), .b(8'h35), .eq(comparator_6_eq));  // open: gt, lt
  Decoder #(.enable("false"), .select(2)) decoder_1 (
    .out0(decoder_1_out0), .out1(decoder_1_out1), .out2(decoder_1_out2), .out3(decoder_1_out3),
    .sel(control_bus[13:12]));
  or or_1 (or_1_out, comparator_6_eq, comparator_4_eq, comparator_3_eq);
  or or_2 (or_2_out, comparator_2_eq, comparator_1_eq);
  or or_3 (or_3_out, ~comparator_1_eq, comparator_2_eq);  // OR_Gate
  and and_1 (and_1_out, decoder_1_out0, or_1_out, not_1_out);
  and and_2 (and_2_out, decoder_1_out0, or_2_out, not_1_out);
  Multiplexer #(.enable("true")) multiplexer_1 (
    .in0(or_4_out), .in1(1'b1), .out(multiplexer_1_out), .sel(comparator_4_eq), .en(not_2_out));
  not not_2 (not_2_out, comparator_3_eq);
  D_Flip_Flop d_ff_1 (.D(multiplexer_1_out), .clk(and_1_out), .Q(out_11), .reset(reset));  // open: Qn, preset
  D_Flip_Flop d_ff_2 (.D(or_3_out), .clk(and_2_out), .Q(out_12), .reset(reset));  // open: Qn, preset
  and and_3 (and_3_out, decoder_1_out0, in_6);
  D_Flip_Flop d_ff_3 (.D(multiplexer_1_out), .clk(and_4_out), .Q(out_13), .reset(reset));  // open: Qn, preset
  and and_4 (and_4_out, decoder_1_out1, or_1_out, not_1_out);
  D_Flip_Flop d_ff_4 (.D(or_3_out), .clk(and_5_out), .Q(out_14), .reset(reset));  // open: Qn, preset
  and and_5 (and_5_out, decoder_1_out1, or_2_out, not_1_out);
  or or_4 (or_4_out, data_bus_in[0], data_bus_in[1], data_bus_in[2], data_bus_in[3], data_bus_in[4], data_bus_in[5], data_bus_in[6], data_bus_in[7], data_bus_in[8], data_bus_in[9], data_bus_in[10], data_bus_in[11], data_bus_in[12], data_bus_in[13], data_bus_in[14], data_bus_in[15]);
  and and_6 (and_6_out, decoder_1_out1, in_7);
  or or_5 (or_5_out, and_3_out, and_6_out);
  D_Flip_Flop d_ff_5 (.D(multiplexer_1_out), .clk(and_7_out), .Q(out_15), .reset(reset));  // open: Qn, preset
  and and_7 (and_7_out, decoder_1_out2, or_1_out, not_1_out);
  D_Flip_Flop d_ff_6 (.D(or_3_out), .clk(and_8_out), .Q(out_16), .reset(reset));  // open: Qn, preset
  and and_8 (and_8_out, decoder_1_out2, or_2_out, not_1_out);
  or or_6 (or_6_out, or_5_out, and_9_out);
  and and_9 (and_9_out, decoder_1_out2, in_8);
  and and_10 (and_10_out, decoder_1_out3, or_1_out, not_1_out);
  and and_11 (and_11_out, decoder_1_out3, or_2_out, not_1_out);
  D_Flip_Flop d_ff_7 (.D(multiplexer_1_out), .clk(and_10_out), .Q(out_17), .reset(reset));  // open: Qn, preset
  D_Flip_Flop d_ff_8 (.D(or_3_out), .clk(and_11_out), .Q(out_18), .reset(reset));  // open: Qn, preset
  or or_7 (or_7_out[0], or_6_out, and_12_out);
  and and_12 (and_12_out, decoder_1_out3, in_9);
  sixt_bit_gatekeeper sixt_bit_gatekeeper_1 (
    .in_1(comparator_5_eq), .in_2({{15{1'b0}}, or_7_out[0]}), .out_3(data_bus_out));
endmodule

module io_pins_8 (
  input  [15:0] control_bus,
  input  [15:0] data_bus_in,
  input  clock,
  input  reset,
  input  in_5,
  input  in_6,
  input  in_7,
  input  in_8,
  input  in_9,
  input  in_10,
  input  in_11,
  input  in_12,
  output [15:0] data_bus_out,
  output out_14,
  output out_15,
  output out_16,
  output out_17,
  output out_18,
  output out_19,
  output out_20,
  output out_21,
  output out_22,
  output out_23,
  output out_24,
  output out_25,
  output out_26,
  output out_27,
  output out_28,
  output out_29
);

  wire and_1_out, and_2_out, and_3_out, and_4_out, and_5_out, and_6_out, and_7_out, and_8_out, and_9_out,
       and_10_out, and_11_out, and_12_out, and_13_out, and_14_out, and_15_out, and_16_out, and_17_out,
       and_18_out, and_19_out, and_20_out, and_21_out, and_22_out, and_23_out, and_24_out, and_25_out,
       buffer_1_out, buffer_2_out, buffer_3_out, buffer_4_out, comparator_1_eq, comparator_2_eq,
       comparator_3_eq, comparator_4_eq, comparator_5_eq, comparator_6_eq, decoder_1_out0, decoder_1_out1,
       decoder_1_out2, decoder_1_out3, decoder_1_out4, decoder_1_out5, decoder_1_out6, decoder_1_out7,
       multiplexer_1_out, not_1_out, not_2_out, not_3_out, or_1_out, or_2_out, or_3_out, or_4_out, or_5_out,
       or_6_out, or_7_out, or_8_out, or_9_out, or_10_out, or_11_out, or_13_out, or_14_out, s_r_ff_1_q,
       s_r_ff_2_q, s_r_ff_3_q, s_r_ff_4_q, s_r_ff_5_q;

  not not_1 (not_1_out, clock);
  Comparator #(.width(12)) comparator_1 (.a(control_bus[11:0]), .b(12'ha0), .eq(comparator_1_eq));  // open: gt, lt
  Comparator #(.width(12)) comparator_2 (.a(control_bus[11:0]), .b(12'ha1), .eq(comparator_2_eq));  // open: gt, lt
  Comparator #(.width(12)) comparator_3 (.a(control_bus[11:0]), .b(12'ha2), .eq(comparator_3_eq));  // open: gt, lt
  Comparator #(.width(12)) comparator_4 (.a(control_bus[11:0]), .b(12'ha3), .eq(comparator_4_eq));  // open: gt, lt
  Comparator comparator_5 (.a(control_bus[7:0]), .b(8'ha4), .eq(comparator_5_eq));  // open: gt, lt
  Comparator comparator_6 (.a(control_bus[7:0]), .b(8'ha5), .eq(comparator_6_eq));  // open: gt, lt
  Decoder #(.enable("false"), .select(3)) decoder_1 (
    .out0(decoder_1_out0), .out1(decoder_1_out1), .out2(decoder_1_out2), .out3(decoder_1_out3),
    .out4(decoder_1_out4), .out5(decoder_1_out5), .out6(decoder_1_out6), .out7(decoder_1_out7),
    .sel(control_bus[14:12]));
  or or_1 (or_1_out, comparator_6_eq, comparator_4_eq, comparator_3_eq);
  or or_2 (or_2_out, comparator_2_eq, comparator_1_eq);
  or or_3 (or_3_out, ~comparator_1_eq, comparator_2_eq);  // OR_Gate
  and and_1 (and_1_out, decoder_1_out0, or_1_out, not_1_out);
  and and_2 (and_2_out, decoder_1_out0, or_2_out, not_1_out);
  or or_4 (or_4_out, data_bus_in[0], data_bus_in[1], data_bus_in[2], data_bus_in[3], data_bus_in[4], data_bus_in[5], data_bus_in[6], data_bus_in[7], data_bus_in[8], data_bus_in[9], data_bus_in[10], data_bus_in[11], data_bus_in[12], data_bus_in[13], data_bus_in[14], data_bus_in[15]);
  Multiplexer #(.enable("true")) multiplexer_1 (
    .in0(or_4_out), .in1(1'b1), .out(multiplexer_1_out), .sel(comparator_4_eq), .en(not_2_out));
  not not_2 (not_2_out, comparator_3_eq);
  D_Flip_Flop d_ff_1 (.D(multiplexer_1_out), .clk(and_1_out), .Q(out_14), .reset(reset));  // open: Qn, preset
  D_Flip_Flop d_ff_2 (.D(or_3_out), .clk(and_2_out), .Q(out_15), .reset(reset));  // open: Qn, preset
  and and_3 (and_3_out, decoder_1_out0, in_5);
  D_Flip_Flop d_ff_3 (.D(multiplexer_1_out), .clk(and_4_out), .Q(out_16), .reset(reset));  // open: Qn, preset
  and and_4 (and_4_out, decoder_1_out1, or_1_out, not_1_out);
  D_Flip_Flop d_ff_4 (.D(or_3_out), .clk(and_5_out), .Q(out_17), .reset(reset));  // open: Qn, preset
  and and_5 (and_5_out, decoder_1_out1, or_2_out, not_1_out);
  and and_6 (and_6_out, decoder_1_out1, in_6);
  or or_5 (or_5_out, and_3_out, and_6_out);
  D_Flip_Flop d_ff_5 (.D(multiplexer_1_out), .clk(and_7_out), .Q(out_18), .reset(reset));  // open: Qn, preset
  and and_7 (and_7_out, decoder_1_out2, or_1_out, not_1_out);
  D_Flip_Flop d_ff_6 (.D(or_3_out), .clk(and_8_out), .Q(out_19), .reset(reset));  // open: Qn, preset
  and and_8 (and_8_out, decoder_1_out2, or_2_out, not_1_out);
  or or_6 (or_6_out, or_5_out, and_9_out);
  and and_9 (and_9_out, decoder_1_out2, in_7);
  and and_10 (and_10_out, decoder_1_out3, or_1_out, not_1_out);
  and and_11 (and_11_out, decoder_1_out3, or_2_out, not_1_out);
  D_Flip_Flop d_ff_7 (.D(multiplexer_1_out), .clk(and_10_out), .Q(out_20), .reset(reset));  // open: Qn, preset
  D_Flip_Flop d_ff_8 (.D(or_3_out), .clk(and_11_out), .Q(out_21), .reset(reset));  // open: Qn, preset
  or or_7 (or_7_out, or_6_out, and_12_out);
  and and_12 (and_12_out, decoder_1_out3, in_8);
  and and_13 (and_13_out, decoder_1_out4, or_1_out, not_1_out);
  and and_14 (and_14_out, decoder_1_out4, or_2_out, not_1_out);
  D_Flip_Flop d_ff_9 (.D(multiplexer_1_out), .clk(and_13_out), .Q(out_22), .reset(reset));  // open: Qn, preset
  D_Flip_Flop d_ff_10 (.D(or_3_out), .clk(and_14_out), .Q(out_23), .reset(reset));  // open: Qn, preset
  and and_15 (and_15_out, decoder_1_out4, in_9);
  or or_8 (or_8_out, or_7_out, and_15_out);
  D_Flip_Flop d_ff_11 (.D(multiplexer_1_out), .clk(and_16_out), .Q(out_24), .reset(reset));  // open: Qn, preset
  and and_16 (and_16_out, decoder_1_out5, or_1_out, not_1_out);
  D_Flip_Flop d_ff_12 (.D(or_3_out), .clk(and_17_out), .Q(out_25), .reset(reset));  // open: Qn, preset
  and and_17 (and_17_out, decoder_1_out5, or_2_out, not_1_out);
  and and_18 (and_18_out, decoder_1_out5, in_10);
  or or_9 (or_9_out, or_8_out, and_18_out);
  D_Flip_Flop d_ff_13 (.D(multiplexer_1_out), .clk(and_19_out), .Q(out_26), .reset(reset));  // open: Qn, preset
  and and_19 (and_19_out, decoder_1_out6, or_1_out, not_1_out);
  D_Flip_Flop d_ff_14 (.D(or_3_out), .clk(and_20_out), .Q(out_27), .reset(reset));  // open: Qn, preset
  and and_20 (and_20_out, decoder_1_out6, or_2_out, not_1_out);
  or or_10 (or_10_out, or_9_out, and_21_out);
  and and_21 (and_21_out, decoder_1_out6, in_11);
  and and_22 (and_22_out, decoder_1_out7, or_1_out, not_1_out);
  and and_23 (and_23_out, decoder_1_out7, or_2_out, not_1_out);
  D_Flip_Flop d_ff_15 (.D(multiplexer_1_out), .clk(and_22_out), .Q(out_28), .reset(reset));  // open: Qn, preset
  D_Flip_Flop d_ff_16 (.D(or_3_out), .clk(and_23_out), .Q(out_29), .reset(reset));  // open: Qn, preset
  or or_11 (or_11_out, or_10_out, and_24_out);
  and and_24 (and_24_out, decoder_1_out7, in_12);
  and and_25 (and_25_out, comparator_5_eq, or_11_out);
  S_R_Flip_Flop s_r_ff_1 (.Q(s_r_ff_1_q), .reset(or_14_out), .preset(and_25_out));  // open: S, R, clk, Qn
  S_R_Flip_Flop s_r_ff_2 (
    .S(s_r_ff_1_q), .R(1'b0), .clk(not_1_out), .Q(s_r_ff_2_q), .reset(or_14_out));  // open: Qn, preset
  S_R_Flip_Flop s_r_ff_3 (
    .S(s_r_ff_2_q), .R(1'b0), .clk(not_1_out), .Q(s_r_ff_3_q), .reset(or_14_out));  // open: Qn, preset
  or or_12 (data_bus_out[0], s_r_ff_1_q, s_r_ff_2_q, s_r_ff_3_q);
  S_R_Flip_Flop #(.trigger("falling")) s_r_ff_4 (
    .S(s_r_ff_3_q), .R(1'b0), .clk(not_1_out), .Q(s_r_ff_4_q), .reset(or_13_out));  // open: Qn, preset
  buf buffer_1 (buffer_1_out, or_14_out);
  buf buffer_2 (buffer_2_out, buffer_1_out);
  or or_13 (or_13_out, reset, s_r_ff_5_q);
  buf buffer_3 (buffer_3_out, buffer_2_out);
  buf buffer_4 (buffer_4_out, buffer_3_out);
  S_R_Flip_Flop s_r_ff_5 (
    .S(buffer_4_out), .R(not_3_out), .clk(not_1_out), .Q(s_r_ff_5_q), .reset(reset));  // open: Qn, preset
  not not_3 (not_3_out, or_14_out);
  or or_14 (or_14_out, s_r_ff_4_q, reset);

  assign data_bus_out[15:1] = {15{1'b0}};
endmodule

module io_pins_16 (
  input  [15:0] control_bus,
  input  [15:0] data_bus_in,
  input  clock,
  input  reset,
  input  in_5,
  input  in_6,
  input  in_7,
  input  in_8,
  input  in_9,
  input  in_10,
  input  in_11,
  input  in_12,
  input  in_13,
  input  in_14,
  input  in_15,
  input  in_16,
  input  in_17,
  input  in_18,
  input  in_19,
  input  in_20,
  output [15:0] data_bus_out,
  output out_22,
  output out_23,
  output out_24,
  output out_25,
  output out_26,
  output out_27,
  output out_28,
  output out_29,
  output out_30,
  output out_31,
  output out_32,
  output out_33,
  output out_34,
  output out_35,
  output out_36,
  output out_37,
  output out_38,
  output out_39,
  output out_40,
  output out_41,
  output out_42,
  output out_43,
  output out_44,
  output out_45,
  output out_46,
  output out_47,
  output out_48,
  output out_49,
  output out_50,
  output out_51,
  output out_52,
  output out_53
);

  wire and_1_out, and_2_out, and_3_out, and_4_out, and_5_out, and_6_out, and_7_out, and_8_out, and_9_out,
       and_10_out, and_11_out, and_12_out, and_13_out, and_14_out, and_15_out, and_16_out, and_17_out,
       and_18_out, and_19_out, and_20_out, and_21_out, and_22_out, and_23_out, and_24_out, and_25_out,
       and_26_out, and_27_out, and_28_out, and_29_out, and_30_out, and_31_out, and_32_out, and_33_out,
       and_34_out, and_35_out, and_36_out, and_37_out, and_38_out, and_39_out, and_40_out, and_41_out,
       and_42_out, and_43_out, and_44_out, and_45_out, and_46_out, and_47_out, and_48_out, and_49_out,
       and_50_out, buffer_1_out, buffer_2_out, buffer_3_out, buffer_4_out, comparator_1_eq, comparator_2_eq,
       comparator_3_eq, comparator_4_eq, comparator_5_eq, comparator_6_eq, decoder_1_out0, decoder_1_out1,
       decoder_1_out2, decoder_1_out3, decoder_1_out4, decoder_1_out5, decoder_1_out6, decoder_1_out7,
       decoder_1_out8, decoder_1_out9, decoder_1_out10, decoder_1_out11, decoder_1_out12, decoder_1_out13,
       decoder_1_out14, decoder_1_out15, multiplexer_1_out, not_1_out, not_2_out, not_3_out, not_4_out,
       or_1_out, or_2_out, or_3_out, or_4_out, or_5_out, or_6_out, or_7_out, or_8_out, or_9_out, or_10_out,
       or_11_out, or_12_out, or_13_out, or_14_out, or_15_out, or_16_out, or_17_out, or_18_out, or_19_out,
       or_21_out, or_22_out, s_r_ff_1_q, s_r_ff_2_q, s_r_ff_3_q, s_r_ff_4_q, s_r_ff_5_q;

  not not_1 (not_1_out, clock);
  Comparator #(.width(12)) comparator_1 (.a(control_bus[11:0]), .b(12'ha0), .eq(comparator_1_eq));  // open: gt, lt
  Comparator #(.width(12)) comparator_2 (.a(control_bus[11:0]), .b(12'ha1), .eq(comparator_2_eq));  // open: gt, lt
  Comparator #(.width(12)) comparator_3 (.a(control_bus[11:0]), .b(12'ha2), .eq(comparator_3_eq));  // open: gt, lt
  Comparator #(.width(12)) comparator_4 (.a(control_bus[11:0]), .b(12'ha3), .eq(comparator_4_eq));  // open: gt, lt
  Comparator comparator_5 (.a(control_bus[7:0]), .b(8'ha4), .eq(comparator_5_eq));  // open: gt, lt
  Comparator comparator_6 (.a(control_bus[7:0]), .b(8'ha5), .eq(comparator_6_eq));  // open: gt, lt
  Decoder #(.enable("false"), .select(4)) decoder_1 (
    .out0(decoder_1_out0), .out1(decoder_1_out1), .out2(decoder_1_out2), .out3(decoder_1_out3),
    .out4(decoder_1_out4), .out5(decoder_1_out5), .out6(decoder_1_out6), .out7(decoder_1_out7),
    .out8(decoder_1_out8), .out9(decoder_1_out9), .out10(decoder_1_out10), .out11(decoder_1_out11),
    .out12(decoder_1_out12), .out13(decoder_1_out13), .out14(decoder_1_out14), .out15(decoder_1_out15),
    .sel(control_bus[15:12]));
  or or_1 (or_1_out, comparator_6_eq, comparator_4_eq, comparator_3_eq);
  or or_2 (or_2_out, comparator_2_eq, comparator_1_eq);
  or or_3 (or_3_out, ~comparator_1_eq, comparator_2_eq);  // OR_Gate
  and and_1 (and_1_out, decoder_1_out0, or_1_out, not_1_out);
  and and_2 (and_2_out, decoder_1_out0, or_2_out, not_1_out);
  or or_4 (or_4_out, data_bus_in[0], data_bus_in[1], data_bus_in[2], data_bus_in[3], data_bus_in[4], data_bus_in[5], data_bus_in[6], data_bus_in[7], data_bus_in[8], data_bus_in[9], data_bus_in[10], data_bus_in[11], data_bus_in[12], data_bus_in[13], data_bus_in[14], data_bus_in[15]);
  Multiplexer #(.enable("true")) multiplexer_1 (
    .in0(or_4_out), .in1(1'b1), .out(multiplexer_1_out), .sel(comparator_4_eq), .en(not_2_out));
  not not_2 (not_2_out, comparator_3_eq);
  D_Flip_Flop d_ff_1 (.D(multiplexer_1_out), .clk(and_1_out), .Q(out_22), .reset(reset));  // open: Qn, preset
  D_Flip_Flop d_ff_2 (.D(or_3_out), .clk(and_2_out), .Q(out_23), .reset(reset));  // open: Qn, preset
  and and_3 (and_3_out, decoder_1_out0, in_5);
  D_Flip_Flop d_ff_3 (.D(multiplexer_1_out), .clk(and_4_out), .Q(out_24), .reset(reset));  // open: Qn, preset
  and and_4 (and_4_out, decoder_1_out1, or_1_out, not_1_out);
  D_Flip_Flop d_ff_4 (.D(or_3_out), .clk(and_5_out), .Q(out_25), .reset(reset));  // open: Qn, preset
  and and_5 (and_5_out, decoder_1_out1, or_2_out, not_1_out);
  and and_6 (and_6_out, decoder_1_out1, in_6);
  or or_5 (or_5_out, and_3_out, and_6_out);
  D_Flip_Flop d_ff_5 (.D(multiplexer_1_out), .clk(and_7_out), .Q(out_26), .reset(reset));  // open: Qn, preset
  and and_7 (and_7_out, decoder_1_out2, or_1_out, not_1_out);
  D_Flip_Flop d_ff_6 (.D(or_3_out), .clk(and_8_out), .Q(out_27), .reset(reset));  // open: Qn, preset
  and and_8 (and_8_out, decoder_1_out2, or_2_out, not_1_out);
  or or_6 (or_6_out, or_5_out, and_9_out);
  and and_9 (and_9_out, decoder_1_out2, in_7);
  and and_10 (and_10_out, decoder_1_out3, or_1_out, not_1_out);
  and and_11 (and_11_out, decoder_1_out3, or_2_out, not_1_out);
  D_Flip_Flop d_ff_7 (.D(multiplexer_1_out), .clk(and_10_out), .Q(out_28), .reset(reset));  // open: Qn, preset
  D_Flip_Flop d_ff_8 (.D(or_3_out), .clk(and_11_out), .Q(out_29), .reset(reset));  // open: Qn, preset
  or or_7 (or_7_out, or_6_out, and_12_out);
  and and_12 (and_12_out, decoder_1_out3, in_8);
  and and_13 (and_13_out, decoder_1_out4, or_1_out, not_1_out);
  and and_14 (and_14_out, decoder_1_out4, or_2_out, not_1_out);
  D_Flip_Flop d_ff_9 (.D(multiplexer_1_out), .clk(and_13_out), .Q(out_30), .reset(reset));  // open: Qn, preset
  D_Flip_Flop d_ff_10 (.D(or_3_out), .clk(and_14_out), .Q(out_31), .reset(reset));  // open: Qn, preset
  and and_15 (and_15_out, decoder_1_out4, in_9);
  or or_8 (or_8_out, or_7_out, and_15_out);
  D_Flip_Flop d_ff_11 (.D(multiplexer_1_out), .clk(and_16_out), .Q(out_32), .reset(reset));  // open: Qn, preset
  and and_16 (and_16_out, decoder_1_out5, or_1_out, not_1_out);
  D_Flip_Flop d_ff_12 (.D(or_3_out), .clk(and_17_out), .Q(out_33), .reset(reset));  // open: Qn, preset
  and and_17 (and_17_out, decoder_1_out5, or_2_out, not_1_out);
  and and_18 (and_18_out, decoder_1_out5, in_10);
  or or_9 (or_9_out, or_8_out, and_18_out);
  D_Flip_Flop d_ff_13 (.D(multiplexer_1_out), .clk(and_19_out), .Q(out_34), .reset(reset));  // open: Qn, preset
  and and_19 (and_19_out, decoder_1_out6, or_1_out, not_1_out);
  D_Flip_Flop d_ff_14 (.D(or_3_out), .clk(and_20_out), .Q(out_35), .reset(reset));  // open: Qn, preset
  and and_20 (and_20_out, decoder_1_out6, or_2_out, not_1_out);
  or or_10 (or_10_out, or_9_out, and_21_out);
  and and_21 (and_21_out, decoder_1_out6, in_11);
  and and_22 (and_22_out, decoder_1_out7, or_1_out, not_1_out);
  and and_23 (and_23_out, decoder_1_out7, or_2_out, not_1_out);
  D_Flip_Flop d_ff_15 (.D(multiplexer_1_out), .clk(and_22_out), .Q(out_36), .reset(reset));  // open: Qn, preset
  D_Flip_Flop d_ff_16 (.D(or_3_out), .clk(and_23_out), .Q(out_37), .reset(reset));  // open: Qn, preset
  or or_11 (or_11_out, or_10_out, and_24_out);
  and and_24 (and_24_out, decoder_1_out7, in_12);
  and and_25 (and_25_out, decoder_1_out8, or_1_out, not_1_out);
  and and_26 (and_26_out, decoder_1_out8, or_2_out, not_1_out);
  D_Flip_Flop d_ff_17 (.D(multiplexer_1_out), .clk(and_25_out), .Q(out_38), .reset(reset));  // open: Qn, preset
  D_Flip_Flop d_ff_18 (.D(or_3_out), .clk(and_26_out), .Q(out_39), .reset(reset));  // open: Qn, preset
  and and_27 (and_27_out, decoder_1_out8, in_13);
  or or_12 (or_12_out, or_11_out, and_27_out);
  D_Flip_Flop d_ff_19 (.D(multiplexer_1_out), .clk(and_28_out), .Q(out_40), .reset(reset));  // open: Qn, preset
  and and_28 (and_28_out, decoder_1_out9, or_1_out, not_1_out);
  D_Flip_Flop d_ff_20 (.D(or_3_out), .clk(and_29_out), .Q(out_41), .reset(reset));  // open: Qn, preset
  and and_29 (and_29_out, decoder_1_out9, or_2_out, not_1_out);
  and and_30 (and_30_out, decoder_1_out9, in_14);
  or or_13 (or_13_out, or_12_out, and_30_out);
  D_Flip_Flop d_ff_21 (.D(multiplexer_1_out), .clk(and_31_out), .Q(out_42), .reset(reset));  // open: Qn, preset
  and and_31 (and_31_out, decoder_1_out10, or_1_out, not_1_out);
  D_Flip_Flop d_ff_22 (.D(or_3_out), .clk(and_32_out), .Q(out_43), .reset(reset));  // open: Qn, preset
  and and_32 (and_32_out, decoder_1_out10, or_2_out, not_1_out);
  or or_14 (or_14_out, or_13_out, and_33_out);
  and and_33 (and_33_out, decoder_1_out10, in_15);
  and and_34 (and_34_out, decoder_1_out11, or_1_out, not_1_out);
  and and_35 (and_35_out, decoder_1_out11, or_2_out, not_1_out);
  D_Flip_Flop d_ff_23 (.D(multiplexer_1_out), .clk(and_34_out), .Q(out_44), .reset(reset));  // open: Qn, preset
  D_Flip_Flop d_ff_24 (.D(or_3_out), .clk(and_35_out), .Q(out_45), .reset(reset));  // open: Qn, preset
  or or_15 (or_15_out, or_14_out, and_36_out);
  and and_36 (and_36_out, decoder_1_out11, in_16);
  and and_37 (and_37_out, decoder_1_out12, or_1_out, not_1_out);
  and and_38 (and_38_out, decoder_1_out12, or_2_out, not_1_out);
  D_Flip_Flop d_ff_25 (.D(multiplexer_1_out), .clk(and_37_out), .Q(out_46), .reset(reset));  // open: Qn, preset
  D_Flip_Flop d_ff_26 (.D(or_3_out), .clk(and_38_out), .Q(out_47), .reset(reset));  // open: Qn, preset
  and and_39 (and_39_out, decoder_1_out12, in_17);
  or or_16 (or_16_out, or_15_out, and_39_out);
  D_Flip_Flop d_ff_27 (.D(multiplexer_1_out), .clk(and_40_out), .Q(out_48), .reset(reset));  // open: Qn, preset
  and and_40 (and_40_out, decoder_1_out13, or_1_out, not_1_out);
  D_Flip_Flop d_ff_28 (.D(or_3_out), .clk(and_41_out), .Q(out_49), .reset(reset));  // open: Qn, preset
  and and_41 (and_41_out, decoder_1_out13, or_2_out, not_1_out);
  and and_42 (and_42_out, decoder_1_out13, in_18);
  or or_17 (or_17_out, or_16_out, and_42_out);
  D_Flip_Flop d_ff_29 (.D(multiplexer_1_out), .clk(and_43_out), .Q(out_50), .reset(reset));  // open: Qn, preset
  and and_43 (and_43_out, decoder_1_out14, or_1_out, not_1_out);
  D_Flip_Flop d_ff_30 (.D(or_3_out), .clk(and_44_out), .Q(out_51), .reset(reset));  // open: Qn, preset
  and and_44 (and_44_out, decoder_1_out14, or_2_out, not_1_out);
  or or_18 (or_18_out, or_17_out, and_45_out);
  and and_45 (and_45_out, decoder_1_out14, in_19);
  and and_46 (and_46_out, decoder_1_out15, or_1_out, not_1_out);
  and and_47 (and_47_out, decoder_1_out15, or_2_out, not_1_out);
  and and_48 (and_48_out, multiplexer_1_out, and_46_out);
  not not_3 (not_3_out, not_1_out);
  D_Flip_Flop d_ff_31 (.D(or_3_out), .clk(and_47_out), .Q(out_53), .reset(reset));  // open: Qn, preset
  or or_19 (or_19_out, or_18_out, and_49_out);
  two_ticker two_ticker_1 (.signal_in(and_48_out), .clock(not_3_out), .reset(reset), .out_4(out_52));
  and and_49 (and_49_out, decoder_1_out15, in_20);
  and and_50 (and_50_out, comparator_5_eq, or_19_out);
  S_R_Flip_Flop s_r_ff_1 (.Q(s_r_ff_1_q), .reset(or_22_out), .preset(and_50_out));  // open: S, R, clk, Qn
  S_R_Flip_Flop s_r_ff_2 (
    .S(s_r_ff_1_q), .R(1'b0), .clk(not_1_out), .Q(s_r_ff_2_q), .reset(or_22_out));  // open: Qn, preset
  S_R_Flip_Flop s_r_ff_3 (
    .S(s_r_ff_2_q), .R(1'b0), .clk(not_1_out), .Q(s_r_ff_3_q), .reset(or_22_out));  // open: Qn, preset
  or or_20 (data_bus_out[0], s_r_ff_1_q, s_r_ff_2_q, s_r_ff_3_q);
  S_R_Flip_Flop #(.trigger("falling")) s_r_ff_4 (
    .S(s_r_ff_3_q), .R(1'b0), .clk(not_1_out), .Q(s_r_ff_4_q), .reset(or_21_out));  // open: Qn, preset
  buf buffer_1 (buffer_1_out, or_22_out);
  buf buffer_2 (buffer_2_out, buffer_1_out);
  or or_21 (or_21_out, reset, s_r_ff_5_q);
  buf buffer_3 (buffer_3_out, buffer_2_out);
  buf buffer_4 (buffer_4_out, buffer_3_out);
  S_R_Flip_Flop s_r_ff_5 (
    .S(buffer_4_out), .R(not_4_out), .clk(not_1_out), .Q(s_r_ff_5_q), .reset(reset));  // open: Qn, preset
  not not_4 (not_4_out, or_22_out);
  or or_22 (or_22_out, s_r_ff_4_q, reset);

  assign data_bus_out[15:1] = {15{1'b0}};
endmodule

module clock_division_bell (
  input  [7:0] divisor,
  input  load_divisor,
  input  restart,
  input  clock,
  input  reset,
  output out_6
);

  wire and_1_out, and_2_out, comparator_1_eq, j_k_ff_1_q, nor_1_out, not_1_out, or_1_out, or_2_out,
       rising_edge_delay_1_out_2;
  wire [7:0] adder_1_out, divisor_register_q, kounter_q, multiplexer_1_out, multiplexer_2_out,
       subtractor_1_out, subtractor_2_out;

  Subtractor subtractor_1 (.a(divisor), .b(8'h1), .out(subtractor_1_out));  // open: bin, bout
  Register divisor_register (.D(subtractor_1_out), .en(load_divisor), .clk(clock), .Q(divisor_register_q), .clr(reset));
  not not_1 (not_1_out, nor_1_out);
  Multiplexer #(.width(8)) multiplexer_1 (.in0({8{1'b0}}), .in1(adder_1_out), .out(multiplexer_1_out), .sel(not_1_out));
  Adder adder_1 (.a(kounter_q), .b(8'h1), .out(adder_1_out));  // open: cin, cout
  and and_1 (and_1_out, clock, ~load_divisor);  // AND_Gate
  or or_1 (or_1_out, load_divisor, restart, reset);
  Multiplexer #(.width(8)) multiplexer_2 (
    .in0(multiplexer_1_out), .in1({8{1'b1}}), .out(multiplexer_2_out), .sel(or_1_out));
  and and_2 (and_2_out, and_1_out, ~or_1_out);  // AND_Gate
  rising_edge_delay rising_edge_delay_1 (.in_1(or_1_out), .out_2(rising_edge_delay_1_out_2));
  Register kounter (.D(multiplexer_2_out), .en(1'b1), .clk(or_2_out), .Q(kounter_q));  // open: clr
  or or_2 (or_2_out, and_2_out, rising_edge_delay_1_out_2);
  Subtractor subtractor_2 (.a(kounter_q), .b(divisor_register_q), .out(subtractor_2_out));  // open: bin, bout
  Comparator #(.mode("unsigned")) comparator_1 (.a(divisor), .b({8{1'b0}}), .eq(comparator_1_eq));  // open: gt, lt
  nor nor_1 (nor_1_out, subtractor_2_out[0], subtractor_2_out[1], subtractor_2_out[2], subtractor_2_out[3], subtractor_2_out[4], subtractor_2_out[5], subtractor_2_out[6], subtractor_2_out[7]);
  J_K_Flip_Flop j_k_ff_1 (.J(1'b1), .K(1'b1), .clk(nor_1_out), .Q(j_k_ff_1_q), .reset(or_1_out));  // open: Qn, preset
  Multiplexer multiplexer_3 (.in0(j_k_ff_1_q), .in1(clock), .out(out_6), .sel(comparator_1_eq));
endmodule

module falling_edge_delay (
  input  in_1,
  output out_2
);

  wire buffer_1_out, buffer_2_out, buffer_3_out, buffer_4_out, buffer_5_out, buffer_6_out, buffer_7_out,
       buffer_8_out, buffer_9_out, buffer_10_out, buffer_11_out, buffer_12_out, buffer_13_out, buffer_14_out,
       buffer_15_out, buffer_16_out, buffer_17_out, buffer_18_out, buffer_19_out, buffer_20_out,
       buffer_21_out, buffer_22_out, buffer_23_out, buffer_24_out, buffer_25_out, buffer_26_out,
       buffer_27_out, buffer_28_out, buffer_29_out, buffer_30_out, buffer_31_out, buffer_32_out,
       buffer_33_out, buffer_34_out, buffer_35_out, buffer_36_out, buffer_37_out, buffer_38_out,
       buffer_39_out, buffer_40_out, buffer_41_out, buffer_42_out, buffer_43_out, buffer_44_out,
       buffer_45_out, buffer_46_out, buffer_47_out, buffer_48_out, buffer_49_out, buffer_50_out,
       buffer_51_out, buffer_52_out, buffer_53_out, buffer_54_out, buffer_55_out, buffer_56_out,
       buffer_57_out, buffer_58_out, buffer_59_out, buffer_60_out, buffer_61_out, buffer_62_out,
       buffer_63_out, buffer_64_out;

  buf buffer_1 (buffer_1_out, in_1);
  buf buffer_2 (buffer_2_out, buffer_1_out);
  buf buffer_3 (buffer_3_out, buffer_4_out);
  buf buffer_4 (buffer_4_out, buffer_5_out);
  buf buffer_5 (buffer_5_out, buffer_25_out);
  buf buffer_6 (buffer_6_out, buffer_3_out);
  buf buffer_7 (buffer_7_out, buffer_6_out);
  buf buffer_8 (buffer_8_out, buffer_9_out);
  buf buffer_9 (buffer_9_out, buffer_10_out);
  buf buffer_10 (buffer_10_out, buffer_33_out);
  buf buffer_11 (buffer_11_out, buffer_8_out);
  buf buffer_12 (buffer_12_out, buffer_11_out);
  buf buffer_13 (buffer_13_out, buffer_14_out);
  buf buffer_14 (buffer_14_out, buffer_15_out);
  buf buffer_15 (buffer_15_out, buffer_41_out);
  buf buffer_16 (buffer_16_out, buffer_13_out);
  buf buffer_17 (buffer_17_out, buffer_16_out);
  buf buffer_18 (buffer_18_out, buffer_19_out);
  buf buffer_19 (buffer_19_out, buffer_20_out);
  buf buffer_20 (buffer_20_out, buffer_49_out);
  buf buffer_21 (buffer_21_out, buffer_2_out);
  buf buffer_22 (buffer_22_out, buffer_21_out);
  buf buffer_23 (buffer_23_out, buffer_22_out);
  buf buffer_24 (buffer_24_out, buffer_23_out);
  buf buffer_25 (buffer_25_out, buffer_26_out);
  buf buffer_26 (buffer_26_out, buffer_27_out);
  buf buffer_27 (buffer_27_out, buffer_28_out);
  buf buffer_28 (buffer_28_out, buffer_55_out);
  buf buffer_29 (buffer_29_out, buffer_7_out);
  buf buffer_30 (buffer_30_out, buffer_29_out);
  buf buffer_31 (buffer_31_out, buffer_30_out);
  buf buffer_32 (buffer_32_out, buffer_31_out);
  buf buffer_33 (buffer_33_out, buffer_34_out);
  buf buffer_34 (buffer_34_out, buffer_35_out);
  buf buffer_35 (buffer_35_out, buffer_36_out);
  buf buffer_36 (buffer_36_out, buffer_58_out);
  buf buffer_37 (buffer_37_out, buffer_12_out);
  buf buffer_38 (buffer_38_out, buffer_37_out);
  buf buffer_39 (buffer_39_out, buffer_38_out);
  buf buffer_40 (buffer_40_out, buffer_39_out);
  buf buffer_41 (buffer_41_out, buffer_42_out);
  buf buffer_42 (buffer_42_out, buffer_43_out);
  buf buffer_43 (buffer_43_out, buffer_44_out);
  buf buffer_44 (buffer_44_out, buffer_61_out);
  buf buffer_45 (buffer_45_out, buffer_17_out);
  buf buffer_46 (buffer_46_out, buffer_45_out);
  buf buffer_47 (buffer_47_out, buffer_46_out);
  buf buffer_48 (buffer_48_out, buffer_47_out);
  buf buffer_49 (buffer_49_out, buffer_50_out);
  buf buffer_50 (buffer_50_out, buffer_51_out);
  buf buffer_51 (buffer_51_out, buffer_52_out);
  buf buffer_52 (buffer_52_out, buffer_64_out);
  or or_1 (out_2, buffer_18_out, in_1);
  buf buffer_53 (buffer_53_out, buffer_24_out);
  buf buffer_54 (buffer_54_out, buffer_53_out);
  buf buffer_55 (buffer_55_out, buffer_54_out);
  buf buffer_56 (buffer_56_out, buffer_32_out);
  buf buffer_57 (buffer_57_out, buffer_56_out);
  buf buffer_58 (buffer_58_out, buffer_57_out);
  buf buffer_59 (buffer_59_out, buffer_40_out);
  buf buffer_60 (buffer_60_out, buffer_59_out);
  buf buffer_61 (buffer_61_out, buffer_60_out);
  buf buffer_62 (buffer_62_out, buffer_48_out);
  buf buffer_63 (buffer_63_out, buffer_62_out);
  buf buffer_64 (buffer_64_out, buffer_63_out);
endmodule

module rising_edge_delay (
  input  in_1,
  output out_2
);

  wire buffer_1_out, buffer_2_out, buffer_3_out, buffer_4_out, buffer_5_out, buffer_6_out, buffer_7_out,
       buffer_8_out, buffer_9_out, buffer_10_out, buffer_11_out, buffer_12_out, buffer_13_out, buffer_14_out,
       buffer_15_out, buffer_16_out, buffer_17_out, buffer_18_out, buffer_19_out, buffer_20_out,
       buffer_21_out, buffer_22_out, buffer_23_out, buffer_24_out, buffer_25_out, buffer_26_out,
       buffer_27_out, buffer_28_out, buffer_29_out, buffer_30_out, buffer_31_out, buffer_32_out,
       buffer_33_out, buffer_34_out, buffer_35_out, buffer_36_out, buffer_37_out, buffer_38_out,
       buffer_39_out, buffer_40_out, buffer_41_out, buffer_42_out, buffer_43_out, buffer_44_out,
       buffer_45_out, buffer_46_out, buffer_47_out, buffer_48_out, buffer_49_out, buffer_50_out,
       buffer_51_out, buffer_52_out, buffer_53_out, buffer_54_out, buffer_55_out, buffer_56_out,
       buffer_57_out, buffer_58_out, buffer_59_out, buffer_60_out, buffer_61_out, buffer_62_out,
       buffer_63_out, buffer_64_out;

  buf buffer_1 (buffer_1_out, in_1);
  buf buffer_2 (buffer_2_out, buffer_1_out);
  buf buffer_3 (buffer_3_out, buffer_4_out);
  buf buffer_4 (buffer_4_out, buffer_5_out);
  buf buffer_5 (buffer_5_out, buffer_25_out);
  buf buffer_6 (buffer_6_out, buffer_3_out);
  buf buffer_7 (buffer_7_out, buffer_6_out);
  buf buffer_8 (buffer_8_out, buffer_9_out);
  buf buffer_9 (buffer_9_out, buffer_10_out);
  buf buffer_10 (buffer_10_out, buffer_33_out);
  buf buffer_11 (buffer_11_out, buffer_8_out);
  buf buffer_12 (buffer_12_out, buffer_11_out);
  buf buffer_13 (buffer_13_out, buffer_14_out);
  buf buffer_14 (buffer_14_out, buffer_15_out);
  buf buffer_15 (buffer_15_out, buffer_41_out);
  buf buffer_16 (buffer_16_out, buffer_13_out);
  buf buffer_17 (buffer_17_out, buffer_16_out);
  buf buffer_18 (buffer_18_out, buffer_19_out);
  buf buffer_19 (buffer_19_out, buffer_20_out);
  buf buffer_20 (buffer_20_out, buffer_49_out);
  buf buffer_21 (buffer_21_out, buffer_2_out);
  buf buffer_22 (buffer_22_out, buffer_21_out);
  buf buffer_23 (buffer_23_out, buffer_22_out);
  buf buffer_24 (buffer_24_out, buffer_23_out);
  buf buffer_25 (buffer_25_out, buffer_26_out);
  buf buffer_26 (buffer_26_out, buffer_27_out);
  buf buffer_27 (buffer_27_out, buffer_28_out);
  buf buffer_28 (buffer_28_out, buffer_55_out);
  buf buffer_29 (buffer_29_out, buffer_7_out);
  buf buffer_30 (buffer_30_out, buffer_29_out);
  buf buffer_31 (buffer_31_out, buffer_30_out);
  buf buffer_32 (buffer_32_out, buffer_31_out);
  buf buffer_33 (buffer_33_out, buffer_34_out);
  buf buffer_34 (buffer_34_out, buffer_35_out);
  buf buffer_35 (buffer_35_out, buffer_36_out);
  buf buffer_36 (buffer_36_out, buffer_58_out);
  buf buffer_37 (buffer_37_out, buffer_12_out);
  buf buffer_38 (buffer_38_out, buffer_37_out);
  buf buffer_39 (buffer_39_out, buffer_38_out);
  buf buffer_40 (buffer_40_out, buffer_39_out);
  buf buffer_41 (buffer_41_out, buffer_42_out);
  buf buffer_42 (buffer_42_out, buffer_43_out);
  buf buffer_43 (buffer_43_out, buffer_44_out);
  buf buffer_44 (buffer_44_out, buffer_61_out);
  buf buffer_45 (buffer_45_out, buffer_17_out);
  buf buffer_46 (buffer_46_out, buffer_45_out);
  buf buffer_47 (buffer_47_out, buffer_46_out);
  buf buffer_48 (buffer_48_out, buffer_47_out);
  buf buffer_49 (buffer_49_out, buffer_50_out);
  buf buffer_50 (buffer_50_out, buffer_51_out);
  buf buffer_51 (buffer_51_out, buffer_52_out);
  buf buffer_52 (buffer_52_out, buffer_64_out);
  and and_1 (out_2, buffer_18_out, in_1);
  buf buffer_53 (buffer_53_out, buffer_24_out);
  buf buffer_54 (buffer_54_out, buffer_53_out);
  buf buffer_55 (buffer_55_out, buffer_54_out);
  buf buffer_56 (buffer_56_out, buffer_32_out);
  buf buffer_57 (buffer_57_out, buffer_56_out);
  buf buffer_58 (buffer_58_out, buffer_57_out);
  buf buffer_59 (buffer_59_out, buffer_40_out);
  buf buffer_60 (buffer_60_out, buffer_59_out);
  buf buffer_61 (buffer_61_out, buffer_60_out);
  buf buffer_62 (buffer_62_out, buffer_48_out);
  buf buffer_63 (buffer_63_out, buffer_62_out);
  buf buffer_64 (buffer_64_out, buffer_63_out);

  // Notes on the sheet:
  //   While the falling edge is propagated ASAP
  //   Delays the rising edge from reaching the output for 48 * (buffer propagation delay),
endmodule

module not_or_hasnt (
  input  in_1,
  output out_2
);

  wire and_1_out, s_r_ff_1_q, s_r_ff_2_q;

  S_R_Flip_Flop s_r_ff_1 (.Q(s_r_ff_1_q), .reset(1'b0), .preset(in_1));  // open: S, R, clk, Qn
  and and_1 (and_1_out, s_r_ff_1_q, ~in_1);  // AND_Gate
  S_R_Flip_Flop s_r_ff_2 (.Q(s_r_ff_2_q), .reset(in_1), .preset(and_1_out));  // open: S, R, clk, Qn
  or or_1 (out_2, s_r_ff_2_q, ~s_r_ff_1_q);  // OR_Gate
endmodule

module addr_bus_controller (
  input  [15:0] control_bus_1,
  input  [15:0] control_bus_2,
  input  [15:0] data_bus_in,
  input  clock,
  input  reset,
  input  [15:0] control_unit_in,
  input  [15:0] registers_in,
  input  [15:0] special_registers_in,
  output [15:0] addr_bus_out
);

  wire nor_1_out, or_1_out, sixt_bit_eq_cmp_1_out_3, sixt_bit_eq_cmp_2_out_3, sixt_bit_eq_cmp_3_out_3,
       sixt_bit_eq_cmp_4_out_3;
  wire [15:0] multiplexer_1_out, or_2_out;

  sixt_bit_eq_cmp sixt_bit_eq_cmp_1 (.in_1(control_bus_1), .in_2(16'h51), .out_3(sixt_bit_eq_cmp_1_out_3));
  sixt_bit_eq_cmp sixt_bit_eq_cmp_2 (.in_1(control_bus_1), .in_2(16'h53), .out_3(sixt_bit_eq_cmp_2_out_3));
  sixt_bit_eq_cmp sixt_bit_eq_cmp_3 (.in_1(control_bus_2), .in_2(16'h51), .out_3(sixt_bit_eq_cmp_3_out_3));
  sixt_bit_eq_cmp sixt_bit_eq_cmp_4 (.in_1(control_bus_2), .in_2(16'h53), .out_3(sixt_bit_eq_cmp_4_out_3));
  nor nor_1 (nor_1_out, sixt_bit_eq_cmp_1_out_3, sixt_bit_eq_cmp_3_out_3);
  or or_1 (or_1_out, sixt_bit_eq_cmp_2_out_3, sixt_bit_eq_cmp_4_out_3);
  Register #(.trigger("falling"), .width(16)) register_1 (
    .D(multiplexer_1_out), .en(nor_1_out), .clk(clock), .Q(addr_bus_out), .clr(reset));
  assign or_2_out = control_unit_in | registers_in | special_registers_in;  // OR_Gate or_2, 16 bits wide
  Multiplexer #(.width(16)) multiplexer_1 (.in0(or_2_out), .in1(data_bus_in), .out(multiplexer_1_out), .sel(or_1_out));
endmodule

module control_bus_controller (
  input  [15:0] control_1,
  input  [15:0] control_2,
  input  clock,
  input  reset,
  output [15:0] control_bus_1,
  output [15:0] control_bus_2
);

  Register #(.width(16)) register_1 (.D(control_1), .clk(clock), .Q(control_bus_1), .clr(reset));  // open: en
  Register #(.width(16)) register_2 (.D(control_2), .clk(clock), .Q(control_bus_2), .clr(reset));  // open: en
endmodule

module eight_bit_gate (
  input  enable,
  input  [7:0] data_in,
  output [7:0] data_out
);

  assign data_out = {8{enable}} & data_in;  // AND_Gate and_1, 8 bits wide
endmodule

module microcode_mixer (
  input  [15:0] instruction,
  input  [15:0] tmpa_in,
  input  [15:0] tmpb_in,
  input  [15:0] microcode_in,
  output [15:0] microcode_out
);

  wire [3:0] multiplexer_1_out, multiplexer_2_out;

  Multiplexer #(.select(4), .width(4)) multiplexer_1 (
    .in0(microcode_in[11:8]), .in1(instruction[15:12]), .in2(instruction[11:8]), .in3(instruction[7:4]),
    .in4(instruction[3:0]), .in5(tmpa_in[15:12]), .in6(tmpa_in[11:8]), .in7(tmpa_in[7:4]),
    .in8(tmpa_in[3:0]), .in9(tmpb_in[15:12]), .in10(tmpb_in[11:8]), .in11(tmpb_in[7:4]), .in12(tmpb_in[3:0]),
    .out(multiplexer_1_out));  // open: in13, in14, in15, sel
  Multiplexer #(.select(4), .width(4)) multiplexer_2 (
    .in0(microcode_in[15:12]), .in1(instruction[15:12]), .in2(instruction[11:8]), .in3(instruction[7:4]),
    .in4(instruction[3:0]), .in5(tmpa_in[15:12]), .in6(tmpa_in[11:8]), .in7(tmpa_in[7:4]),
    .in8(tmpa_in[3:0]), .in9(tmpb_in[15:12]), .in10(tmpb_in[11:8]), .in11(tmpb_in[7:4]), .in12(tmpb_in[3:0]),
    .out(multiplexer_2_out));  // open: in13, in14, in15, sel
  Multiplexer #(.width(4)) multiplexer_3 (
    .in0(microcode_in[11:8]), .in1(multiplexer_1_out), .out(microcode_out[11:8]), .sel(microcode_in[7]));
  Multiplexer #(.width(4)) multiplexer_4 (
    .in0(microcode_in[15:12]), .in1(multiplexer_2_out), .out(microcode_out[15:12]), .sel(microcode_in[7]));

  assign microcode_out[7:0] = {1'b0, microcode_in[6:0]};
endmodule

module tick_counter (
  input  clock,
  input  reset,
  output [31:0] posedge_count,
  output [31:0] cycle_count,
  output [31:0] negedge_count
);

  wire [31:0] adder_1_out, adder_2_out;

  Register #(.width(32)) register_1 (.D(adder_1_out), .clk(clock), .Q(posedge_count), .clr(reset));  // open: en
  Adder #(.width(32)) adder_1 (.a(posedge_count), .b(32'h1), .out(adder_1_out));  // open: cin, cout
  Register #(.trigger("falling"), .width(32)) register_2 (
    .D(adder_2_out), .clk(clock), .Q(negedge_count), .clr(reset));  // open: en
  Adder #(.width(32)) adder_2 (.a(negedge_count), .b(32'h1), .out(adder_2_out));  // open: cin, cout
  Adder #(.width(32)) adder_3 (.a(posedge_count), .b(negedge_count), .out(cycle_count));  // open: cin, cout
endmodule

module four_bit_conditional_incrementer (
  input  in_1,
  input  [3:0] in_2,
  output [3:0] out_3
);

  Adder #(.width(4)) adder_1 (.a(in_2), .b(4'b0000), .out(out_3), .cin(in_1));  // open: cout
endmodule

module auto_reset_register (
  input  [15:0] data_in,
  input  write,
  input  [15:0] reset_value,
  input  clock,
  input  reset,
  output [15:0] data_out
);

  wire and_1_out, and_2_out, and_3_out, buffer_1_out, buffer_2_out, buffer_3_out, buffer_4_out, buffer_5_out,
       buffer_6_out, buffer_7_out, d_ff_1_q, not_1_out, or_1_out, or_2_out, s_r_ff_1_qn, s_r_ff_2_q,
       s_r_ff_3_q, sixt_bit_eq_zero_1_out_2;
  wire [15:0] multiplexer_1_out, multiplexer_2_out;

  Pull_Resistor pull_resistor_1 (.node(reset_value));
  sixt_bit_eq_zero sixt_bit_eq_zero_1 (.in_1(reset_value), .out_2(sixt_bit_eq_zero_1_out_2));
  S_R_Flip_Flop s_r_ff_1 (.Qn(s_r_ff_1_qn), .preset(clock));  // open: S, R, clk, Q, reset
  Multiplexer #(.width(16)) multiplexer_1 (
    .in0({16{1'b0}}), .in1(reset_value), .out(multiplexer_1_out), .sel(not_1_out));
  not not_1 (not_1_out, sixt_bit_eq_zero_1_out_2);
  or or_1 (or_1_out, s_r_ff_1_qn, reset);
  buf buffer_1 (buffer_1_out, clock);
  buf buffer_2 (buffer_2_out, buffer_1_out);
  buf buffer_3 (buffer_3_out, buffer_2_out);
  S_R_Flip_Flop s_r_ff_2 (.Q(s_r_ff_2_q), .reset(and_2_out), .preset(or_1_out));  // open: S, R, clk, Qn
  and and_1 (and_1_out, clock, ~buffer_4_out);  // AND_Gate
  buf buffer_4 (buffer_4_out, buffer_3_out);
  and and_2 (and_2_out, ~s_r_ff_3_q, buffer_7_out, s_r_ff_2_q);  // AND_Gate
  Multiplexer #(.width(16)) multiplexer_2 (
    .in0(data_in), .in1(multiplexer_1_out), .out(multiplexer_2_out), .sel(s_r_ff_2_q));
  D_Flip_Flop d_ff_1 (.D(clock), .clk(s_r_ff_2_q), .Q(d_ff_1_q), .reset(and_1_out));  // open: Qn, preset
  S_R_Flip_Flop s_r_ff_3 (.Q(s_r_ff_3_q), .reset(and_1_out), .preset(and_3_out));  // open: S, R, clk, Qn
  buf buffer_5 (buffer_5_out, and_1_out);
  buf buffer_6 (buffer_6_out, buffer_5_out);
  buf buffer_7 (buffer_7_out, buffer_6_out);
  and and_3 (and_3_out, d_ff_1_q, ~s_r_ff_3_q);  // AND_Gate
  Register #(.width(16)) register_1 (.D(multiplexer_2_out), .en(or_2_out), .clk(clock), .Q(data_out));  // open: clr
  or or_2 (or_2_out, s_r_ff_2_q, write);
endmodule

module default_register_00ff (
  input  [15:0] data_in,
  input  write,
  input  [15:0] reset_value,
  input  clock,
  input  reset,
  output [15:0] data_out
);

  wire and_1_out, and_2_out, and_3_out, buffer_1_out, buffer_2_out, buffer_3_out, buffer_4_out, buffer_5_out,
       buffer_6_out, buffer_7_out, d_ff_1_q, not_1_out, or_1_out, or_2_out, s_r_ff_1_qn, s_r_ff_2_q,
       s_r_ff_3_q, sixt_bit_eq_zero_1_out_2;
  wire [15:0] multiplexer_1_out, multiplexer_2_out;

  Pull_Resistor pull_resistor_1 (.node(reset_value));
  sixt_bit_eq_zero sixt_bit_eq_zero_1 (.in_1(reset_value), .out_2(sixt_bit_eq_zero_1_out_2));
  S_R_Flip_Flop s_r_ff_1 (.Qn(s_r_ff_1_qn), .preset(clock));  // open: S, R, clk, Q, reset
  Multiplexer #(.width(16)) multiplexer_1 (.in0(16'hff), .in1(reset_value), .out(multiplexer_1_out), .sel(not_1_out));
  not not_1 (not_1_out, sixt_bit_eq_zero_1_out_2);
  or or_1 (or_1_out, s_r_ff_1_qn, reset);
  buf buffer_1 (buffer_1_out, clock);
  buf buffer_2 (buffer_2_out, buffer_1_out);
  buf buffer_3 (buffer_3_out, buffer_2_out);
  S_R_Flip_Flop s_r_ff_2 (.Q(s_r_ff_2_q), .reset(and_2_out), .preset(or_1_out));  // open: S, R, clk, Qn
  and and_1 (and_1_out, clock, ~buffer_4_out);  // AND_Gate
  buf buffer_4 (buffer_4_out, buffer_3_out);
  buf buffer_5 (buffer_5_out, and_1_out);
  and and_2 (and_2_out, ~s_r_ff_3_q, buffer_7_out, s_r_ff_2_q);  // AND_Gate
  buf buffer_6 (buffer_6_out, buffer_5_out);
  buf buffer_7 (buffer_7_out, buffer_6_out);
  Multiplexer #(.width(16)) multiplexer_2 (
    .in0(data_in), .in1(multiplexer_1_out), .out(multiplexer_2_out), .sel(s_r_ff_2_q));
  D_Flip_Flop d_ff_1 (.D(clock), .clk(s_r_ff_2_q), .Q(d_ff_1_q), .reset(and_1_out));  // open: Qn, preset
  S_R_Flip_Flop s_r_ff_3 (.Q(s_r_ff_3_q), .reset(and_1_out), .preset(and_3_out));  // open: S, R, clk, Qn
  and and_3 (and_3_out, d_ff_1_q, ~s_r_ff_3_q);  // AND_Gate
  Register #(.width(16)) register_1 (.D(multiplexer_2_out), .en(or_2_out), .clk(clock), .Q(data_out));  // open: clr
  or or_2 (or_2_out, s_r_ff_2_q, write);
endmodule
module stacker (
  input  bypass_mask,
  input  enable,
  input  write_changemask,
  input  [15:0] mem_in,
  input  clk,
  input  reset,
  input  [15:0] register_write,
  input  [15:0] stacking_mask,
  output active,
  output [15:0] control_bus_1_out,
  output [15:0] change_mask,
  output [15:0] control_bus_2_out,
  output [15:0] to_data_bus
);

  wire adder_1_out, and_1_out, and_18_out, and_19_out, and_20_out, and_21_out, and_22_out, and_23_out,
       and_24_out, and_25_out, and_26_out, and_27_out, and_28_out, and_29_out, and_30_out, and_31_out,
       and_32_out, and_33_out, and_34_out, and_35_out, and_36_out, and_37_out, and_38_out, and_39_out,
       and_40_out, and_41_out, and_42_out, and_43_out, and_44_out, and_45_out, and_46_out, and_47_out,
       and_48_out, and_49_out, and_50_out, and_51_out, and_52_out, and_53_out, and_54_out, and_55_out,
       and_56_out, and_57_out, and_58_out, and_59_out, and_60_out, and_61_out, and_62_out, and_63_out,
       and_64_out, and_65_out, and_66_out, and_67_out, and_68_out, and_69_out, buffer_1_out, buffer_2_out,
       buffer_3_out, buffer_4_out, buffer_5_out, buffer_6_out, buffer_7_out, buffer_8_out, buffer_9_out,
       buffer_10_out, buffer_11_out, buffer_12_out, buffer_13_out, buffer_14_out, buffer_15_out,
       button_1_out, d_ff_1_q, d_ff_2_q, four_bit_eq_zero_1_out_2, four_bit_eq_zero_2_out_2,
       four_bit_eq_zero_3_out_2, four_bit_eq_zero_4_out_2, four_bit_eq_zero_5_out_2,
       four_bit_eq_zero_6_out_2, four_bit_eq_zero_7_out_2, four_bit_eq_zero_8_out_2,
       four_bit_eq_zero_9_out_2, four_bit_eq_zero_10_out_2, four_bit_eq_zero_11_out_2,
       four_bit_eq_zero_12_out_2, four_bit_eq_zero_13_out_2, four_bit_eq_zero_14_out_2,
       four_bit_eq_zero_15_out_2, four_bit_eq_zero_16_out_2, or_1_out, or_2_out, or_3_out, or_4_out,
       or_5_out, or_6_out, or_7_out, or_8_out, or_9_out, or_10_out, or_11_out, or_12_out, or_13_out,
       or_14_out, or_15_out, or_16_out, or_17_out, or_34_out, register_1_q, register_2_q, register_3_q,
       register_4_q, register_5_q, register_6_q, register_7_q, register_8_q, register_9_q, register_10_q,
       register_11_q, register_12_q, register_13_q, register_14_q, register_15_q, register_16_q,
       register_17_q, s_r_ff_1_q, s_r_ff_19_q;
  wire [3:0] four_bit_conditional_incrementer_1_out_3, four_bit_conditional_incrementer_2_out_3,
       four_bit_conditional_incrementer_3_out_3, four_bit_conditional_incrementer_4_out_3,
       four_bit_conditional_incrementer_5_out_3, four_bit_conditional_incrementer_6_out_3,
       four_bit_conditional_incrementer_7_out_3, four_bit_conditional_incrementer_8_out_3,
       four_bit_conditional_incrementer_9_out_3, four_bit_conditional_incrementer_10_out_3,
       four_bit_conditional_incrementer_11_out_3, four_bit_conditional_incrementer_12_out_3,
       four_bit_conditional_incrementer_13_out_3, four_bit_conditional_incrementer_14_out_3,
       four_bit_conditional_incrementer_15_out_3, four_bit_conditional_incrementer_16_out_3,
       four_bit_g8_1_out_3, four_bit_g8_2_out_3, four_bit_g8_3_out_3, four_bit_g8_4_out_3,
       four_bit_g8_5_out_3, four_bit_g8_6_out_3, four_bit_g8_7_out_3, four_bit_g8_8_out_3,
       four_bit_g8_9_out_3, four_bit_g8_10_out_3, four_bit_g8_11_out_3, four_bit_g8_12_out_3,
       four_bit_g8_13_out_3, four_bit_g8_14_out_3, four_bit_g8_15_out_3, four_bit_g8_16_out_3, or_19_out,
       or_20_out, or_21_out, or_22_out, or_23_out, or_24_out, or_25_out, or_26_out, or_27_out, or_28_out,
       or_29_out, or_30_out, or_31_out, or_32_out, or_33_out;
  wire [15:0] multiplexer_1_out, multiplexer_2_out, multiplexer_3_out, multiplexer_4_out, multiplexer_5_out,
       multiplexer_6_out, multiplexer_7_out, not_1_out, s_r_ff_3_q;
  wire [15:12] or_18_out;

  Button button_1 (.out(button_1_out));
  or or_1 (or_1_out, reset, and_69_out, button_1_out);
  Multiplexer #(.width(16)) multiplexer_1 (
    .in0(register_write), .in1(mem_in), .out(multiplexer_1_out), .sel(s_r_ff_1_q));
  Multiplexer #(.width(16)) multiplexer_2 (
    .in0(stacking_mask), .in1({16{1'b1}}), .out(multiplexer_2_out), .sel(bypass_mask));
  Pull_Resistor pull_resistor_1 (.node(bypass_mask));
  buf buffer_1 (buffer_1_out, write_changemask);
  buf buffer_2 (buffer_2_out, buffer_1_out);
  buf buffer_3 (buffer_3_out, buffer_2_out);
  and and_1 (and_1_out, write_changemask, ~buffer_4_out);  // AND_Gate
  buf buffer_4 (buffer_4_out, buffer_3_out);
  S_R_Flip_Flop s_r_ff_1 (.Q(s_r_ff_1_q), .reset(clk), .preset(and_1_out));  // open: S, R, clk, Qn
  Register #(.width(1)) register_1 (
    .D(multiplexer_1_out[0]), .en(or_2_out), .clk(clk), .Q(register_1_q), .clr(or_1_out));
  or or_2 (or_2_out, multiplexer_1_out[0], s_r_ff_1_q);
  Register #(.width(1)) register_2 (
    .D(multiplexer_1_out[1]), .en(or_3_out), .clk(clk), .Q(register_2_q), .clr(or_1_out));
  or or_3 (or_3_out, multiplexer_1_out[1], s_r_ff_1_q);
  Register #(.width(1)) register_3 (
    .D(multiplexer_1_out[2]), .en(or_4_out), .clk(clk), .Q(register_3_q), .clr(or_1_out));
  or or_4 (or_4_out, multiplexer_1_out[2], s_r_ff_1_q);
  Register #(.width(1)) register_4 (
    .D(multiplexer_1_out[3]), .en(or_5_out), .clk(clk), .Q(register_4_q), .clr(or_1_out));
  or or_5 (or_5_out, multiplexer_1_out[3], s_r_ff_1_q);
  Register #(.width(1)) register_5 (
    .D(multiplexer_1_out[4]), .en(or_6_out), .clk(clk), .Q(register_5_q), .clr(or_1_out));
  or or_6 (or_6_out, multiplexer_1_out[4], s_r_ff_1_q);
  Register #(.width(1)) register_6 (
    .D(multiplexer_1_out[5]), .en(or_7_out), .clk(clk), .Q(register_6_q), .clr(or_1_out));
  or or_7 (or_7_out, multiplexer_1_out[5], s_r_ff_1_q);
  Register #(.width(1)) register_7 (
    .D(multiplexer_1_out[6]), .en(or_8_out), .clk(clk), .Q(register_7_q), .clr(or_1_out));
  or or_8 (or_8_out, multiplexer_1_out[6], s_r_ff_1_q);
  Register #(.width(1)) register_8 (
    .D(multiplexer_1_out[7]), .en(or_9_out), .clk(clk), .Q(register_8_q), .clr(or_1_out));
  or or_9 (or_9_out, multiplexer_1_out[7], s_r_ff_1_q);
  Register #(.width(1)) register_9 (
    .D(multiplexer_1_out[8]), .en(or_10_out), .clk(clk), .Q(register_9_q), .clr(or_1_out));
  or or_10 (or_10_out, multiplexer_1_out[8], s_r_ff_1_q);
  Register #(.width(1)) register_10 (
    .D(multiplexer_1_out[9]), .en(or_11_out), .clk(clk), .Q(register_10_q), .clr(or_1_out));
  or or_11 (or_11_out, multiplexer_1_out[9], s_r_ff_1_q);
  Register #(.width(1)) register_11 (
    .D(multiplexer_1_out[10]), .en(or_12_out), .clk(clk), .Q(register_11_q), .clr(or_1_out));
  or or_12 (or_12_out, multiplexer_1_out[10], s_r_ff_1_q);
  Register #(.width(1)) register_12 (
    .D(multiplexer_1_out[11]), .en(or_13_out), .clk(clk), .Q(register_12_q), .clr(or_1_out));
  or or_13 (or_13_out, multiplexer_1_out[11], s_r_ff_1_q);
  Register #(.width(1)) register_13 (
    .D(multiplexer_1_out[12]), .en(or_14_out), .clk(clk), .Q(register_13_q), .clr(or_1_out));
  or or_14 (or_14_out, multiplexer_1_out[12], s_r_ff_1_q);
  Register #(.width(1)) register_14 (
    .D(multiplexer_1_out[13]), .en(or_15_out), .clk(clk), .Q(register_14_q), .clr(or_1_out));
  or or_15 (or_15_out, multiplexer_1_out[13], s_r_ff_1_q);
  Register #(.width(1)) register_15 (
    .D(multiplexer_1_out[14]), .en(or_16_out), .clk(clk), .Q(register_15_q), .clr(or_1_out));
  or or_16 (or_16_out, multiplexer_1_out[14], s_r_ff_1_q);
  Register #(.width(1)) register_16 (
    .D(multiplexer_1_out[15]), .en(or_17_out), .clk(clk), .Q(register_16_q), .clr(or_1_out));
  or or_17 (or_17_out, multiplexer_1_out[15], s_r_ff_1_q);
  S_R_Flip_Flop s_r_ff_2 (.Q(active), .reset(or_1_out), .preset(and_18_out));  // open: S, R, clk, Qn
  and and_2 (change_mask[0], multiplexer_2_out[0], register_1_q);
  and and_3 (change_mask[1], multiplexer_2_out[1], register_2_q);
  and and_4 (change_mask[2], multiplexer_2_out[2], register_3_q);
  and and_5 (change_mask[3], multiplexer_2_out[3], register_4_q);
  and and_6 (change_mask[4], multiplexer_2_out[4], register_5_q);
  and and_7 (change_mask[5], multiplexer_2_out[5], register_6_q);
  and and_8 (change_mask[6], multiplexer_2_out[6], register_7_q);
  and and_9 (change_mask[7], multiplexer_2_out[7], register_8_q);
  and and_10 (change_mask[8], multiplexer_2_out[8], register_9_q);
  and and_11 (change_mask[9], multiplexer_2_out[9], register_10_q);
  and and_12 (change_mask[10], multiplexer_2_out[10], register_11_q);
  and and_13 (change_mask[11], multiplexer_2_out[11], register_12_q);
  and and_14 (change_mask[12], multiplexer_2_out[12], register_13_q);
  and and_15 (change_mask[13], multiplexer_2_out[13], register_14_q);
  and and_16 (change_mask[14], multiplexer_2_out[14], register_15_q);
  and and_17 (change_mask[15], multiplexer_2_out[15], register_16_q);
  and and_18 (and_18_out, enable, ~active);  // AND_Gate
  assign not_1_out = ~s_r_ff_3_q;  // NOT_Gate not_1, 16 bits wide
  and and_19 (and_19_out, change_mask[0], not_1_out[0]);
  and and_20 (and_20_out, change_mask[1], not_1_out[1]);
  and and_21 (and_21_out, change_mask[2], not_1_out[2]);
  and and_22 (and_22_out, change_mask[3], not_1_out[3]);
  and and_23 (and_23_out, change_mask[4], not_1_out[4]);
  and and_24 (and_24_out, change_mask[5], not_1_out[5]);
  and and_25 (and_25_out, change_mask[6], not_1_out[6]);
  and and_26 (and_26_out, change_mask[7], not_1_out[7]);
  and and_27 (and_27_out, change_mask[8], not_1_out[8]);
  and and_28 (and_28_out, change_mask[9], not_1_out[9]);
  and and_29 (and_29_out, change_mask[10], not_1_out[10]);
  and and_30 (and_30_out, change_mask[11], not_1_out[11]);
  and and_31 (and_31_out, change_mask[12], not_1_out[12]);
  and and_32 (and_32_out, change_mask[13], not_1_out[13]);
  and and_33 (and_33_out, change_mask[14], not_1_out[14]);
  and and_34 (and_34_out, change_mask[15], not_1_out[15]);
  four_bit_conditional_incrementer four_bit_conditional_incrementer_1 (
    .in_2(4'b0000), .in_1(and_19_out), .out_3(four_bit_conditional_incrementer_1_out_3));
  four_bit_eq_zero four_bit_eq_zero_1 (
    .in_1(four_bit_conditional_incrementer_1_out_3), .out_2(four_bit_eq_zero_1_out_2));
  four_bit_conditional_incrementer four_bit_conditional_incrementer_2 (
    .in_2(four_bit_conditional_incrementer_1_out_3), .in_1(and_20_out),
    .out_3(four_bit_conditional_incrementer_2_out_3));
  four_bit_eq_zero four_bit_eq_zero_2 (
    .in_1(four_bit_conditional_incrementer_2_out_3), .out_2(four_bit_eq_zero_2_out_2));
  four_bit_conditional_incrementer four_bit_conditional_incrementer_3 (
    .in_2(four_bit_conditional_incrementer_2_out_3), .in_1(and_21_out),
    .out_3(four_bit_conditional_incrementer_3_out_3));
  four_bit_eq_zero four_bit_eq_zero_3 (
    .in_1(four_bit_conditional_incrementer_3_out_3), .out_2(four_bit_eq_zero_3_out_2));
  four_bit_conditional_incrementer four_bit_conditional_incrementer_4 (
    .in_2(four_bit_conditional_incrementer_3_out_3), .in_1(and_22_out),
    .out_3(four_bit_conditional_incrementer_4_out_3));
  four_bit_eq_zero four_bit_eq_zero_4 (
    .in_1(four_bit_conditional_incrementer_4_out_3), .out_2(four_bit_eq_zero_4_out_2));
  four_bit_conditional_incrementer four_bit_conditional_incrementer_5 (
    .in_2(four_bit_conditional_incrementer_4_out_3), .in_1(and_23_out),
    .out_3(four_bit_conditional_incrementer_5_out_3));
  four_bit_eq_zero four_bit_eq_zero_5 (
    .in_1(four_bit_conditional_incrementer_5_out_3), .out_2(four_bit_eq_zero_5_out_2));
  four_bit_conditional_incrementer four_bit_conditional_incrementer_6 (
    .in_2(four_bit_conditional_incrementer_5_out_3), .in_1(and_24_out),
    .out_3(four_bit_conditional_incrementer_6_out_3));
  four_bit_eq_zero four_bit_eq_zero_6 (
    .in_1(four_bit_conditional_incrementer_6_out_3), .out_2(four_bit_eq_zero_6_out_2));
  four_bit_conditional_incrementer four_bit_conditional_incrementer_7 (
    .in_2(four_bit_conditional_incrementer_6_out_3), .in_1(and_25_out),
    .out_3(four_bit_conditional_incrementer_7_out_3));
  four_bit_eq_zero four_bit_eq_zero_7 (
    .in_1(four_bit_conditional_incrementer_7_out_3), .out_2(four_bit_eq_zero_7_out_2));
  four_bit_conditional_incrementer four_bit_conditional_incrementer_8 (
    .in_2(four_bit_conditional_incrementer_7_out_3), .in_1(and_26_out),
    .out_3(four_bit_conditional_incrementer_8_out_3));
  four_bit_eq_zero four_bit_eq_zero_8 (
    .in_1(four_bit_conditional_incrementer_8_out_3), .out_2(four_bit_eq_zero_8_out_2));
  four_bit_conditional_incrementer four_bit_conditional_incrementer_9 (
    .in_2(four_bit_conditional_incrementer_8_out_3), .in_1(and_27_out),
    .out_3(four_bit_conditional_incrementer_9_out_3));
  four_bit_eq_zero four_bit_eq_zero_9 (
    .in_1(four_bit_conditional_incrementer_9_out_3), .out_2(four_bit_eq_zero_9_out_2));
  four_bit_conditional_incrementer four_bit_conditional_incrementer_10 (
    .in_2(four_bit_conditional_incrementer_9_out_3), .in_1(and_28_out),
    .out_3(four_bit_conditional_incrementer_10_out_3));
  four_bit_eq_zero four_bit_eq_zero_10 (
    .in_1(four_bit_conditional_incrementer_10_out_3), .out_2(four_bit_eq_zero_10_out_2));
  four_bit_conditional_incrementer four_bit_conditional_incrementer_11 (
    .in_2(four_bit_conditional_incrementer_10_out_3), .in_1(and_29_out),
    .out_3(four_bit_conditional_incrementer_11_out_3));
  four_bit_eq_zero four_bit_eq_zero_11 (
    .in_1(four_bit_conditional_incrementer_11_out_3), .out_2(four_bit_eq_zero_11_out_2));
  four_bit_conditional_incrementer four_bit_conditional_incrementer_12 (
    .in_2(four_bit_conditional_incrementer_11_out_3), .in_1(and_30_out),
    .out_3(four_bit_conditional_incrementer_12_out_3));
  four_bit_eq_zero four_bit_eq_zero_12 (
    .in_1(four_bit_conditional_incrementer_12_out_3), .out_2(four_bit_eq_zero_12_out_2));
  four_bit_conditional_incrementer four_bit_conditional_incrementer_13 (
    .in_2(four_bit_conditional_incrementer_12_out_3), .in_1(and_31_out),
    .out_3(four_bit_conditional_incrementer_13_out_3));
  four_bit_eq_zero four_bit_eq_zero_13 (
    .in_1(four_bit_conditional_incrementer_13_out_3), .out_2(four_bit_eq_zero_13_out_2));
  four_bit_conditional_incrementer four_bit_conditional_incrementer_14 (
    .in_2(four_bit_conditional_incrementer_13_out_3), .in_1(and_32_out),
    .out_3(four_bit_conditional_incrementer_14_out_3));
  four_bit_eq_zero four_bit_eq_zero_14 (
    .in_1(four_bit_conditional_incrementer_14_out_3), .out_2(four_bit_eq_zero_14_out_2));
  four_bit_conditional_incrementer four_bit_conditional_incrementer_15 (
    .in_2(four_bit_conditional_incrementer_14_out_3), .in_1(and_33_out),
    .out_3(four_bit_conditional_incrementer_15_out_3));
  four_bit_eq_zero four_bit_eq_zero_15 (
    .in_1(four_bit_conditional_incrementer_15_out_3), .out_2(four_bit_eq_zero_15_out_2));
  four_bit_conditional_incrementer four_bit_conditional_incrementer_16 (
    .in_2(four_bit_conditional_incrementer_15_out_3), .in_1(and_34_out),
    .out_3(four_bit_conditional_incrementer_16_out_3));
  // Probe on four_bit_conditional_incrementer_16_out_3
  and and_35 (and_35_out, four_bit_eq_zero_1_out_2, and_20_out);
  and and_36 (and_36_out, four_bit_eq_zero_2_out_2, and_21_out);
  and and_37 (and_37_out, four_bit_eq_zero_3_out_2, and_22_out);
  and and_38 (and_38_out, four_bit_eq_zero_4_out_2, and_23_out);
  and and_39 (and_39_out, four_bit_eq_zero_5_out_2, and_24_out);
  and and_40 (and_40_out, four_bit_eq_zero_6_out_2, and_25_out);
  and and_41 (and_41_out, four_bit_eq_zero_7_out_2, and_26_out);
  and and_42 (and_42_out, four_bit_eq_zero_8_out_2, and_27_out);
  and and_43 (and_43_out, four_bit_eq_zero_9_out_2, and_28_out);
  and and_44 (and_44_out, four_bit_eq_zero_10_out_2, and_29_out);
  and and_45 (and_45_out, four_bit_eq_zero_11_out_2, and_30_out);
  and and_46 (and_46_out, four_bit_eq_zero_12_out_2, and_31_out);
  and and_47 (and_47_out, four_bit_eq_zero_13_out_2, and_32_out);
  and and_48 (and_48_out, four_bit_eq_zero_14_out_2, and_33_out);
  and and_49 (and_49_out, four_bit_eq_zero_15_out_2, and_34_out);
  and and_50 (and_50_out, register_17_q, and_19_out);
  four_bit_g8 four_bit_g8_1 (.in_1(and_19_out), .in_2(4'b0000), .out_3(four_bit_g8_1_out_3));
  and and_51 (and_51_out, register_17_q, and_35_out);
  four_bit_g8 four_bit_g8_2 (.in_1(and_35_out), .in_2(4'b0001), .out_3(four_bit_g8_2_out_3));
  and and_52 (and_52_out, register_17_q, and_36_out);
  four_bit_g8 four_bit_g8_3 (.in_1(and_36_out), .in_2(4'b0010), .out_3(four_bit_g8_3_out_3));
  and and_53 (and_53_out, register_17_q, and_37_out);
  four_bit_g8 four_bit_g8_4 (.in_1(and_37_out), .in_2(4'b0011), .out_3(four_bit_g8_4_out_3));
  and and_54 (and_54_out, register_17_q, and_38_out);
  four_bit_g8 four_bit_g8_5 (.in_1(and_38_out), .in_2(4'b0100), .out_3(four_bit_g8_5_out_3));
  and and_55 (and_55_out, register_17_q, and_39_out);
  four_bit_g8 four_bit_g8_6 (.in_1(and_39_out), .in_2(4'b0101), .out_3(four_bit_g8_6_out_3));
  and and_56 (and_56_out, register_17_q, and_40_out);
  four_bit_g8 four_bit_g8_7 (.in_1(and_40_out), .in_2(4'b0110), .out_3(four_bit_g8_7_out_3));
  and and_57 (and_57_out, register_17_q, and_41_out);
  four_bit_g8 four_bit_g8_8 (.in_1(and_41_out), .in_2(4'b0111), .out_3(four_bit_g8_8_out_3));
  and and_58 (and_58_out, register_17_q, and_42_out);
  four_bit_g8 four_bit_g8_9 (.in_1(and_42_out), .in_2(4'b1000), .out_3(four_bit_g8_9_out_3));
  and and_59 (and_59_out, register_17_q, and_43_out);
  four_bit_g8 four_bit_g8_10 (.in_1(and_43_out), .in_2(4'b1001), .out_3(four_bit_g8_10_out_3));
  and and_60 (and_60_out, register_17_q, and_44_out);
  four_bit_g8 four_bit_g8_11 (.in_1(and_44_out), .in_2(4'b1010), .out_3(four_bit_g8_11_out_3));
  and and_61 (and_61_out, register_17_q, and_45_out);
  four_bit_g8 four_bit_g8_12 (.in_1(and_45_out), .in_2(4'b1011), .out_3(four_bit_g8_12_out_3));
  and and_62 (and_62_out, register_17_q, and_46_out);
  four_bit_g8 four_bit_g8_13 (.in_1(and_46_out), .in_2(4'b1100), .out_3(four_bit_g8_13_out_3));
  and and_63 (and_63_out, register_17_q, and_47_out);
  four_bit_g8 four_bit_g8_14 (.in_1(and_47_out), .in_2(4'b1101), .out_3(four_bit_g8_14_out_3));
  and and_64 (and_64_out, register_17_q, and_48_out);
  four_bit_g8 four_bit_g8_15 (.in_1(and_48_out), .in_2(4'b1110), .out_3(four_bit_g8_15_out_3));
  and and_65 (and_65_out, register_17_q, and_49_out);
  four_bit_g8 four_bit_g8_16 (.in_1(and_49_out), .in_2(4'b1111), .out_3(four_bit_g8_16_out_3));
  four_bit_eq_zero four_bit_eq_zero_16 (
    .in_1(four_bit_conditional_incrementer_16_out_3), .out_2(four_bit_eq_zero_16_out_2));
  assign or_18_out = four_bit_g8_1_out_3 | or_19_out;  // OR_Gate or_18, 4 bits wide
  assign or_19_out = four_bit_g8_2_out_3 | or_20_out;  // OR_Gate or_19, 4 bits wide
  assign or_20_out = four_bit_g8_3_out_3 | or_21_out;  // OR_Gate or_20, 4 bits wide
  assign or_21_out = four_bit_g8_4_out_3 | or_22_out;  // OR_Gate or_21, 4 bits wide
  assign or_22_out = four_bit_g8_5_out_3 | or_23_out;  // OR_Gate or_22, 4 bits wide
  assign or_23_out = four_bit_g8_6_out_3 | or_24_out;  // OR_Gate or_23, 4 bits wide
  assign or_24_out = four_bit_g8_7_out_3 | or_25_out;  // OR_Gate or_24, 4 bits wide
  assign or_25_out = four_bit_g8_8_out_3 | or_26_out;  // OR_Gate or_25, 4 bits wide
  assign or_26_out = four_bit_g8_9_out_3 | or_27_out;  // OR_Gate or_26, 4 bits wide
  assign or_27_out = four_bit_g8_10_out_3 | or_28_out;  // OR_Gate or_27, 4 bits wide
  assign or_28_out = four_bit_g8_11_out_3 | or_29_out;  // OR_Gate or_28, 4 bits wide
  assign or_29_out = four_bit_g8_12_out_3 | or_30_out;  // OR_Gate or_29, 4 bits wide
  assign or_30_out = four_bit_g8_13_out_3 | or_31_out;  // OR_Gate or_30, 4 bits wide
  assign or_31_out = four_bit_g8_14_out_3 | or_32_out;  // OR_Gate or_31, 4 bits wide
  assign or_32_out = four_bit_g8_15_out_3 | or_33_out;  // OR_Gate or_32, 4 bits wide
  assign or_33_out = four_bit_g8_16_out_3 | four_bit_g8_16_out_3;  // OR_Gate or_33, 4 bits wide
  and and_66 (and_66_out, active, four_bit_eq_zero_16_out_2);
  S_R_Flip_Flop s_r_ff_3 (
    .S(and_50_out), .R(1'b0), .clk(clk), .Q(s_r_ff_3_q[0]), .reset(or_1_out));  // open: Qn, preset
  S_R_Flip_Flop s_r_ff_4 (
    .S(and_51_out), .R(1'b0), .clk(clk), .Q(s_r_ff_3_q[1]), .reset(or_1_out));  // open: Qn, preset
  S_R_Flip_Flop s_r_ff_5 (
    .S(and_52_out), .R(1'b0), .clk(clk), .Q(s_r_ff_3_q[2]), .reset(or_1_out));  // open: Qn, preset
  S_R_Flip_Flop s_r_ff_6 (
    .S(and_53_out), .R(1'b0), .clk(clk), .Q(s_r_ff_3_q[3]), .reset(or_1_out));  // open: Qn, preset
  S_R_Flip_Flop s_r_ff_7 (
    .S(and_54_out), .R(1'b0), .clk(clk), .Q(s_r_ff_3_q[4]), .reset(or_1_out));  // open: Qn, preset
  S_R_Flip_Flop s_r_ff_8 (
    .S(and_55_out), .R(1'b0), .clk(clk), .Q(s_r_ff_3_q[5]), .reset(or_1_out));  // open: Qn, preset
  S_R_Flip_Flop s_r_ff_9 (
    .S(and_56_out), .R(1'b0), .clk(clk), .Q(s_r_ff_3_q[6]), .reset(or_1_out));  // open: Qn, preset
  S_R_Flip_Flop s_r_ff_10 (
    .S(and_57_out), .R(1'b0), .clk(clk), .Q(s_r_ff_3_q[7]), .reset(or_1_out));  // open: Qn, preset
  S_R_Flip_Flop s_r_ff_11 (
    .S(and_58_out), .R(1'b0), .clk(clk), .Q(s_r_ff_3_q[8]), .reset(or_1_out));  // open: Qn, preset
  S_R_Flip_Flop s_r_ff_12 (
    .S(and_59_out), .R(1'b0), .clk(clk), .Q(s_r_ff_3_q[9]), .reset(or_1_out));  // open: Qn, preset
  S_R_Flip_Flop s_r_ff_13 (
    .S(and_60_out), .R(1'b0), .clk(clk), .Q(s_r_ff_3_q[10]), .reset(or_1_out));  // open: Qn, preset
  S_R_Flip_Flop s_r_ff_14 (
    .S(and_61_out), .R(1'b0), .clk(clk), .Q(s_r_ff_3_q[11]), .reset(or_1_out));  // open: Qn, preset
  S_R_Flip_Flop s_r_ff_15 (
    .S(and_62_out), .R(1'b0), .clk(clk), .Q(s_r_ff_3_q[12]), .reset(or_1_out));  // open: Qn, preset
  S_R_Flip_Flop s_r_ff_16 (
    .S(and_63_out), .R(1'b0), .clk(clk), .Q(s_r_ff_3_q[13]), .reset(or_1_out));  // open: Qn, preset
  S_R_Flip_Flop s_r_ff_17 (
    .S(and_64_out), .R(1'b0), .clk(clk), .Q(s_r_ff_3_q[14]), .reset(or_1_out));  // open: Qn, preset
  S_R_Flip_Flop s_r_ff_18 (
    .S(and_65_out), .R(1'b0), .clk(clk), .Q(s_r_ff_3_q[15]), .reset(or_1_out));  // open: Qn, preset
  buf buffer_5 (buffer_5_out, and_66_out);
  buf buffer_6 (buffer_6_out, buffer_5_out);
  and and_67 (and_67_out, and_66_out, buffer_8_out);
  buf buffer_7 (buffer_7_out, buffer_6_out);
  buf buffer_8 (buffer_8_out, buffer_7_out);
  Register #(.width(1)) register_17 (.D(adder_1_out), .en(active), .clk(clk), .Q(register_17_q), .clr(or_34_out));
  or or_34 (or_34_out, or_1_out, and_68_out);
  Multiplexer #(.width(16)) multiplexer_3 (
    .in0({or_18_out, 12'h20}), .in1(16'h25), .out(multiplexer_3_out), .sel(register_17_q));
  Multiplexer #(.width(16)) multiplexer_4 (
    .in0(16'h1012), .in1({16{1'b0}}), .out(multiplexer_4_out), .sel(register_17_q));
  Adder #(.width(1)) adder_1 (.a(register_17_q), .b(1'b1), .out(adder_1_out));  // open: cin, cout
  Multiplexer #(.width(16)) multiplexer_5 (.in0(16'h1012), .in1(16'h25), .out(multiplexer_5_out), .sel(register_17_q));
  S_R_Flip_Flop s_r_ff_19 (.Q(s_r_ff_19_q), .reset(or_1_out), .preset(and_67_out));  // open: S, R, clk, Qn
  buf buffer_9 (buffer_9_out, active);
  buf buffer_10 (buffer_10_out, buffer_9_out);
  buf buffer_11 (buffer_11_out, buffer_10_out);
  and and_68 (and_68_out, active, ~buffer_11_out);  // AND_Gate
  Multiplexer #(.width(16)) multiplexer_6 (
    .in0(multiplexer_3_out), .in1(multiplexer_5_out), .out(multiplexer_6_out), .sel(s_r_ff_19_q));
  Multiplexer #(.width(16)) multiplexer_7 (
    .in0(multiplexer_4_out), .in1({16{1'b0}}), .out(multiplexer_7_out), .sel(s_r_ff_19_q));
  sixt_bit_gatekeeper sixt_bit_gatekeeper_1 (.in_1(active), .in_2(multiplexer_6_out), .out_3(control_bus_1_out));
  sixt_bit_gatekeeper sixt_bit_gatekeeper_2 (.in_1(active), .in_2(multiplexer_7_out), .out_3(control_bus_2_out));
  sixt_bit_gatekeeper sixt_bit_gatekeeper_3 (.in_1(d_ff_1_q), .in_2(change_mask), .out_3(to_data_bus));
  D_Flip_Flop d_ff_1 (.D(s_r_ff_19_q), .clk(clk), .Q(d_ff_1_q), .reset(or_1_out));  // open: Qn, preset
  // Probe on control_bus_1_out
  // Probe on control_bus_2_out
  D_Flip_Flop d_ff_2 (.D(d_ff_1_q), .clk(clk), .Q(d_ff_2_q), .reset(or_1_out));  // open: Qn, preset
  and and_69 (and_69_out, d_ff_2_q, ~buffer_12_out);  // AND_Gate
  buf buffer_12 (buffer_12_out, buffer_13_out);
  buf buffer_13 (buffer_13_out, buffer_14_out);
  buf buffer_14 (buffer_14_out, buffer_15_out);
  buf buffer_15 (buffer_15_out, d_ff_2_q);
endmodule

module unstacker (
  input  enable,
  input  clk,
  input  reset,
  input  [15:0] unstacking_mask,
  output active,
  output [15:0] control_bus_1_out,
  output [15:0] control_bus_2_out
);

  wire adder_1_out, and_1_out, and_2_out, and_3_out, and_4_out, and_5_out, and_6_out, and_7_out, and_8_out,
       and_9_out, and_10_out, and_11_out, and_12_out, and_13_out, and_14_out, and_15_out, and_16_out,
       and_17_out, and_18_out, and_19_out, and_20_out, and_21_out, and_22_out, and_23_out, and_24_out,
       and_25_out, and_26_out, and_27_out, and_28_out, and_29_out, and_30_out, and_31_out, and_32_out,
       and_33_out, buffer_1_out, buffer_2_out, buffer_3_out, buffer_4_out, buffer_5_out, buffer_6_out,
       buffer_7_out, buffer_8_out, buffer_9_out, button_1_out, d_ff_1_q, d_ff_2_q, d_ff_3_q, d_ff_4_q,
       d_ff_5_q, d_ff_6_q, d_ff_7_q, d_ff_8_q, d_ff_9_q, d_ff_10_q, d_ff_11_q, d_ff_12_q, d_ff_13_q,
       d_ff_14_q, d_ff_15_q, d_ff_16_q, four_bit_eq_zero_1_out_2, four_bit_eq_zero_2_out_2,
       four_bit_eq_zero_3_out_2, four_bit_eq_zero_4_out_2, four_bit_eq_zero_5_out_2,
       four_bit_eq_zero_6_out_2, four_bit_eq_zero_7_out_2, four_bit_eq_zero_8_out_2,
       four_bit_eq_zero_9_out_2, four_bit_eq_zero_10_out_2, four_bit_eq_zero_11_out_2,
       four_bit_eq_zero_12_out_2, four_bit_eq_zero_13_out_2, four_bit_eq_zero_14_out_2,
       four_bit_eq_zero_15_out_2, four_bit_eq_zero_16_out_2, or_1_out, or_19_out, register_1_q;
  wire [3:0] four_bit_conditional_incrementer_1_out_3, four_bit_conditional_incrementer_2_out_3,
       four_bit_conditional_incrementer_3_out_3, four_bit_conditional_incrementer_4_out_3,
       four_bit_conditional_incrementer_5_out_3, four_bit_conditional_incrementer_6_out_3,
       four_bit_conditional_incrementer_7_out_3, four_bit_conditional_incrementer_8_out_3,
       four_bit_conditional_incrementer_9_out_3, four_bit_conditional_incrementer_10_out_3,
       four_bit_conditional_incrementer_11_out_3, four_bit_conditional_incrementer_12_out_3,
       four_bit_conditional_incrementer_13_out_3, four_bit_conditional_incrementer_14_out_3,
       four_bit_conditional_incrementer_15_out_3, four_bit_conditional_incrementer_16_out_3,
       four_bit_g8_1_out_3, four_bit_g8_2_out_3, four_bit_g8_3_out_3, four_bit_g8_4_out_3,
       four_bit_g8_5_out_3, four_bit_g8_6_out_3, four_bit_g8_7_out_3, four_bit_g8_8_out_3,
       four_bit_g8_9_out_3, four_bit_g8_10_out_3, four_bit_g8_11_out_3, four_bit_g8_12_out_3,
       four_bit_g8_13_out_3, four_bit_g8_14_out_3, four_bit_g8_15_out_3, four_bit_g8_16_out_3, or_3_out,
       or_4_out, or_5_out, or_6_out, or_7_out, or_8_out, or_9_out, or_10_out, or_11_out, or_12_out,
       or_13_out, or_14_out, or_15_out, or_16_out, or_17_out;
  wire [15:0] bit_extender_1_out, multiplexer_1_out, multiplexer_2_out, or_18_out, s_r_ff_1_q;
  wire [15:12] or_2_out;

  Button button_1 (.out(button_1_out));
  or or_1 (or_1_out, reset, and_1_out, button_1_out);
  D_Flip_Flop d_ff_1 (.D(unstacking_mask[0]), .clk(enable), .Q(d_ff_1_q), .reset(or_18_out[0]));  // open: Qn, preset
  D_Flip_Flop d_ff_2 (.D(unstacking_mask[1]), .clk(enable), .Q(d_ff_2_q), .reset(or_18_out[1]));  // open: Qn, preset
  D_Flip_Flop d_ff_3 (.D(unstacking_mask[2]), .clk(enable), .Q(d_ff_3_q), .reset(or_18_out[2]));  // open: Qn, preset
  D_Flip_Flop d_ff_4 (.D(unstacking_mask[3]), .clk(enable), .Q(d_ff_4_q), .reset(or_18_out[3]));  // open: Qn, preset
  D_Flip_Flop d_ff_5 (.D(unstacking_mask[4]), .clk(enable), .Q(d_ff_5_q), .reset(or_18_out[4]));  // open: Qn, preset
  D_Flip_Flop d_ff_6 (.D(unstacking_mask[5]), .clk(enable), .Q(d_ff_6_q), .reset(or_18_out[5]));  // open: Qn, preset
  D_Flip_Flop d_ff_7 (.D(unstacking_mask[6]), .clk(enable), .Q(d_ff_7_q), .reset(or_18_out[6]));  // open: Qn, preset
  D_Flip_Flop d_ff_8 (.D(unstacking_mask[7]), .clk(enable), .Q(d_ff_8_q), .reset(or_18_out[7]));  // open: Qn, preset
  D_Flip_Flop d_ff_9 (.D(unstacking_mask[8]), .clk(enable), .Q(d_ff_9_q), .reset(or_18_out[8]));  // open: Qn, preset
  D_Flip_Flop d_ff_10 (.D(unstacking_mask[9]), .clk(enable), .Q(d_ff_10_q), .reset(or_18_out[9]));  // open: Qn, preset
  D_Flip_Flop d_ff_11 (
    .D(unstacking_mask[10]), .clk(enable), .Q(d_ff_11_q), .reset(or_18_out[10]));  // open: Qn, preset
  D_Flip_Flop d_ff_12 (
    .D(unstacking_mask[11]), .clk(enable), .Q(d_ff_12_q), .reset(or_18_out[11]));  // open: Qn, preset
  D_Flip_Flop d_ff_13 (
    .D(unstacking_mask[12]), .clk(enable), .Q(d_ff_13_q), .reset(or_18_out[12]));  // open: Qn, preset
  D_Flip_Flop d_ff_14 (
    .D(unstacking_mask[13]), .clk(enable), .Q(d_ff_14_q), .reset(or_18_out[13]));  // open: Qn, preset
  D_Flip_Flop d_ff_15 (
    .D(unstacking_mask[14]), .clk(enable), .Q(d_ff_15_q), .reset(or_18_out[14]));  // open: Qn, preset
  D_Flip_Flop d_ff_16 (
    .D(unstacking_mask[15]), .clk(enable), .Q(d_ff_16_q), .reset(or_18_out[15]));  // open: Qn, preset
  and and_1 (and_1_out, ~buffer_1_out, four_bit_eq_zero_1_out_2);  // AND_Gate
  buf buffer_1 (buffer_1_out, buffer_2_out);
  buf buffer_2 (buffer_2_out, buffer_3_out);
  buf buffer_3 (buffer_3_out, buffer_4_out);
  buf buffer_4 (buffer_4_out, four_bit_eq_zero_1_out_2);
  four_bit_eq_zero four_bit_eq_zero_1 (
    .in_1(four_bit_conditional_incrementer_1_out_3), .out_2(four_bit_eq_zero_1_out_2));
  four_bit_conditional_incrementer four_bit_conditional_incrementer_1 (
    .in_2(four_bit_conditional_incrementer_2_out_3), .in_1(d_ff_1_q),
    .out_3(four_bit_conditional_incrementer_1_out_3));
  four_bit_conditional_incrementer four_bit_conditional_incrementer_2 (
    .in_2(four_bit_conditional_incrementer_3_out_3), .in_1(d_ff_2_q),
    .out_3(four_bit_conditional_incrementer_2_out_3));
  four_bit_eq_zero four_bit_eq_zero_2 (
    .in_1(four_bit_conditional_incrementer_3_out_3), .out_2(four_bit_eq_zero_2_out_2));
  four_bit_conditional_incrementer four_bit_conditional_incrementer_3 (
    .in_2(four_bit_conditional_incrementer_4_out_3), .in_1(d_ff_3_q),
    .out_3(four_bit_conditional_incrementer_3_out_3));
  four_bit_eq_zero four_bit_eq_zero_3 (
    .in_1(four_bit_conditional_incrementer_4_out_3), .out_2(four_bit_eq_zero_3_out_2));
  four_bit_conditional_incrementer four_bit_conditional_incrementer_4 (
    .in_2(four_bit_conditional_incrementer_5_out_3), .in_1(d_ff_4_q),
    .out_3(four_bit_conditional_incrementer_4_out_3));
  four_bit_eq_zero four_bit_eq_zero_4 (
    .in_1(four_bit_conditional_incrementer_5_out_3), .out_2(four_bit_eq_zero_4_out_2));
  four_bit_conditional_incrementer four_bit_conditional_incrementer_5 (
    .in_2(four_bit_conditional_incrementer_6_out_3), .in_1(d_ff_5_q),
    .out_3(four_bit_conditional_incrementer_5_out_3));
  four_bit_eq_zero four_bit_eq_zero_5 (
    .in_1(four_bit_conditional_incrementer_6_out_3), .out_2(four_bit_eq_zero_5_out_2));
  four_bit_conditional_incrementer four_bit_conditional_incrementer_6 (
    .in_2(four_bit_conditional_incrementer_7_out_3), .in_1(d_ff_6_q),
    .out_3(four_bit_conditional_incrementer_6_out_3));
  four_bit_eq_zero four_bit_eq_zero_6 (
    .in_1(four_bit_conditional_incrementer_7_out_3), .out_2(four_bit_eq_zero_6_out_2));
  four_bit_conditional_incrementer four_bit_conditional_incrementer_7 (
    .in_2(four_bit_conditional_incrementer_8_out_3), .in_1(d_ff_7_q),
    .out_3(four_bit_conditional_incrementer_7_out_3));
  four_bit_eq_zero four_bit_eq_zero_7 (
    .in_1(four_bit_conditional_incrementer_8_out_3), .out_2(four_bit_eq_zero_7_out_2));
  four_bit_conditional_incrementer four_bit_conditional_incrementer_8 (
    .in_2(four_bit_conditional_incrementer_9_out_3), .in_1(d_ff_8_q),
    .out_3(four_bit_conditional_incrementer_8_out_3));
  four_bit_eq_zero four_bit_eq_zero_8 (
    .in_1(four_bit_conditional_incrementer_9_out_3), .out_2(four_bit_eq_zero_8_out_2));
  four_bit_conditional_incrementer four_bit_conditional_incrementer_9 (
    .in_2(four_bit_conditional_incrementer_10_out_3), .in_1(d_ff_9_q),
    .out_3(four_bit_conditional_incrementer_9_out_3));
  four_bit_eq_zero four_bit_eq_zero_9 (
    .in_1(four_bit_conditional_incrementer_10_out_3), .out_2(four_bit_eq_zero_9_out_2));
  four_bit_conditional_incrementer four_bit_conditional_incrementer_10 (
    .in_2(four_bit_conditional_incrementer_11_out_3), .in_1(d_ff_10_q),
    .out_3(four_bit_conditional_incrementer_10_out_3));
  four_bit_eq_zero four_bit_eq_zero_10 (
    .in_1(four_bit_conditional_incrementer_11_out_3), .out_2(four_bit_eq_zero_10_out_2));
  four_bit_conditional_incrementer four_bit_conditional_incrementer_11 (
    .in_2(four_bit_conditional_incrementer_12_out_3), .in_1(d_ff_11_q),
    .out_3(four_bit_conditional_incrementer_11_out_3));
  four_bit_eq_zero four_bit_eq_zero_11 (
    .in_1(four_bit_conditional_incrementer_12_out_3), .out_2(four_bit_eq_zero_11_out_2));
  four_bit_conditional_incrementer four_bit_conditional_incrementer_12 (
    .in_2(four_bit_conditional_incrementer_13_out_3), .in_1(d_ff_12_q),
    .out_3(four_bit_conditional_incrementer_12_out_3));
  four_bit_eq_zero four_bit_eq_zero_12 (
    .in_1(four_bit_conditional_incrementer_13_out_3), .out_2(four_bit_eq_zero_12_out_2));
  four_bit_conditional_incrementer four_bit_conditional_incrementer_13 (
    .in_2(four_bit_conditional_incrementer_14_out_3), .in_1(d_ff_13_q),
    .out_3(four_bit_conditional_incrementer_13_out_3));
  four_bit_eq_zero four_bit_eq_zero_13 (
    .in_1(four_bit_conditional_incrementer_14_out_3), .out_2(four_bit_eq_zero_13_out_2));
  four_bit_conditional_incrementer four_bit_conditional_incrementer_14 (
    .in_2(four_bit_conditional_incrementer_15_out_3), .in_1(d_ff_14_q),
    .out_3(four_bit_conditional_incrementer_14_out_3));
  four_bit_eq_zero four_bit_eq_zero_14 (
    .in_1(four_bit_conditional_incrementer_15_out_3), .out_2(four_bit_eq_zero_14_out_2));
  four_bit_conditional_incrementer four_bit_conditional_incrementer_15 (
    .in_2(four_bit_conditional_incrementer_16_out_3), .in_1(d_ff_15_q),
    .out_3(four_bit_conditional_incrementer_15_out_3));
  four_bit_eq_zero four_bit_eq_zero_15 (
    .in_1(four_bit_conditional_incrementer_16_out_3), .out_2(four_bit_eq_zero_15_out_2));
  four_bit_conditional_incrementer four_bit_conditional_incrementer_16 (
    .in_2(4'b0000), .in_1(d_ff_16_q), .out_3(four_bit_conditional_incrementer_16_out_3));
  not not_1 (active, four_bit_eq_zero_1_out_2);
  and and_2 (and_2_out, d_ff_1_q, four_bit_eq_zero_16_out_2);
  four_bit_eq_zero four_bit_eq_zero_16 (
    .in_1(four_bit_conditional_incrementer_2_out_3), .out_2(four_bit_eq_zero_16_out_2));
  and and_3 (and_3_out, four_bit_eq_zero_2_out_2, d_ff_2_q);
  and and_4 (and_4_out, four_bit_eq_zero_3_out_2, d_ff_3_q);
  and and_5 (and_5_out, four_bit_eq_zero_4_out_2, d_ff_4_q);
  and and_6 (and_6_out, four_bit_eq_zero_5_out_2, d_ff_5_q);
  and and_7 (and_7_out, four_bit_eq_zero_6_out_2, d_ff_6_q);
  and and_8 (and_8_out, four_bit_eq_zero_7_out_2, d_ff_7_q);
  and and_9 (and_9_out, four_bit_eq_zero_8_out_2, d_ff_8_q);
  and and_10 (and_10_out, four_bit_eq_zero_9_out_2, d_ff_9_q);
  and and_11 (and_11_out, four_bit_eq_zero_10_out_2, d_ff_10_q);
  and and_12 (and_12_out, four_bit_eq_zero_11_out_2, d_ff_11_q);
  and and_13 (and_13_out, four_bit_eq_zero_12_out_2, d_ff_12_q);
  and and_14 (and_14_out, four_bit_eq_zero_13_out_2, d_ff_13_q);
  and and_15 (and_15_out, four_bit_eq_zero_14_out_2, d_ff_14_q);
  and and_16 (and_16_out, four_bit_eq_zero_15_out_2, d_ff_15_q);
  and and_17 (and_17_out, register_1_q, and_2_out);
  assign or_2_out = four_bit_g8_1_out_3 | or_3_out;  // OR_Gate or_2, 4 bits wide
  four_bit_g8 four_bit_g8_1 (.in_1(and_2_out), .in_2(4'b0000), .out_3(four_bit_g8_1_out_3));
  and and_18 (and_18_out, register_1_q, and_3_out);
  assign or_3_out = four_bit_g8_2_out_3 | or_4_out;  // OR_Gate or_3, 4 bits wide
  four_bit_g8 four_bit_g8_2 (.in_1(and_3_out), .in_2(4'b0001), .out_3(four_bit_g8_2_out_3));
  and and_19 (and_19_out, register_1_q, and_4_out);
  assign or_4_out = four_bit_g8_3_out_3 | or_5_out;  // OR_Gate or_4, 4 bits wide
  four_bit_g8 four_bit_g8_3 (.in_1(and_4_out), .in_2(4'b0010), .out_3(four_bit_g8_3_out_3));
  and and_20 (and_20_out, register_1_q, and_5_out);
  assign or_5_out = four_bit_g8_4_out_3 | or_6_out;  // OR_Gate or_5, 4 bits wide
  four_bit_g8 four_bit_g8_4 (.in_1(and_5_out), .in_2(4'b0011), .out_3(four_bit_g8_4_out_3));
  and and_21 (and_21_out, register_1_q, and_6_out);
  assign or_6_out = four_bit_g8_5_out_3 | or_7_out;  // OR_Gate or_6, 4 bits wide
  four_bit_g8 four_bit_g8_5 (.in_1(and_6_out), .in_2(4'b0100), .out_3(four_bit_g8_5_out_3));
  and and_22 (and_22_out, register_1_q, and_7_out);
  assign or_7_out = four_bit_g8_6_out_3 | or_8_out;  // OR_Gate or_7, 4 bits wide
  four_bit_g8 four_bit_g8_6 (.in_1(and_7_out), .in_2(4'b0101), .out_3(four_bit_g8_6_out_3));
  and and_23 (and_23_out, register_1_q, and_8_out);
  assign or_8_out = four_bit_g8_7_out_3 | or_9_out;  // OR_Gate or_8, 4 bits wide
  four_bit_g8 four_bit_g8_7 (.in_1(and_8_out), .in_2(4'b0110), .out_3(four_bit_g8_7_out_3));
  and and_24 (and_24_out, register_1_q, and_9_out);
  assign or_9_out = four_bit_g8_8_out_3 | or_10_out;  // OR_Gate or_9, 4 bits wide
  four_bit_g8 four_bit_g8_8 (.in_1(and_9_out), .in_2(4'b0111), .out_3(four_bit_g8_8_out_3));
  and and_25 (and_25_out, register_1_q, and_10_out);
  assign or_10_out = four_bit_g8_9_out_3 | or_11_out;  // OR_Gate or_10, 4 bits wide
  four_bit_g8 four_bit_g8_9 (.in_1(and_10_out), .in_2(4'b1000), .out_3(four_bit_g8_9_out_3));
  and and_26 (and_26_out, register_1_q, and_11_out);
  assign or_11_out = four_bit_g8_10_out_3 | or_12_out;  // OR_Gate or_11, 4 bits wide
  four_bit_g8 four_bit_g8_10 (.in_1(and_11_out), .in_2(4'b1001), .out_3(four_bit_g8_10_out_3));
  and and_27 (and_27_out, register_1_q, and_12_out);
  assign or_12_out = four_bit_g8_11_out_3 | or_13_out;  // OR_Gate or_12, 4 bits wide
  four_bit_g8 four_bit_g8_11 (.in_1(and_12_out), .in_2(4'b1010), .out_3(four_bit_g8_11_out_3));
  and and_28 (and_28_out, register_1_q, and_13_out);
  assign or_13_out = four_bit_g8_12_out_3 | or_14_out;  // OR_Gate or_13, 4 bits wide
  four_bit_g8 four_bit_g8_12 (.in_1(and_13_out), .in_2(4'b1011), .out_3(four_bit_g8_12_out_3));
  and and_29 (and_29_out, register_1_q, and_14_out);
  assign or_14_out = four_bit_g8_13_out_3 | or_15_out;  // OR_Gate or_14, 4 bits wide
  four_bit_g8 four_bit_g8_13 (.in_1(and_14_out), .in_2(4'b1100), .out_3(four_bit_g8_13_out_3));
  and and_30 (and_30_out, register_1_q, and_15_out);
  assign or_15_out = four_bit_g8_14_out_3 | or_16_out;  // OR_Gate or_15, 4 bits wide
  four_bit_g8 four_bit_g8_14 (.in_1(and_15_out), .in_2(4'b1101), .out_3(four_bit_g8_14_out_3));
  and and_31 (and_31_out, register_1_q, and_16_out);
  assign or_16_out = four_bit_g8_15_out_3 | or_17_out;  // OR_Gate or_16, 4 bits wide
  four_bit_g8 four_bit_g8_15 (.in_1(and_16_out), .in_2(4'b1110), .out_3(four_bit_g8_15_out_3));
  and and_32 (and_32_out, register_1_q, d_ff_16_q);
  assign or_17_out = four_bit_g8_16_out_3 | four_bit_g8_16_out_3;  // OR_Gate or_17, 4 bits wide
  four_bit_g8 four_bit_g8_16 (.in_1(d_ff_16_q), .in_2(4'b1111), .out_3(four_bit_g8_16_out_3));
  S_R_Flip_Flop s_r_ff_1 (
    .S(and_17_out), .R(1'b0), .clk(clk), .Q(s_r_ff_1_q[0]), .reset(or_1_out));  // open: Qn, preset
  S_R_Flip_Flop s_r_ff_2 (
    .S(and_18_out), .R(1'b0), .clk(clk), .Q(s_r_ff_1_q[1]), .reset(or_1_out));  // open: Qn, preset
  S_R_Flip_Flop s_r_ff_3 (
    .S(and_19_out), .R(1'b0), .clk(clk), .Q(s_r_ff_1_q[2]), .reset(or_1_out));  // open: Qn, preset
  S_R_Flip_Flop s_r_ff_4 (
    .S(and_20_out), .R(1'b0), .clk(clk), .Q(s_r_ff_1_q[3]), .reset(or_1_out));  // open: Qn, preset
  S_R_Flip_Flop s_r_ff_5 (
    .S(and_21_out), .R(1'b0), .clk(clk), .Q(s_r_ff_1_q[4]), .reset(or_1_out));  // open: Qn, preset
  S_R_Flip_Flop s_r_ff_6 (
    .S(and_22_out), .R(1'b0), .clk(clk), .Q(s_r_ff_1_q[5]), .reset(or_1_out));  // open: Qn, preset
  S_R_Flip_Flop s_r_ff_7 (
    .S(and_23_out), .R(1'b0), .clk(clk), .Q(s_r_ff_1_q[6]), .reset(or_1_out));  // open: Qn, preset
  S_R_Flip_Flop s_r_ff_8 (
    .S(and_24_out), .R(1'b0), .clk(clk), .Q(s_r_ff_1_q[7]), .reset(or_1_out));  // open: Qn, preset
  S_R_Flip_Flop s_r_ff_9 (
    .S(and_25_out), .R(1'b0), .clk(clk), .Q(s_r_ff_1_q[8]), .reset(or_1_out));  // open: Qn, preset
  S_R_Flip_Flop s_r_ff_10 (
    .S(and_26_out), .R(1'b0), .clk(clk), .Q(s_r_ff_1_q[9]), .reset(or_1_out));  // open: Qn, preset
  S_R_Flip_Flop s_r_ff_11 (
    .S(and_27_out), .R(1'b0), .clk(clk), .Q(s_r_ff_1_q[10]), .reset(or_1_out));  // open: Qn, preset
  S_R_Flip_Flop s_r_ff_12 (
    .S(and_28_out), .R(1'b0), .clk(clk), .Q(s_r_ff_1_q[11]), .reset(or_1_out));  // open: Qn, preset
  S_R_Flip_Flop s_r_ff_13 (
    .S(and_29_out), .R(1'b0), .clk(clk), .Q(s_r_ff_1_q[12]), .reset(or_1_out));  // open: Qn, preset
  S_R_Flip_Flop s_r_ff_14 (
    .S(and_30_out), .R(1'b0), .clk(clk), .Q(s_r_ff_1_q[13]), .reset(or_1_out));  // open: Qn, preset
  S_R_Flip_Flop s_r_ff_15 (
    .S(and_31_out), .R(1'b0), .clk(clk), .Q(s_r_ff_1_q[14]), .reset(or_1_out));  // open: Qn, preset
  S_R_Flip_Flop s_r_ff_16 (
    .S(and_32_out), .R(1'b0), .clk(clk), .Q(s_r_ff_1_q[15]), .reset(or_1_out));  // open: Qn, preset
  assign or_18_out = bit_extender_1_out | s_r_ff_1_q;  // OR_Gate or_18, 16 bits wide
  assign bit_extender_1_out = {{15{or_1_out}}, or_1_out};  // Bit_Extender bit_extender_1
  Register #(.width(1)) register_1 (.D(adder_1_out), .en(active), .clk(clk), .Q(register_1_q), .clr(or_19_out));
  or or_19 (or_19_out, or_1_out, and_33_out);
  Multiplexer #(.width(16)) multiplexer_1 (
    .in0(16'h1004), .in1({or_2_out, 12'h24}), .out(multiplexer_1_out), .sel(register_1_q));
  Multiplexer #(.width(16)) multiplexer_2 (
    .in0({16{1'b0}}), .in1(16'h1010), .out(multiplexer_2_out), .sel(register_1_q));
  Adder #(.width(1)) adder_1 (.a(register_1_q), .b(1'b1), .out(adder_1_out));  // open: cin, cout
  buf buffer_5 (buffer_5_out, enable);
  buf buffer_6 (buffer_6_out, buffer_5_out);
  buf buffer_7 (buffer_7_out, buffer_6_out);
  buf buffer_8 (buffer_8_out, buffer_7_out);
  buf buffer_9 (buffer_9_out, buffer_8_out);
  and and_33 (and_33_out, enable, ~buffer_9_out);  // AND_Gate
  // Probe on control_bus_1_out
  sixt_bit_gatekeeper sixt_bit_gatekeeper_1 (.in_1(active), .in_2(multiplexer_1_out), .out_3(control_bus_1_out));
  // Probe on control_bus_2_out
  sixt_bit_gatekeeper sixt_bit_gatekeeper_2 (.in_1(active), .in_2(multiplexer_2_out), .out_3(control_bus_2_out));
endmodule

module L (
  input  in_1,
  output out_2
);

  wire buffer_1_out, buffer_2_out, buffer_3_out;

  buf buffer_1 (buffer_1_out, in_1);
  buf buffer_2 (buffer_2_out, buffer_1_out);
  buf buffer_3 (buffer_3_out, buffer_2_out);
  and and_1 (out_2, in_1, ~buffer_3_out);  // AND_Gate
endmodule

module eight_bit_conditional_incrementer (
  input  in_1,
  input  [7:0] in_2,
  output [7:0] out_3
);

  Adder adder_1 (.a(in_2), .b({8{1'b0}}), .out(out_3), .cin(in_1));  // open: cout
endmodule

module which_bit (
  input  [7:0] in_1,
  output [7:0] out_2
);

  wire or_1_out, or_2_out, or_3_out, or_4_out, or_5_out, or_6_out, or_7_out;
  wire [7:0] eight_bit_conditional_incrementer_1_out_3, eight_bit_conditional_incrementer_2_out_3,
       eight_bit_conditional_incrementer_3_out_3, eight_bit_conditional_incrementer_4_out_3,
       eight_bit_conditional_incrementer_5_out_3, eight_bit_conditional_incrementer_6_out_3,
       eight_bit_conditional_incrementer_7_out_3;

  or or_1 (or_1_out, in_1[7], in_1[6]);
  eight_bit_conditional_incrementer eight_bit_conditional_incrementer_1 (
    .in_2({8{1'b0}}), .in_1(in_1[7]), .out_3(eight_bit_conditional_incrementer_1_out_3));
  eight_bit_conditional_incrementer eight_bit_conditional_incrementer_2 (
    .in_2(eight_bit_conditional_incrementer_1_out_3), .in_1(or_1_out),
    .out_3(eight_bit_conditional_incrementer_2_out_3));
  or or_2 (or_2_out, or_1_out, in_1[5]);
  eight_bit_conditional_incrementer eight_bit_conditional_incrementer_3 (
    .in_2(eight_bit_conditional_incrementer_2_out_3), .in_1(or_2_out),
    .out_3(eight_bit_conditional_incrementer_3_out_3));
  or or_3 (or_3_out, or_2_out, in_1[4]);
  or or_4 (or_4_out, or_3_out, in_1[3]);
  eight_bit_conditional_incrementer eight_bit_conditional_incrementer_4 (
    .in_2(eight_bit_conditional_incrementer_3_out_3), .in_1(or_3_out),
    .out_3(eight_bit_conditional_incrementer_4_out_3));
  or or_5 (or_5_out, or_4_out, in_1[2]);
  eight_bit_conditional_incrementer eight_bit_conditional_incrementer_5 (
    .in_2(eight_bit_conditional_incrementer_4_out_3), .in_1(or_4_out),
    .out_3(eight_bit_conditional_incrementer_5_out_3));
  eight_bit_conditional_incrementer eight_bit_conditional_incrementer_6 (
    .in_2(eight_bit_conditional_incrementer_5_out_3), .in_1(or_5_out),
    .out_3(eight_bit_conditional_incrementer_6_out_3));
  or or_6 (or_6_out, or_5_out, in_1[1]);
  eight_bit_conditional_incrementer eight_bit_conditional_incrementer_7 (
    .in_2(eight_bit_conditional_incrementer_6_out_3), .in_1(or_6_out),
    .out_3(eight_bit_conditional_incrementer_7_out_3));
  or or_7 (or_7_out, or_6_out, in_1[0]);
  eight_bit_conditional_incrementer eight_bit_conditional_incrementer_8 (
    .in_2(eight_bit_conditional_incrementer_7_out_3), .in_1(or_7_out), .out_3(out_2));
endmodule

module interrupt_queue (
  input  next_ir,
  input  [7:0] pins_in,
  input  reset,
  output waiting,
  output [7:0] id
);

  wire and_1_out, buffer_1_out, buffer_2_out, buffer_3_out, buffer_4_out, buffer_5_out, buffer_6_out,
       buffer_7_out, buffer_8_out, buffer_9_out, button_1_out, or_1_out, or_2_out;
  wire [7:0] l_8_out_2, multiplexer_1_out, multiplexer_2_out, multiplexer_3_out, multiplexer_4_out,
       multiplexer_5_out, multiplexer_6_out, multiplexer_7_out, multiplexer_8_out, register_2_q,
       register_3_q, register_4_q, register_5_q, register_6_q, register_7_q, register_8_q;

  L l_1 (.in_1(pins_in[7]), .out_2(l_8_out_2[7]));
  Button button_1 (.out(button_1_out));
  L l_2 (.in_1(pins_in[6]), .out_2(l_8_out_2[6]));
  L l_3 (.in_1(pins_in[5]), .out_2(l_8_out_2[5]));
  or or_1 (or_1_out, reset, button_1_out);
  buf buffer_1 (buffer_1_out, next_ir);
  buf buffer_2 (buffer_2_out, buffer_1_out);
  L l_4 (.in_1(pins_in[4]), .out_2(l_8_out_2[4]));
  L l_5 (.in_1(pins_in[3]), .out_2(l_8_out_2[3]));
  L l_6 (.in_1(pins_in[2]), .out_2(l_8_out_2[2]));
  buf buffer_3 (buffer_3_out, buffer_2_out);
  buf buffer_4 (buffer_4_out, buffer_3_out);
  buf buffer_5 (buffer_5_out, buffer_4_out);
  buf buffer_6 (buffer_6_out, buffer_5_out);
  L l_7 (.in_1(pins_in[1]), .out_2(l_8_out_2[1]));
  L l_8 (.in_1(pins_in[0]), .out_2(l_8_out_2[0]));
  and and_1 (and_1_out, ~buffer_6_out, next_ir);  // AND_Gate
  or or_2 (or_2_out, and_1_out, l_8_out_2[0], l_8_out_2[1], l_8_out_2[2], l_8_out_2[3], l_8_out_2[4], l_8_out_2[5], l_8_out_2[6], l_8_out_2[7]);
  buf buffer_7 (buffer_7_out, or_2_out);
  Multiplexer #(.width(8)) multiplexer_1 (
    .in0(l_8_out_2), .in1(register_2_q), .out(multiplexer_1_out), .sel(and_1_out));
  buf buffer_8 (buffer_8_out, buffer_7_out);
  buf buffer_9 (buffer_9_out, buffer_8_out);
  Register register_1 (.D(multiplexer_1_out), .clk(buffer_9_out), .Q(id), .clr(or_1_out));  // open: en
  Register register_2 (.D(multiplexer_2_out), .clk(buffer_9_out), .Q(register_2_q), .clr(or_1_out));  // open: en
  Multiplexer #(.width(8)) multiplexer_2 (.in0(id), .in1(register_3_q), .out(multiplexer_2_out), .sel(and_1_out));
  Multiplexer #(.width(8)) multiplexer_3 (
    .in0(register_2_q), .in1(register_4_q), .out(multiplexer_3_out), .sel(and_1_out));
  Register register_3 (.D(multiplexer_3_out), .clk(buffer_9_out), .Q(register_3_q), .clr(or_1_out));  // open: en
  Register register_4 (.D(multiplexer_4_out), .clk(buffer_9_out), .Q(register_4_q), .clr(or_1_out));  // open: en
  Multiplexer #(.width(8)) multiplexer_4 (
    .in0(register_3_q), .in1(register_5_q), .out(multiplexer_4_out), .sel(and_1_out));
  Register register_5 (.D(multiplexer_5_out), .clk(buffer_9_out), .Q(register_5_q), .clr(or_1_out));  // open: en
  Multiplexer #(.width(8)) multiplexer_5 (
    .in0(register_4_q), .in1(register_6_q), .out(multiplexer_5_out), .sel(and_1_out));
  Register register_6 (.D(multiplexer_6_out), .clk(buffer_9_out), .Q(register_6_q), .clr(or_1_out));  // open: en
  Multiplexer #(.width(8)) multiplexer_6 (
    .in0(register_5_q), .in1(register_7_q), .out(multiplexer_6_out), .sel(and_1_out));
  Register register_7 (.D(multiplexer_7_out), .clk(buffer_9_out), .Q(register_7_q), .clr(or_1_out));  // open: en
  Multiplexer #(.width(8)) multiplexer_7 (
    .in0(register_6_q), .in1(register_8_q), .out(multiplexer_7_out), .sel(and_1_out));
  or or_3 (waiting, id[0], id[1], id[2], id[3], id[4], id[5], id[6], id[7]);
  Register register_8 (.D(multiplexer_8_out), .clk(buffer_9_out), .Q(register_8_q), .clr(or_1_out));  // open: en
  Multiplexer #(.width(8)) multiplexer_8 (
    .in0(register_7_q), .in1({8{1'b0}}), .out(multiplexer_8_out), .sel(and_1_out));
endmodule

module interrupt_table (
  input  [15:0] control_bus_1,
  input  [15:0] control_bus_2,
  input  [7:0] id,
  input  [15:0] data_in,
  input  clk,
  input  reset,
  output [15:0] ih_addr,
  output [15:0] to_data_bus
);

  wire or_1_out, or_2_out, or_3_out, or_4_out, or_5_out, or_6_out, or_7_out, or_8_out, or_9_out, or_10_out,
       or_11_out, or_12_out, or_13_out, or_14_out, or_15_out, or_16_out, or_17_out, sixt_bit_eq_cmp_1_out_3,
       sixt_bit_eq_cmp_2_out_3, sixt_bit_eq_cmp_3_out_3, sixt_bit_eq_cmp_4_out_3, sixt_bit_eq_cmp_5_out_3,
       sixt_bit_eq_cmp_6_out_3, sixt_bit_eq_cmp_7_out_3, sixt_bit_eq_cmp_8_out_3, sixt_bit_eq_cmp_9_out_3,
       sixt_bit_eq_cmp_10_out_3, sixt_bit_eq_cmp_11_out_3, sixt_bit_eq_cmp_12_out_3,
       sixt_bit_eq_cmp_13_out_3, sixt_bit_eq_cmp_14_out_3, sixt_bit_eq_cmp_15_out_3,
       sixt_bit_eq_cmp_16_out_3, sixt_bit_eq_cmp_17_out_3, sixt_bit_eq_cmp_18_out_3,
       sixt_bit_eq_cmp_19_out_3, sixt_bit_eq_cmp_20_out_3, sixt_bit_eq_cmp_21_out_3,
       sixt_bit_eq_cmp_22_out_3, sixt_bit_eq_cmp_23_out_3, sixt_bit_eq_cmp_24_out_3,
       sixt_bit_eq_cmp_25_out_3, sixt_bit_eq_cmp_26_out_3, sixt_bit_eq_cmp_27_out_3,
       sixt_bit_eq_cmp_28_out_3, sixt_bit_eq_cmp_29_out_3, sixt_bit_eq_cmp_30_out_3,
       sixt_bit_eq_cmp_31_out_3, sixt_bit_eq_cmp_32_out_3, sixt_bit_eq_cmp_33_out_3, sixt_bit_eq_cmp_34_out_3;
  wire [3:0] subtractor_1_out;
  wire [7:0] which_bit_1_out_2;
  wire [15:0] or_18_out, or_19_out, or_20_out, or_21_out, or_22_out, or_23_out, or_24_out, register_1_q,
       register_2_q, register_3_q, register_4_q, register_5_q, register_6_q, register_7_q, register_8_q,
       register_9_q, sixt_bit_gatekeeper_1_out_3, sixt_bit_gatekeeper_2_out_3, sixt_bit_gatekeeper_3_out_3,
       sixt_bit_gatekeeper_4_out_3, sixt_bit_gatekeeper_5_out_3, sixt_bit_gatekeeper_6_out_3,
       sixt_bit_gatekeeper_7_out_3, sixt_bit_gatekeeper_8_out_3;

  Register #(.trigger("falling"), .width(16)) register_1 (
    .D(data_in), .clk(clk), .Q(register_1_q), .clr(reset));  // open: en
  sixt_bit_eq_cmp sixt_bit_eq_cmp_1 (.in_1(control_bus_1), .in_2(16'h8002), .out_3(sixt_bit_eq_cmp_1_out_3));
  sixt_bit_eq_cmp sixt_bit_eq_cmp_2 (.in_1(control_bus_2), .in_2(16'h8002), .out_3(sixt_bit_eq_cmp_2_out_3));
  sixt_bit_eq_cmp sixt_bit_eq_cmp_3 (.in_1(control_bus_1), .in_2(16'h8006), .out_3(sixt_bit_eq_cmp_3_out_3));
  sixt_bit_eq_cmp sixt_bit_eq_cmp_4 (.in_1(control_bus_2), .in_2(16'h8006), .out_3(sixt_bit_eq_cmp_4_out_3));
  sixt_bit_eq_cmp sixt_bit_eq_cmp_5 (.in_1(control_bus_1), .in_2(16'h9002), .out_3(sixt_bit_eq_cmp_5_out_3));
  sixt_bit_eq_cmp sixt_bit_eq_cmp_6 (.in_1(control_bus_2), .in_2(16'h9002), .out_3(sixt_bit_eq_cmp_6_out_3));
  sixt_bit_eq_cmp sixt_bit_eq_cmp_7 (.in_1(control_bus_1), .in_2(16'h9006), .out_3(sixt_bit_eq_cmp_7_out_3));
  sixt_bit_eq_cmp sixt_bit_eq_cmp_8 (.in_1(control_bus_2), .in_2(16'h9006), .out_3(sixt_bit_eq_cmp_8_out_3));
  sixt_bit_eq_cmp sixt_bit_eq_cmp_9 (.in_1(control_bus_1), .in_2(16'ha002), .out_3(sixt_bit_eq_cmp_9_out_3));
  sixt_bit_eq_cmp sixt_bit_eq_cmp_10 (.in_1(control_bus_2), .in_2(16'ha002), .out_3(sixt_bit_eq_cmp_10_out_3));
  sixt_bit_eq_cmp sixt_bit_eq_cmp_11 (.in_1(control_bus_1), .in_2(16'ha006), .out_3(sixt_bit_eq_cmp_11_out_3));
  sixt_bit_eq_cmp sixt_bit_eq_cmp_12 (.in_1(control_bus_2), .in_2(16'ha006), .out_3(sixt_bit_eq_cmp_12_out_3));
  sixt_bit_eq_cmp sixt_bit_eq_cmp_13 (.in_1(control_bus_1), .in_2(16'hb002), .out_3(sixt_bit_eq_cmp_13_out_3));
  sixt_bit_eq_cmp sixt_bit_eq_cmp_14 (.in_1(control_bus_2), .in_2(16'hb002), .out_3(sixt_bit_eq_cmp_14_out_3));
  sixt_bit_eq_cmp sixt_bit_eq_cmp_15 (.in_1(control_bus_1), .in_2(16'hb006), .out_3(sixt_bit_eq_cmp_15_out_3));
  sixt_bit_eq_cmp sixt_bit_eq_cmp_16 (.in_1(control_bus_2), .in_2(16'hb006), .out_3(sixt_bit_eq_cmp_16_out_3));
  sixt_bit_eq_cmp sixt_bit_eq_cmp_17 (.in_1(control_bus_1), .in_2(16'hc002), .out_3(sixt_bit_eq_cmp_17_out_3));
  sixt_bit_eq_cmp sixt_bit_eq_cmp_18 (.in_1(control_bus_2), .in_2(16'hc002), .out_3(sixt_bit_eq_cmp_18_out_3));
  sixt_bit_eq_cmp sixt_bit_eq_cmp_19 (.in_1(control_bus_1), .in_2(16'hc006), .out_3(sixt_bit_eq_cmp_19_out_3));
  sixt_bit_eq_cmp sixt_bit_eq_cmp_20 (.in_1(control_bus_2), .in_2(16'hc006), .out_3(sixt_bit_eq_cmp_20_out_3));
  sixt_bit_eq_cmp sixt_bit_eq_cmp_21 (.in_1(control_bus_1), .in_2(16'hd002), .out_3(sixt_bit_eq_cmp_21_out_3));
  sixt_bit_eq_cmp sixt_bit_eq_cmp_22 (.in_1(control_bus_2), .in_2(16'hd002), .out_3(sixt_bit_eq_cmp_22_out_3));
  sixt_bit_eq_cmp sixt_bit_eq_cmp_23 (.in_1(control_bus_1), .in_2(16'hd006), .out_3(sixt_bit_eq_cmp_23_out_3));
  sixt_bit_eq_cmp sixt_bit_eq_cmp_24 (.in_1(control_bus_2), .in_2(16'hd006), .out_3(sixt_bit_eq_cmp_24_out_3));
  sixt_bit_eq_cmp sixt_bit_eq_cmp_25 (.in_1(control_bus_1), .in_2(16'he002), .out_3(sixt_bit_eq_cmp_25_out_3));
  sixt_bit_eq_cmp sixt_bit_eq_cmp_26 (.in_1(control_bus_2), .in_2(16'he002), .out_3(sixt_bit_eq_cmp_26_out_3));
  sixt_bit_eq_cmp sixt_bit_eq_cmp_27 (.in_1(control_bus_1), .in_2(16'he006), .out_3(sixt_bit_eq_cmp_27_out_3));
  sixt_bit_eq_cmp sixt_bit_eq_cmp_28 (.in_1(control_bus_2), .in_2(16'he006), .out_3(sixt_bit_eq_cmp_28_out_3));
  sixt_bit_eq_cmp sixt_bit_eq_cmp_29 (.in_1(control_bus_1), .in_2(16'hf002), .out_3(sixt_bit_eq_cmp_29_out_3));
  sixt_bit_eq_cmp sixt_bit_eq_cmp_30 (.in_1(control_bus_2), .in_2(16'hf002), .out_3(sixt_bit_eq_cmp_30_out_3));
  sixt_bit_eq_cmp sixt_bit_eq_cmp_31 (.in_1(control_bus_1), .in_2(16'hf006), .out_3(sixt_bit_eq_cmp_31_out_3));
  sixt_bit_eq_cmp sixt_bit_eq_cmp_32 (.in_1(control_bus_2), .in_2(16'hf006), .out_3(sixt_bit_eq_cmp_32_out_3));
  sixt_bit_eq_cmp sixt_bit_eq_cmp_33 (.in_1(16'h1b), .in_2(control_bus_1), .out_3(sixt_bit_eq_cmp_33_out_3));
  or or_1 (or_1_out, sixt_bit_eq_cmp_33_out_3, sixt_bit_eq_cmp_34_out_3);
  sixt_bit_eq_cmp sixt_bit_eq_cmp_34 (.in_1(16'h1b), .in_2(control_bus_2), .out_3(sixt_bit_eq_cmp_34_out_3));
  which_bit which_bit_1 (.in_1(id), .out_2(which_bit_1_out_2));
  or or_2 (or_2_out, sixt_bit_eq_cmp_1_out_3, sixt_bit_eq_cmp_2_out_3);
  or or_3 (or_3_out, sixt_bit_eq_cmp_3_out_3, sixt_bit_eq_cmp_4_out_3);
  or or_4 (or_4_out, sixt_bit_eq_cmp_5_out_3, sixt_bit_eq_cmp_6_out_3);
  or or_5 (or_5_out, sixt_bit_eq_cmp_7_out_3, sixt_bit_eq_cmp_8_out_3);
  or or_6 (or_6_out, sixt_bit_eq_cmp_9_out_3, sixt_bit_eq_cmp_10_out_3);
  or or_7 (or_7_out, sixt_bit_eq_cmp_11_out_3, sixt_bit_eq_cmp_12_out_3);
  or or_8 (or_8_out, sixt_bit_eq_cmp_13_out_3, sixt_bit_eq_cmp_14_out_3);
  or or_9 (or_9_out, sixt_bit_eq_cmp_15_out_3, sixt_bit_eq_cmp_16_out_3);
  or or_10 (or_10_out, sixt_bit_eq_cmp_17_out_3, sixt_bit_eq_cmp_18_out_3);
  or or_11 (or_11_out, sixt_bit_eq_cmp_19_out_3, sixt_bit_eq_cmp_20_out_3);
  or or_12 (or_12_out, sixt_bit_eq_cmp_21_out_3, sixt_bit_eq_cmp_22_out_3);
  or or_13 (or_13_out, sixt_bit_eq_cmp_23_out_3, sixt_bit_eq_cmp_24_out_3);
  or or_14 (or_14_out, sixt_bit_eq_cmp_25_out_3, sixt_bit_eq_cmp_26_out_3);
  or or_15 (or_15_out, sixt_bit_eq_cmp_27_out_3, sixt_bit_eq_cmp_28_out_3);
  or or_16 (or_16_out, sixt_bit_eq_cmp_29_out_3, sixt_bit_eq_cmp_30_out_3);
  or or_17 (or_17_out, sixt_bit_eq_cmp_31_out_3, sixt_bit_eq_cmp_32_out_3);
  Register #(.width(16)) register_2 (.D(register_1_q), .en(or_3_out), .clk(clk), .Q(register_2_q), .clr(reset));
  Register #(.width(16)) register_3 (.D(register_1_q), .en(or_5_out), .clk(clk), .Q(register_3_q), .clr(reset));
  Register #(.width(16)) register_4 (.D(register_1_q), .en(or_7_out), .clk(clk), .Q(register_4_q), .clr(reset));
  Register #(.width(16)) register_5 (.D(register_1_q), .en(or_9_out), .clk(clk), .Q(register_5_q), .clr(reset));
  Register #(.width(16)) register_6 (.D(register_1_q), .en(or_11_out), .clk(clk), .Q(register_6_q), .clr(reset));
  Register #(.width(16)) register_7 (.D(register_1_q), .en(or_13_out), .clk(clk), .Q(register_7_q), .clr(reset));
  Register #(.width(16)) register_8 (.D(register_1_q), .en(or_15_out), .clk(clk), .Q(register_8_q), .clr(reset));
  Register #(.width(16)) register_9 (.D(register_1_q), .en(or_17_out), .clk(clk), .Q(register_9_q), .clr(reset));
  Subtractor #(.width(4)) subtractor_1 (
    .a(which_bit_1_out_2[3:0]), .b(4'b0001), .out(subtractor_1_out));  // open: bin, bout
  sixt_bit_gatekeeper sixt_bit_gatekeeper_1 (.in_1(or_2_out), .in_2(register_2_q), .out_3(sixt_bit_gatekeeper_1_out_3));
  assign or_18_out = sixt_bit_gatekeeper_2_out_3 | or_19_out;  // OR_Gate or_18, 16 bits wide
  sixt_bit_gatekeeper sixt_bit_gatekeeper_2 (.in_1(or_4_out), .in_2(register_3_q), .out_3(sixt_bit_gatekeeper_2_out_3));
  assign or_19_out = sixt_bit_gatekeeper_3_out_3 | or_20_out;  // OR_Gate or_19, 16 bits wide
  sixt_bit_gatekeeper sixt_bit_gatekeeper_3 (.in_1(or_6_out), .in_2(register_4_q), .out_3(sixt_bit_gatekeeper_3_out_3));
  assign or_20_out = sixt_bit_gatekeeper_4_out_3 | or_21_out;  // OR_Gate or_20, 16 bits wide
  sixt_bit_gatekeeper sixt_bit_gatekeeper_4 (.in_1(or_8_out), .in_2(register_5_q), .out_3(sixt_bit_gatekeeper_4_out_3));
  assign or_21_out = sixt_bit_gatekeeper_5_out_3 | or_22_out;  // OR_Gate or_21, 16 bits wide
  sixt_bit_gatekeeper sixt_bit_gatekeeper_5 (
    .in_1(or_10_out), .in_2(register_6_q), .out_3(sixt_bit_gatekeeper_5_out_3));
  assign or_22_out = sixt_bit_gatekeeper_6_out_3 | or_23_out;  // OR_Gate or_22, 16 bits wide
  sixt_bit_gatekeeper sixt_bit_gatekeeper_6 (
    .in_1(or_12_out), .in_2(register_7_q), .out_3(sixt_bit_gatekeeper_6_out_3));
  assign or_23_out = sixt_bit_gatekeeper_7_out_3 | sixt_bit_gatekeeper_8_out_3;  // OR_Gate or_23, 16 bits wide
  sixt_bit_gatekeeper sixt_bit_gatekeeper_7 (
    .in_1(or_14_out), .in_2(register_8_q), .out_3(sixt_bit_gatekeeper_7_out_3));
  sixt_bit_gatekeeper sixt_bit_gatekeeper_8 (
    .in_1(or_16_out), .in_2(register_9_q), .out_3(sixt_bit_gatekeeper_8_out_3));
  // Probe on subtractor_1_out[2:0]
  Multiplexer #(.select(3), .width(16)) multiplexer_1 (
    .in0(register_2_q), .in1(register_3_q), .in2(register_4_q), .in3(register_5_q), .in4(register_6_q),
    .in5(register_7_q), .in6(register_8_q), .in7(register_9_q), .out(ih_addr));  // open: sel
  assign or_24_out = sixt_bit_gatekeeper_1_out_3 | or_18_out;  // OR_Gate or_24, 16 bits wide
  sixt_bit_gatekeeper sixt_bit_gatekeeper_9 (.in_1(or_1_out), .in_2(or_24_out), .out_3(to_data_bus));
endmodule

module input_pins_8 (
  input  in_1,
  input  in_2,
  input  in_3,
  input  in_4,
  input  in_5,
  input  in_6,
  input  in_7,
  input  in_8,
  output [7:0] out_9
);

  Pull_Resistor pull_resistor_1 (.node(in_1));
  Pull_Resistor pull_resistor_2 (.node(in_2));
  Pull_Resistor pull_resistor_3 (.node(in_3));
  Pull_Resistor pull_resistor_4 (.node(in_4));
  Pull_Resistor pull_resistor_5 (.node(in_5));
  Pull_Resistor pull_resistor_6 (.node(in_6));
  Pull_Resistor pull_resistor_7 (.node(in_7));
  Pull_Resistor pull_resistor_8 (.node(in_8));

  assign out_9 = {in_1, in_2, in_3, in_4, in_5, in_6, in_7, in_8};
endmodule

module spi_controller (
  input  write,
  input  read,
  input  [15:0] spi_out_config,
  input  [15:0] data_in,
  input  [15:0] spi_in_config,
  input  clock,
  input  reset,
  input  miso,
  output [15:0] data_out,
  output done,
  output cs,
  output clk,
  output mosi
);

  wire and_1_out, and_2_out, and_3_out, and_4_out, and_5_out, and_6_out, and_7_out, and_8_out, and_9_out,
       and_10_out, and_11_out, and_12_out, and_13_out, and_14_out, and_15_out, clock_division_bell_1_out_6,
       comparator_1_gt, comparator_2_eq, comparator_3_lt, comparator_4_gt, comparator_5_eq,
       falling_edge_delay_1_out_2, falling_edge_delay_2_out_2, nor_1_out, not_2_out, not_or_hasnt_1_out_2,
       not_or_hasnt_2_out_2, or_1_out, or_2_out, or_6_out, or_7_out, or_8_out, or_10_out, or_11_out,
       or_12_out, pulse_extender_1_out_6, rising_edge_delay_1_out_2, rising_edge_delay_2_out_2,
       rising_edge_delay_4_out_2, s_r_ff_1_q, s_r_ff_2_q, s_r_ff_3_q, s_r_ff_4_q, shift_register_1_p3,
       shift_register_1_p4, shift_register_2_p1, shift_register_2_p4, shift_register_2_p15,
       shift_register_2_p16, shift_register_3_p1, shift_register_3_p2, shift_register_3_p3,
       two_ticker_1_out_4, two_ticker_2_out_4, two_ticker_3_out_4, two_ticker_4_out_4;
  wire [1:0] bytes_to_write_q;
  wire [4:0] adder_1_out, adder_2_out, kounter_q, multiplexer_1_out, register_2_q;
  wire [15:0] register_1_q, undriven;

  two_ticker two_ticker_1 (.signal_in(s_r_ff_1_q), .clock(clock), .reset(reset), .out_4(two_ticker_1_out_4));
  Register #(.width(2)) bytes_to_write (
    .D(spi_out_config[1:0]), .clk(two_ticker_1_out_4), .Q(bytes_to_write_q), .clr(reset));  // open: en
  clock_division_bell clock_division_bell_1 (
    .divisor(spi_out_config[15:8]), .load_divisor(two_ticker_1_out_4), .restart(two_ticker_1_out_4),
    .clock(clock), .reset(reset), .out_6(clock_division_bell_1_out_6));
  Comparator #(.mode("unsigned"), .width(2)) comparator_1 (
    .a(bytes_to_write_q), .b(2'b01), .gt(comparator_1_gt));  // open: eq, lt
  Register #(.width(16)) register_1 (.D(data_in), .clk(s_r_ff_1_q), .Q(register_1_q), .clr(reset));  // open: en
  // Shift_Register shift_register_1: pin names not known; wires that end beside it: reset, two_ticker_1_out_4, shift_register_1_p3, shift_register_1_p4, 1'b0, register_1_q[0], register_1_q[1], register_1_q[2], register_1_q[3], register_1_q[4], register_1_q[5], register_1_q[6], register_1_q[7]
  or or_1 (or_1_out, s_r_ff_1_q, shift_register_3_p2);
  not not_1 (cs, or_1_out);
  and and_1 (and_1_out, write, ~shift_register_3_p2);  // AND_Gate
  not_or_hasnt not_or_hasnt_1 (.in_1(and_1_out), .out_2(not_or_hasnt_1_out_2));
  and and_2 (and_2_out, and_1_out, falling_edge_delay_1_out_2);
  S_R_Flip_Flop s_r_ff_1 (.Q(s_r_ff_1_q), .reset(or_2_out), .preset(and_2_out));  // open: S, R, clk, Qn
  or or_2 (or_2_out, reset, two_ticker_3_out_4);
  or or_3 (shift_register_1_p3, and_11_out, and_12_out);
  and and_3 (and_3_out, s_r_ff_1_q, clock_division_bell_1_out_6);
  and and_4 (and_4_out, or_12_out, shift_register_3_p2);
  or or_4 (clk, and_3_out, and_4_out);
  falling_edge_delay falling_edge_delay_1 (.in_1(not_or_hasnt_1_out_2), .out_2(falling_edge_delay_1_out_2));
  and and_5 (and_5_out, s_r_ff_1_q, ~rising_edge_delay_4_out_2);  // AND_Gate
  S_R_Flip_Flop #(.trigger("falling")) s_r_ff_2 (
    .S(1'b0), .R(1'b1), .clk(clock), .Q(s_r_ff_2_q), .reset(reset), .preset(and_5_out));  // open: Qn
  and and_6 (and_6_out, shift_register_2_p1, and_11_out);
  or or_5 (mosi, and_6_out, and_8_out);
  or or_6 (or_6_out, reset, two_ticker_3_out_4);
  and and_7 (and_7_out, ~s_r_ff_2_q, clock_division_bell_1_out_6);  // AND_Gate
  // Shift_Register shift_register_2: pin names not known; wires that end beside it: shift_register_2_p1, reset, two_ticker_1_out_4, shift_register_2_p4, shift_register_1_p4, 1'b0, register_1_q[8], register_1_q[9], register_1_q[10], register_1_q[11], register_1_q[12], register_1_q[13], register_1_q[14], register_1_q[15], shift_register_2_p15, shift_register_2_p16
  S_R_Flip_Flop #(.trigger("falling")) s_r_ff_3 (
    .Q(s_r_ff_3_q), .reset(or_6_out), .preset(s_r_ff_2_q));  // open: S, R, clk, Qn
  rising_edge_delay rising_edge_delay_1 (.in_1(s_r_ff_2_q), .out_2(rising_edge_delay_1_out_2));
  rising_edge_delay rising_edge_delay_2 (.in_1(s_r_ff_1_q), .out_2(rising_edge_delay_2_out_2));
  rising_edge_delay rising_edge_delay_3 (.in_1(and_12_out), .out_2(shift_register_2_p4));
  rising_edge_delay rising_edge_delay_4 (.in_1(s_r_ff_3_q), .out_2(rising_edge_delay_4_out_2));
  or or_7 (or_7_out, rising_edge_delay_1_out_2, and_7_out);
  and and_8 (and_8_out, shift_register_2_p15, and_12_out);
  and and_9 (and_9_out, read, ~s_r_ff_1_q);  // AND_Gate
  rising_edge_delay rising_edge_delay_5 (.in_1(or_7_out), .out_2(shift_register_1_p4));
  Register #(.width(5)) kounter (
    .D(adder_1_out), .en(rising_edge_delay_2_out_2), .clk(and_10_out), .Q(kounter_q), .clr(or_8_out));
  and and_10 (and_10_out, clock, s_r_ff_1_q);
  or or_8 (or_8_out, reset, two_ticker_3_out_4);
  // Shift_Register #(.length(16)) shift_register_3: pin names not known; wires that end beside it: shift_register_3_p1, shift_register_3_p2, shift_register_3_p3, miso
  or or_9 (shift_register_3_p1, two_ticker_4_out_4, reset);
  Adder #(.width(5)) adder_1 (.a(kounter_q), .b(5'b00001), .out(adder_1_out));  // open: cin, cout
  Comparator #(.mode("unsigned"), .width(5)) comparator_2 (
    .a(kounter_q), .b(5'b10000), .eq(comparator_2_eq));  // open: gt, lt
  Comparator #(.mode("unsigned"), .width(5)) comparator_3 (
    .a(kounter_q), .b(5'b00001), .lt(comparator_3_lt));  // open: gt, eq
  Comparator #(.mode("unsigned"), .width(5)) comparator_4 (
    .a(kounter_q), .b(5'b01000), .gt(comparator_4_gt));  // open: eq, lt
  and and_11 (and_11_out, ~comparator_3_lt, ~comparator_4_gt);  // AND_Gate
  and and_12 (and_12_out, comparator_4_gt, comparator_1_gt);
  and and_13 (and_13_out, and_9_out, falling_edge_delay_2_out_2);
  S_R_Flip_Flop s_r_ff_4 (.Q(s_r_ff_4_q), .reset(or_11_out), .preset(and_13_out));  // open: S, R, clk, Qn
  two_ticker two_ticker_2 (.signal_in(shift_register_3_p2), .clock(clock), .reset(reset), .out_4(two_ticker_2_out_4));
  and and_14 (and_14_out, comparator_2_eq, comparator_1_gt);
  or or_10 (or_10_out, and_14_out, and_15_out);
  and and_15 (and_15_out, comparator_4_gt, ~comparator_1_gt);  // AND_Gate
  not_or_hasnt not_or_hasnt_2 (.in_1(and_9_out), .out_2(not_or_hasnt_2_out_2));
  S_R_Flip_Flop s_r_ff_5 (
    .S(s_r_ff_4_q), .R(not_2_out), .clk(clock), .Q(shift_register_3_p2), .reset(or_11_out));  // open: Qn, preset
  not not_2 (not_2_out, s_r_ff_4_q);
  two_ticker two_ticker_3 (.signal_in(or_10_out), .clock(clock), .reset(reset), .out_4(two_ticker_3_out_4));
  falling_edge_delay falling_edge_delay_2 (.in_1(not_or_hasnt_2_out_2), .out_2(falling_edge_delay_2_out_2));
  clock_division_bell clock_division_bell_2 (
    .divisor(spi_out_config[15:8]), .load_divisor(two_ticker_2_out_4), .clock(clock), .reset(reset),
    .out_6(shift_register_3_p3));  // open: restart
  nor nor_1 (nor_1_out, spi_in_config[0], spi_in_config[1], spi_in_config[2], spi_in_config[3], spi_in_config[4]);
  Register #(.width(5)) register_2 (
    .D(adder_2_out), .en(shift_register_3_p2), .clk(shift_register_3_p3), .Q(register_2_q), .clr(or_11_out));
  or or_11 (or_11_out, reset, two_ticker_4_out_4);
  Multiplexer #(.width(5)) multiplexer_1 (
    .in0(spi_in_config[4:0]), .in1(5'b01000), .out(multiplexer_1_out), .sel(nor_1_out));
  Adder #(.width(5)) adder_2 (.a(register_2_q), .b(5'b00001), .out(adder_2_out));  // open: cin, cout
  Comparator #(.mode("unsigned"), .width(5)) comparator_5 (
    .a(register_2_q), .b(multiplexer_1_out), .eq(comparator_5_eq));  // open: gt, lt
  pulse_extender pulse_extender_1 (
    .in_1(comparator_5_eq), .in_2(reset), .in_3(or_12_out), .out_6(pulse_extender_1_out_6));  // open: out_4, out_5
  or or_12 (or_12_out, reset, two_ticker_2_out_4);
  two_ticker two_ticker_4 (
    .signal_in(pulse_extender_1_out_6), .clock(clock), .reset(or_12_out), .out_4(two_ticker_4_out_4));
  Register #(.width(16)) register_3 (.D(undriven), .clk(comparator_5_eq), .Q(data_out), .clr(reset));  // open: en
  or or_13 (done, two_ticker_3_out_4, two_ticker_4_out_4);
endmodule
